// Logisim project alpha blending tests.circ as structural Verilog: 1 circuit, main circuit main
module main (
  input  [3:0] Source,
  input  [7:0] in_2,
  input  [3:0] New,
  input  [7:0] in_4,
  input  [7:0] in_5,
  input  [3:0] Alpha,
  input  [3:0] New_2,
  input  [3:0] Source_2,
  input  [3:0] Alpha_2
);

  wire adder_3_cout, adder_4_cout, and_1_out;
  wire [3:0] multiplexer_1_out, multiplexer_2_out, multiplexer_3_out, multiplexer_4_out, multiplier_1_cout,
       multiplier_1_out, multiplier_2_cout, multiplier_2_out, not_1_out;
  wire [4:0] adder_2_out, adder_3_out;
  wire [5:5] adder_2_cout;
  wire [6:0] adder_4_out;
  wire [7:0] adder_1_out, divider_1_out, divider_2_out;
  wire [7:7] or_1_out;

  assign not_1_out = ~Alpha;  // NOT_Gate not_1, 4 bits wide
  Multiplier #(.width(4)) multiplier_1 (
    .a(Source), .b(not_1_out), .out(multiplier_1_out), .cout(multiplier_1_cout));  // open: cin
  Multiplier #(.width(4)) multiplier_2 (
    .a(New), .b(Alpha), .out(multiplier_2_out), .cout(multiplier_2_cout));  // open: cin
  // Probe on multiplier_2_cout
  Multiplexer #(.width(4), .enable("false")) multiplexer_1 (
    .in0(Source_2), .in1(New_2), .out(multiplexer_1_out), .sel(Alpha_2[0]));
  Multiplexer #(.width(4), .enable("false")) multiplexer_2 (
    .in0(Source_2), .in1(New_2), .out(multiplexer_2_out), .sel(Alpha_2[1]));
  Multiplexer #(.width(4), .enable("false")) multiplexer_3 (
    .in0(Source_2), .in1(New_2), .out(multiplexer_3_out), .sel(Alpha_2[2]));
  Multiplexer #(.width(4), .enable("false")) multiplexer_4 (
    .in0(Source_2), .in1(New_2), .out(multiplexer_4_out), .sel(Alpha_2[3]));
  // Probe on adder_1_out
  Adder adder_1 (
    .a({multiplier_1_cout, multiplier_1_out}), .b({multiplier_2_cout, multiplier_2_out}), .out(adder_1_out));  // open: cin, cout
  Adder #(.width(5)) adder_2 (
    .a({1'b0, multiplexer_1_out}), .b({multiplexer_2_out, 1'b0}), .out(adder_2_out), .cout(adder_2_cout[5]));  // open: cin
  Adder #(.width(5)) adder_3 (
    .a({1'b0, multiplexer_3_out}), .b({multiplexer_4_out, 1'b0}), .out(adder_3_out), .cout(adder_3_cout));  // open: cin
  Divider divider_1 (.a(adder_1_out), .b(in_4), .out(divider_1_out));  // open: upper, rem
  // Probe on divider_1_out
  Adder #(.width(7)) adder_4 (
    .a({1'b0, adder_2_cout[5], adder_2_out}), .b({adder_3_out, 2'b00}), .out(adder_4_out), .cout(adder_4_cout));  // open: cin
  // Probe on {or_1_out[7], adder_4_out}
  or or_1 (or_1_out[7], adder_4_cout, adder_3_cout);
  // Probe on divider_2_out
  Divider divider_2 (.a(in_2), .b(8'hf), .out(divider_2_out));  // open: upper, rem
  // XOR_Gate xor_1 is placed but not wired
  and and_1 (and_1_out, in_5[3], in_5[4], in_5[5], in_5[6]);
  // OR_Gate or_2 has open pins: in0=and_1_out, in1=in_5[7], out=open
  // XOR_Gate xor_2 is placed but not wired
endmodule
