// Logisim project computer.circ as structural Verilog: 14 circuits, main circuit Central processing unit
module Computer (
);

  wire central_processing_unit_1__16_bit, central_processing_unit_1_get_ram,
       central_processing_unit_1_set_ram;
  wire [15:0] central_processing_unit_1_ram_addres, central_processing_unit_1_ram_output, ram_1_ram_output;

  Central_processing_unit central_processing_unit_1 (
    .Get_Ram(central_processing_unit_1_get_ram), .Set_Ram(central_processing_unit_1_set_ram),
    .RAM_input(ram_1_ram_output), .RAM_Addres(central_processing_unit_1_ram_addres),
    .RAM_output(central_processing_unit_1_ram_output), ._16_bit(central_processing_unit_1__16_bit));  // open: in_1
  RAM ram_1 (
    ._16_bit(central_processing_unit_1__16_bit), .Set_Ram(central_processing_unit_1_set_ram),
    .Get_Ram(central_processing_unit_1_get_ram), .RAM_output(ram_1_ram_output),
    .RAM_Addres(central_processing_unit_1_ram_addres), .RAM_input(central_processing_unit_1_ram_output));
endmodule

module RAM (
  input  _16_bit,
  input  Set_Ram,
  input  Get_Ram,
  input  [15:0] RAM_Addres,
  input  [15:0] RAM_input,
  output [15:0] RAM_output
);

  wire button_1_out, button_2_out, nor_1_out, nor_2_out, nor_3_out, nor_4_out, not_1_out, not_2_out;
  wire [7:0] multiplexer_3_out, multiplexer_4_out, ram_1_data, ram_2_data;
  wire [14:0] adder_1_out;

  not not_1 (not_1_out, Set_Ram);
  nor nor_1 (nor_1_out, RAM_Addres[0], _16_bit);
  not not_2 (not_2_out, RAM_Addres[0]);
  nor nor_2 (nor_2_out, not_2_out, _16_bit);
  nor nor_3 (nor_3_out, not_1_out, nor_1_out);
  nor nor_4 (nor_4_out, not_1_out, nor_2_out);
  Adder #(.width(15)) adder_1 (
    .a(RAM_Addres[15:1]), .b({15{1'b0}}), .out(adder_1_out), .cin(RAM_Addres[0]));  // open: cout
  Button button_1 (.out(button_1_out));
  Button button_2 (.out(button_2_out));
  Multiplexer #(.width(8), .enable("false")) multiplexer_1 (
    .in0(ram_2_data), .in1(ram_1_data), .out(RAM_output[7:0]), .sel(RAM_Addres[0]));
  RAM_part #(.addrWidth(15)) ram_1 (
    .addr(RAM_Addres[15:1]), .data(ram_1_data), .clk(nor_3_out), .ld(Get_Ram), .clr(button_1_out));  // open: sel
  RAM_part #(.addrWidth(15)) ram_2 (
    .addr(adder_1_out), .data(ram_2_data), .clk(nor_4_out), .ld(Get_Ram), .clr(button_2_out));  // open: sel
  Multiplexer #(.width(8), .enable("false")) multiplexer_2 (
    .in0(ram_1_data), .in1(ram_2_data), .out(RAM_output[15:8]), .sel(RAM_Addres[0]));
  Multiplexer #(.width(8), .enable("false")) multiplexer_3 (
    .in0(RAM_input[7:0]), .in1(RAM_input[15:8]), .out(multiplexer_3_out), .sel(RAM_Addres[0]));
  assign ram_2_data = Set_Ram ? multiplexer_3_out : 8'bz;  // Controlled_Buffer controlled_buffer_1
  assign ram_1_data = Set_Ram ? multiplexer_4_out : 8'bz;  // Controlled_Buffer controlled_buffer_2
  Multiplexer #(.width(8), .enable("false")) multiplexer_4 (
    .in0(RAM_input[15:8]), .in1(RAM_input[7:0]), .out(multiplexer_4_out), .sel(RAM_Addres[0]));
endmodule

module Central_processing_unit (
  input  in_1,
  input  [15:0] RAM_input,
  output _16_bit,
  output Set_Ram,
  output Get_Ram,
  output [15:0] RAM_Addres,
  output [15:0] RAM_output
);

  wire arithmetic_logic_unit_1_carry_out, arithmetic_logic_unit_1_overflow, control_unit_1__16_bit,
       control_unit_1__16_bit_2, control_unit_1_carry_in, control_unit_1_decrease_address,
       control_unit_1_get_ram, control_unit_1_set_ram, control_unit_1_update_fs;
  wire [2:0] control_unit_1_alu_micro_operation;
  wire [3:0] control_unit_1_reg_address, control_unit_1_reg_address_2;
  wire [7:0] control_unit_1_output_fs_2, registery_1_fs_out;
  wire [15:0] arithmetic_logic_unit_1_result, control_unit_1_a, control_unit_1_b, control_unit_1_input_reg,
       control_unit_1_ram_addres, control_unit_1_ram_output, ram_interface_1_new_ram_addres,
       ram_interface_1_ram_input_2, registery_1_cs_out, registery_1_output_data, registery_1_rs_out;

  Update_Clock update_clock_1 (.Start(in_1));  // open: out_2, out_3, out_4, out_5, out_6, out_7, out_8, out_9
  RAM_interface ram_interface_1 (
    .Get_RAM_2(Set_Ram), .Set_RAM_2(Get_Ram), .RAM_input(RAM_input), .RAM_Addres_2(RAM_Addres),
    .RAM_output_2(RAM_output), .Decrease_Address(control_unit_1_decrease_address),
    ._16_bit(control_unit_1__16_bit_2), .Get_RAM(control_unit_1_get_ram), .Set_RAM(control_unit_1_set_ram),
    .RAM_input_2(ram_interface_1_ram_input_2), .RAM_Addres(control_unit_1_ram_addres),
    .RAM_output(control_unit_1_ram_output), .New_RAM_Addres(ram_interface_1_new_ram_addres),
    ._16_bit_2(_16_bit));
  Registery registery_1 (
    .Output_Data(registery_1_output_data), .Output_Register(control_unit_1_reg_address),
    .Data_In(control_unit_1_input_reg), .Input_Register(control_unit_1_reg_address_2),
    .RS_Out(registery_1_rs_out), .CS_Out(registery_1_cs_out), .FS_Out(registery_1_fs_out),
    .FS_In(control_unit_1_output_fs_2), .Update_FS(control_unit_1_update_fs));
  Control_unit control_unit_1 (
    .Carry_In(control_unit_1_carry_in), ._16_bit(control_unit_1__16_bit), .B(control_unit_1_b),
    .A(control_unit_1_a), .ALU_Micro_Operation(control_unit_1_alu_micro_operation),
    .Result(arithmetic_logic_unit_1_result), .Carry_Out(arithmetic_logic_unit_1_carry_out),
    .Overflow_Out(arithmetic_logic_unit_1_overflow), .Output_FS_2(control_unit_1_output_fs_2),
    .Update_FS(control_unit_1_update_fs), .Input_Reg(control_unit_1_input_reg),
    .Reg_Address_2(control_unit_1_reg_address_2), .Output_CS(registery_1_cs_out),
    .Output_FS(registery_1_fs_out), .Output_Reg(registery_1_output_data),
    .Reg_Address(control_unit_1_reg_address), .RAM_output(control_unit_1_ram_output),
    .RAM_Addres(control_unit_1_ram_addres), .RAM_input(ram_interface_1_ram_input_2),
    ._16_bit_2(control_unit_1__16_bit_2), .Get_RAM(control_unit_1_get_ram), .Set_RAM(control_unit_1_set_ram),
    .Output_RS(registery_1_rs_out), .New_RAM_Addres(ram_interface_1_new_ram_addres),
    .Decrease_Address(control_unit_1_decrease_address));  // open: Clock
  Arithmetic_logic_unit arithmetic_logic_unit_1 (
    .Carry_In(control_unit_1_carry_in), ._16_bit(control_unit_1__16_bit), .B(control_unit_1_b),
    .A(control_unit_1_a), .Micro_Operation(control_unit_1_alu_micro_operation),
    .Result(arithmetic_logic_unit_1_result), .Carry_Out(arithmetic_logic_unit_1_carry_out),
    .Overflow(arithmetic_logic_unit_1_overflow));
endmodule

module Control_unit (
  input  Clock,
  input  [15:0] RAM_input,
  input  [15:0] Result,
  input  [15:0] New_RAM_Addres,
  input  Carry_Out,
  input  Overflow_Out,
  input  [15:0] Output_Reg,
  input  [15:0] Output_RS,
  input  [15:0] Output_CS,
  input  [7:0] Output_FS,
  output Carry_In,
  output _16_bit,
  output [15:0] B,
  output Decrease_Address,
  output _16_bit_2,
  output [15:0] A,
  output Get_RAM,
  output Set_RAM,
  output [15:0] RAM_Addres,
  output [2:0] ALU_Micro_Operation,
  output [15:0] RAM_output,
  output [15:0] Input_Reg,
  output [3:0] Reg_Address,
  output [3:0] Reg_Address_2,
  output Update_FS,
  output [7:0] Output_FS_2
);

  wire decoder_1_out4, decoder_1_out5, nand_1_out, not_1_out, or_1_out, or_2_out, Reg_Result;
  wire [3:0] bit_extender_1_out;
  wire [3:3] command_selector_1_micro_opcode;
  wire [15:0] multiplexer_1_out, Y_in;

  Y_Register y_register_1 (
    .Clock(Clock), .Selector(Reg_Result), .Y_out(A), .Update(or_1_out), .Y_in(Y_in), ._0(Output_Reg),
    ._1(multiplexer_1_out));
  Multiplexer #(.width(16), .enable("false")) multiplexer_1 (
    .in0(Result), .in1(New_RAM_Addres), .out(multiplexer_1_out), .sel(Get_RAM));
  Command_Selector command_selector_1 (
    .RS(Output_RS), .Carry_In(Output_FS[3]), .Test(_16_bit_2), .Carry_Out(Update_FS), .Register(Reg_Address),
    .Micro_opcode({command_selector_1_micro_opcode[3], ALU_Micro_Operation}));  // open: OP, Stage
  // Probe on {command_selector_1_micro_opcode[3], ALU_Micro_Operation}
  or or_1 (or_1_out, Set_RAM, command_selector_1_micro_opcode[3], decoder_1_out4, Get_RAM);
  Decoder #(.select(3), .disabled(0)) decoder_1 (
    .out4(decoder_1_out4), .out5(decoder_1_out5), .out6(Set_RAM), .out7(Get_RAM), .sel(ALU_Micro_Operation),
    .en(not_1_out));  // open: out0, out1, out2, out3
  not not_1 (not_1_out, command_selector_1_micro_opcode[3]);
  or or_2 (or_2_out, Get_RAM, decoder_1_out5);
  not not_2 (Reg_Result, decoder_1_out4);
  nand nand_1 (nand_1_out, or_2_out, Clock);
  assign bit_extender_1_out = {{3{nand_1_out}}, nand_1_out};  // Bit_Extender bit_extender_1
  Multiplexer #(.width(16), .enable("false")) multiplexer_2 (.in0(A), .in1(RAM_input), .out(Input_Reg), .sel(Get_RAM));
  assign Reg_Address_2 = bit_extender_1_out | Reg_Address;  // OR_Gate or_3, 4 bits wide
  Value_Tester value_tester_1 (
    .Test_Reg(Y_in), ._16_bit(_16_bit), .Overflow(Overflow_Out), .Carry(Carry_Out), .Flags_In(Output_FS),
    .Flags_Out(Output_FS_2));

  assign B = Output_Reg;
  assign Carry_In = _16_bit_2;
  assign Decrease_Address = _16_bit_2;
  assign RAM_Addres = A;
  assign RAM_output = Output_Reg;

  // Other names for the same wires on the sheet: _16 = _16_bit; Carry = _16_bit_2; CS[15:0] = Output_CS;
  //   FS[7:0] = Output_FS; Ram[15:0] = RAM_input; Reg[3:0] = Reg_Address; RS[15:0] = Output_RS; Test = Update_FS;
  //   Y_out[15:0] = A

  // Notes on the sheet:
  //   NXTO
  //   CNXT
  //   NXTB?
  //   ?
  //   RG>Y
  //   Y>RG
  //   RG>R
  //   R>RG
endmodule

module Registery (
  input  [3:0] Output_Register,
  input  [15:0] Data_In,
  input  [3:0] Input_Register,
  input  [7:0] FS_In,
  input  Update_FS,
  output [7:0] FS_Out,
  output [15:0] RS_Out,
  output [15:0] CS_Out,
  output [15:0] Output_Data
);

  wire decoder_1_out0, decoder_1_out1, decoder_1_out2, decoder_1_out3, decoder_1_out4, decoder_1_out5,
       decoder_1_out6, decoder_1_out7, decoder_1_out8, decoder_1_out9, decoder_1_out10, decoder_1_out12,
       decoder_1_out13, decoder_1_out14, or_1_out, or_2_out, or_3_out, or_4_out, or_5_out;
  wire [7:0] AH_q, AL_q, BH_q, BL_q, multiplexer_2_out, multiplexer_3_out, multiplexer_4_out, R1_q, R2_q;
  wire [15:0] CX_q, DX_q, SS_q;

  Multiplexer #(.select(4), .width(16), .enable("false")) multiplexer_1 (
    .in0({{8{1'b0}}, AL_q}), .in1({{8{1'b0}}, AH_q}), .in2({{8{1'b0}}, BL_q}), .in3({{8{1'b0}}, BH_q}),
    .in4({AH_q, AL_q}), .in5({BH_q, BL_q}), .in6(CX_q), .in7(DX_q), .in8({{8{1'b0}}, FS_Out}),
    .in9({{8{1'b0}}, R1_q}), .in10({{8{1'b0}}, R2_q}), .in11(16'h1), .in12(CS_Out), .in13(SS_q),
    .in14(RS_Out), .in15({16{1'b0}}), .out(Output_Data), .sel(Output_Register));
  Register #(.width(16), .trigger("high")) RS (.D(Data_In), .Q(RS_Out), .clk(decoder_1_out14));  // open: en, clr
  Register #(.width(16), .trigger("high")) SS (.D(Data_In), .Q(SS_q), .clk(decoder_1_out13));  // open: en, clr
  Register #(.width(16), .trigger("high")) CS (.D(Data_In), .Q(CS_Out), .clk(decoder_1_out12));  // open: en, clr
  Register #(.trigger("high")) R2 (.D(Data_In[7:0]), .Q(R2_q), .clr(decoder_1_out10));  // open: en, clk
  Register #(.trigger("high")) R1 (.D(Data_In[7:0]), .Q(R1_q), .clk(decoder_1_out9));  // open: en, clr
  Multiplexer #(.width(8), .enable("false")) multiplexer_2 (
    .in0(FS_In), .in1(Data_In[7:0]), .out(multiplexer_2_out), .sel(decoder_1_out8));
  Register #(.trigger("high")) FS (.D(multiplexer_2_out), .Q(FS_Out), .clk(or_1_out));  // open: en, clr
  or or_1 (or_1_out, Update_FS, decoder_1_out8);
  Register #(.width(16), .trigger("high")) DX (.D(Data_In), .Q(DX_q), .clk(decoder_1_out7));  // open: en, clr
  Register #(.width(16), .trigger("high")) CX (.D(Data_In), .Q(CX_q), .clk(decoder_1_out6));  // open: en, clr
  Multiplexer #(.width(8), .enable("false")) multiplexer_3 (
    .in0(Data_In[7:0]), .in1(Data_In[15:8]), .out(multiplexer_3_out), .sel(decoder_1_out5));
  Register #(.trigger("high")) BH (.D(multiplexer_3_out), .Q(BH_q), .clk(or_2_out));  // open: en, clr
  or or_2 (or_2_out, decoder_1_out5, decoder_1_out3);
  Register #(.trigger("high")) BL (.D(Data_In[7:0]), .Q(BL_q), .clk(or_3_out));  // open: en, clr
  Multiplexer #(.width(8), .enable("false")) multiplexer_4 (
    .in0(Data_In[7:0]), .in1(Data_In[15:8]), .out(multiplexer_4_out), .sel(decoder_1_out4));
  or or_3 (or_3_out, decoder_1_out5, decoder_1_out2);
  Register #(.trigger("high")) AH (.D(multiplexer_4_out), .Q(AH_q), .clk(or_4_out));  // open: en, clr
  or or_4 (or_4_out, decoder_1_out4, decoder_1_out1);
  Register #(.trigger("high")) AL (.D(Data_In[7:0]), .Q(AL_q), .clk(or_5_out));  // open: en, clr
  or or_5 (or_5_out, decoder_1_out4, decoder_1_out0);
  // Probe on Data_In
  Decoder #(.select(4), .enable("false")) decoder_1 (
    .out0(decoder_1_out0), .out1(decoder_1_out1), .out2(decoder_1_out2), .out3(decoder_1_out3),
    .out4(decoder_1_out4), .out5(decoder_1_out5), .out6(decoder_1_out6), .out7(decoder_1_out7),
    .out8(decoder_1_out8), .out9(decoder_1_out9), .out10(decoder_1_out10), .out12(decoder_1_out12),
    .out13(decoder_1_out13), .out14(decoder_1_out14), .sel(Input_Register));  // open: out11, out15
endmodule

module Arithmetic_logic_unit (
  input  Carry_In,
  input  _16_bit,
  input  [15:0] B,
  input  [15:0] A,
  input  [2:0] Micro_Operation,
  output [15:0] Result,
  output Carry_Out,
  output Overflow
);

  wire adder_1_cout, adder_2_cout, adder_3_cout, adder_4_cout, decoder_1_out0, decoder_1_out1,
       decoder_1_out2, decoder_1_out3, decoder_1_out4, decoder_1_out5, decoder_1_out6, decoder_1_out7,
       multiplexer_1_out, multiplexer_3_out, multiplexer_4_out, multiplexer_5_out, multiplexer_6_out,
       multiplexer_7_out, multiplexer_8_out, multiplexer_9_out, multiplexer_10_out, nor_1_out, nor_2_out,
       subtractor_1_bout, subtractor_2_bout, subtractor_3_bout, subtractor_4_bout, xnor_1_out, xnor_2_out,
       xor_2_out, xor_3_out;
  wire [6:0] adder_1_out, adder_3_out, subtractor_1_out, subtractor_3_out;
  wire [7:7] multiplexer_2_out;
  wire [15:0] and_1_out, not_1_out, or_1_out, xor_1_out;
  wire [15:7] adder_2_out, subtractor_2_out;

  Decoder #(.select(3), .enable("false")) decoder_1 (
    .out0(decoder_1_out0), .out1(decoder_1_out1), .out2(decoder_1_out2), .out3(decoder_1_out3),
    .out4(decoder_1_out4), .out5(decoder_1_out5), .out6(decoder_1_out6), .out7(decoder_1_out7),
    .sel(Micro_Operation));
  Pull_Resistor pull_resistor_1 (.node(Result));
  Pull_Resistor pull_resistor_2 (.node(Carry_Out));
  Pull_Resistor pull_resistor_3 (.node(Overflow));
  assign or_1_out = A | B;  // OR_Gate or_1, 16 bits wide
  assign not_1_out = ~A;  // NOT_Gate not_1, 16 bits wide
  assign Result = decoder_1_out0 ? not_1_out : 16'bz;  // Controlled_Buffer controlled_buffer_1
  assign Result = decoder_1_out1 ? or_1_out : 16'bz;  // Controlled_Buffer controlled_buffer_2
  assign and_1_out = A & B;  // AND_Gate and_1, 16 bits wide
  assign Result = decoder_1_out2 ? and_1_out : 16'bz;  // Controlled_Buffer controlled_buffer_3
  assign xor_1_out = A ^ B;  // XOR_Gate xor_1, 16 bits wide
  assign Result = decoder_1_out3 ? xor_1_out : 16'bz;  // Controlled_Buffer controlled_buffer_4
  Multiplexer #(.enable("false")) multiplexer_1 (.in0(A[7]), .in1(A[15]), .out(multiplexer_1_out), .sel(_16_bit));
  assign Carry_Out = decoder_1_out4 ? multiplexer_1_out : 1'bz;  // Controlled_Buffer controlled_buffer_5
  Multiplexer #(.enable("false")) multiplexer_2 (.in0(Carry_In), .in1(A[8]), .out(multiplexer_2_out[7]), .sel(_16_bit));
  assign Result = decoder_1_out4 ? {A[14:0], Carry_In} : 16'bz;  // Controlled_Buffer controlled_buffer_6
  assign Carry_Out = decoder_1_out5 ? A[0] : 1'bz;  // Controlled_Buffer controlled_buffer_7
  assign Result = decoder_1_out5 ? {Carry_In, A[15:9], multiplexer_2_out[7], A[7:1]} : 16'bz;  // Controlled_Buffer controlled_buffer_8
  Multiplexer #(.enable("false")) multiplexer_3 (.in0(B[7]), .in1(B[15]), .out(multiplexer_3_out), .sel(_16_bit));
  Adder #(.width(7)) adder_1 (.a(A[6:0]), .b(B[6:0]), .out(adder_1_out), .cin(Carry_In), .cout(adder_1_cout));
  Adder #(.width(1)) adder_2 (.a(A[7]), .b(B[7]), .out(adder_2_out[7]), .cin(adder_1_cout), .cout(adder_2_cout));
  Adder #(.width(7)) adder_3 (.a(A[14:8]), .b(B[14:8]), .out(adder_3_out), .cin(adder_2_cout), .cout(adder_3_cout));
  Adder #(.width(1)) adder_4 (.a(A[15]), .b(B[15]), .out(adder_2_out[15]), .cin(adder_3_cout), .cout(adder_4_cout));
  Multiplexer #(.enable("false")) multiplexer_4 (.in0(A[7]), .in1(A[15]), .out(multiplexer_4_out), .sel(_16_bit));
  xor xor_2 (xor_2_out, multiplexer_4_out, multiplexer_3_out);
  Multiplexer #(.enable("false")) multiplexer_5 (
    .in0(adder_2_cout), .in1(adder_4_cout), .out(multiplexer_5_out), .sel(_16_bit));
  assign Carry_Out = decoder_1_out6 ? multiplexer_5_out : 1'bz;  // Controlled_Buffer controlled_buffer_9
  assign Result = decoder_1_out6 ? {adder_2_out[15], adder_3_out, adder_2_out[7], adder_1_out} : 16'bz;  // Controlled_Buffer controlled_buffer_10
  Multiplexer #(.enable("false")) multiplexer_6 (
    .in0(adder_1_cout), .in1(adder_3_cout), .out(multiplexer_6_out), .sel(_16_bit));
  xnor xnor_1 (xnor_1_out, multiplexer_4_out, multiplexer_6_out);
  nor nor_1 (nor_1_out, xor_2_out, xnor_1_out);
  assign Overflow = decoder_1_out6 ? nor_1_out : 1'bz;  // Controlled_Buffer controlled_buffer_11
  Multiplexer #(.enable("false")) multiplexer_7 (.in0(B[7]), .in1(B[15]), .out(multiplexer_7_out), .sel(_16_bit));
  Subtractor #(.width(7)) subtractor_1 (
    .a(A[6:0]), .b(B[6:0]), .out(subtractor_1_out), .bin(Carry_In), .bout(subtractor_1_bout));
  Subtractor #(.width(1)) subtractor_2 (
    .a(A[7]), .b(B[7]), .out(subtractor_2_out[7]), .bin(subtractor_1_bout), .bout(subtractor_2_bout));
  Subtractor #(.width(7)) subtractor_3 (
    .a(A[14:8]), .b(B[14:8]), .out(subtractor_3_out), .bin(subtractor_2_bout), .bout(subtractor_3_bout));
  Subtractor #(.width(1)) subtractor_4 (
    .a(A[15]), .b(B[15]), .out(subtractor_2_out[15]), .bin(subtractor_3_bout), .bout(subtractor_4_bout));
  Multiplexer #(.enable("false")) multiplexer_8 (.in0(A[7]), .in1(A[15]), .out(multiplexer_8_out), .sel(_16_bit));
  Multiplexer #(.enable("false")) multiplexer_9 (
    .in0(subtractor_2_bout), .in1(subtractor_4_bout), .out(multiplexer_9_out), .sel(_16_bit));
  xnor xnor_2 (xnor_2_out, multiplexer_8_out, multiplexer_7_out);
  assign Carry_Out = decoder_1_out7 ? multiplexer_9_out : 1'bz;  // Controlled_Buffer controlled_buffer_12
  assign Result = decoder_1_out7 ? {subtractor_2_out[15], subtractor_3_out, subtractor_2_out[7], subtractor_1_out} : 16'bz;  // Controlled_Buffer controlled_buffer_13
  Multiplexer #(.enable("false")) multiplexer_10 (
    .in0(subtractor_1_bout), .in1(subtractor_3_bout), .out(multiplexer_10_out), .sel(_16_bit));
  xor xor_3 (xor_3_out, multiplexer_8_out, multiplexer_10_out);
  nor nor_2 (nor_2_out, xnor_2_out, xor_3_out);
  assign Overflow = decoder_1_out7 ? nor_2_out : 1'bz;  // Controlled_Buffer controlled_buffer_14

  // Notes on the sheet:
  //   NOT
  //   OR
  //   XOR
  //   AND
  //   LSH
  //   RSH
  //   ADD
  //   SUB
endmodule

module RAM_interface (
  input  Decrease_Address,
  input  _16_bit,
  input  Get_RAM,
  input  Set_RAM,
  input  [15:0] RAM_input,
  input  [15:0] RAM_Addres,
  input  [15:0] RAM_output,
  output _16_bit_2,
  output Get_RAM_2,
  output Set_RAM_2,
  output [15:0] RAM_input_2,
  output [15:0] RAM_Addres_2,
  output [15:0] RAM_output_2,
  output [15:0] New_RAM_Addres
);

  wire not_3_out, not_4_out, not_5_out, not_6_out, not_7_out, not_8_out, not_9_out, not_10_out, not_11_out,
       not_12_out, not_14_out, not_15_out, not_16_out, not_17_out;
  wire [0:0] not_13_out;
  wire [15:0] adder_1_out, subtractor_1_out;

  not not_1 (Get_RAM_2, not_3_out);
  not not_2 (Set_RAM_2, not_4_out);
  not not_3 (not_3_out, not_5_out);
  not not_4 (not_4_out, not_8_out);
  Multiplexer #(.width(16), .enable("false")) multiplexer_1 (
    .in0(RAM_Addres), .in1(subtractor_1_out), .out(RAM_Addres_2), .sel(Decrease_Address));
  not not_5 (not_5_out, not_6_out);
  not not_6 (not_6_out, not_9_out);
  not not_7 (not_7_out, not_12_out);
  not not_8 (not_8_out, not_7_out);
  not not_9 (not_9_out, not_10_out);
  not not_10 (not_10_out, not_15_out);
  not not_11 (not_11_out, not_16_out);
  not not_12 (not_12_out, not_11_out);
  Subtractor #(.width(16)) subtractor_1 (
    .a(RAM_Addres), .b({{14{1'b0}}, _16_bit, not_13_out[0]}), .out(subtractor_1_out));  // open: bin, bout
  Adder #(.width(16)) adder_1 (
    .a(RAM_Addres), .b({{14{1'b0}}, _16_bit, not_13_out[0]}), .out(adder_1_out));  // open: cin, cout
  not not_13 (not_13_out[0], _16_bit);
  not not_14 (not_14_out, Get_RAM);
  not not_15 (not_15_out, not_14_out);
  not not_16 (not_16_out, not_17_out);
  not not_17 (not_17_out, Set_RAM);
  Multiplexer #(.width(16), .enable("false")) multiplexer_2 (
    .in0(adder_1_out), .in1(subtractor_1_out), .out(New_RAM_Addres), .sel(Decrease_Address));

  assign _16_bit_2 = _16_bit;
  assign RAM_input_2 = RAM_input;
  assign RAM_output_2 = RAM_output;
endmodule

module Update_Clock (
  input  Start,
  output out_2,
  output out_3,
  output out_4,
  output out_5,
  output out_6,
  output out_7,
  output out_8,
  output out_9
);

  wire clock_1_out, not_1_out;

  not not_1 (not_1_out, Start);
  Clock clock_1 (.out(clock_1_out));
  D_Flip_Flop #(.trigger("low")) d_ff_1 (
    .clk(clock_1_out), .D(out_2), .Q(out_3), .preset(not_1_out));  // open: Qn, en, reset
  D_Flip_Flop #(.trigger("high")) d_ff_2 (
    .clk(clock_1_out), .D(out_9), .Q(out_2), .preset(not_1_out));  // open: Qn, en, reset
  D_Flip_Flop #(.trigger("high")) d_ff_3 (
    .clk(clock_1_out), .D(out_3), .Q(out_4), .reset(not_1_out));  // open: Qn, preset, en
  D_Flip_Flop #(.trigger("low")) d_ff_4 (
    .clk(clock_1_out), .D(out_4), .Q(out_5), .reset(not_1_out));  // open: Qn, preset, en
  D_Flip_Flop #(.trigger("high")) d_ff_5 (
    .clk(clock_1_out), .D(out_5), .Q(out_6), .reset(not_1_out));  // open: Qn, preset, en
  D_Flip_Flop #(.trigger("low")) d_ff_6 (
    .clk(clock_1_out), .D(out_6), .Q(out_7), .reset(not_1_out));  // open: Qn, preset, en
  D_Flip_Flop #(.trigger("high")) d_ff_7 (
    .clk(clock_1_out), .D(out_7), .Q(out_8), .reset(not_1_out));  // open: Qn, preset, en
  D_Flip_Flop #(.trigger("low")) d_ff_8 (
    .clk(clock_1_out), .D(out_8), .Q(out_9), .reset(not_1_out));  // open: Qn, preset, en
endmodule

module Command_Selector (
  input  [7:0] Stage,
  input  [7:0] OP,
  input  [15:0] RS,
  input  Carry_In,
  output Test,
  output Carry_Out,
  output [3:0] Register,
  output [3:0] Micro_opcode
);

  wire command_pass_1_carry_3, command_pass_1_enable_2, command_pass_1_test_3, command_pass_2_carry_3,
       command_pass_2_enable_2, command_pass_2_test_3, command_pass_3_carry_3, command_pass_3_enable_2,
       command_pass_3_test_3, command_pass_4_carry_3, command_pass_4_enable_2, command_pass_4_test_3,
       command_pass_5_carry_3, command_pass_5_enable_2, command_pass_5_test_3, command_pass_6_carry_3,
       command_pass_6_enable_2, command_pass_6_test_3, command_pass_7_carry_3, command_pass_7_enable_2,
       command_pass_7_test_3, command_pass_8_carry_3, command_pass_8_enable_2, command_pass_8_test_3,
       command_pass_9_carry_3, command_pass_9_enable_2, command_pass_9_test_3, command_pass_10_carry_3,
       command_pass_10_enable_2, command_pass_10_test_3, command_pass_11_carry_3, command_pass_11_enable_2,
       command_pass_11_test_3, command_pass_12_carry_3, command_pass_12_enable_2, command_pass_12_test_3,
       command_pass_13_carry_3, command_pass_13_enable_2, command_pass_13_test_3, command_pass_14_carry_3,
       command_pass_14_enable_2, command_pass_14_test_3, command_pass_15_carry_3, command_pass_15_enable_2,
       command_pass_15_test_3, command_pass_16_carry_3, command_pass_16_enable_2, command_pass_16_test_3,
       command_pass_17_carry_3, command_pass_17_enable_2, command_pass_17_test_3, command_pass_18_carry_3,
       command_pass_18_enable_2, command_pass_18_test_3, command_pass_19_carry_3, command_pass_19_enable_2,
       command_pass_19_test_3, command_pass_20_carry_3, command_pass_20_enable_2, command_pass_20_test_3,
       command_pass_21_carry_3, command_pass_21_enable_2, command_pass_21_test_3, command_pass_22_carry_3,
       command_pass_22_enable_2, command_pass_22_test_3, command_pass_23_carry_3, command_pass_23_enable_2,
       command_pass_23_test_3, command_pass_24_carry_3, command_pass_24_enable_2, command_pass_24_test_3,
       command_pass_25_carry_3, command_pass_25_enable_2, command_pass_25_test_3, command_pass_26_carry_3,
       command_pass_26_enable_2, command_pass_26_test_3, command_pass_27_carry_3, command_pass_27_enable_2,
       command_pass_27_test_3, command_pass_28_carry_3, command_pass_28_enable_2, command_pass_28_test_3,
       command_pass_29_carry_3, command_pass_29_enable_2, command_pass_29_test_3, command_pass_30_carry_3,
       command_pass_30_enable_2, command_pass_30_test_3, command_pass_31_carry_3, command_pass_31_test_3,
       command_pass_32_carry_3, command_pass_32_enable_2, command_pass_32_test_3, command_pass_33_carry_3,
       command_pass_33_enable_2, command_pass_33_test_3, command_pass_34_carry_3, command_pass_34_enable_2,
       command_pass_34_test_3, command_pass_35_carry_3, command_pass_35_enable_2, command_pass_35_test_3,
       command_pass_36_carry_3, command_pass_36_enable_2, command_pass_36_test_3, command_pass_37_carry_3,
       command_pass_37_enable_2, command_pass_37_test_3, command_pass_38_carry_3, command_pass_38_enable_2,
       command_pass_38_test_3, command_pass_39_carry_3, command_pass_39_enable_2, command_pass_39_test_3,
       command_pass_40_carry_3, command_pass_40_enable_2, command_pass_40_test_3, command_pass_41_carry_3,
       command_pass_41_enable_2, command_pass_41_test_3, command_pass_42_carry_3, command_pass_42_enable_2,
       command_pass_42_test_3, command_pass_43_carry_3, command_pass_43_enable_2, command_pass_43_test_3,
       command_pass_44_carry_3, command_pass_44_enable_2, command_pass_44_test_3, command_pass_45_carry_3,
       command_pass_45_enable_2, command_pass_45_test_3, command_pass_46_carry_3, command_pass_46_enable_2,
       command_pass_46_test_3, command_pass_47_carry_3, command_pass_47_enable_2, command_pass_47_test_3,
       command_pass_48_carry_3, command_pass_48_enable_2, command_pass_48_test_3, command_pass_49_carry_3,
       command_pass_49_enable_2, command_pass_49_test_3, command_pass_50_carry_3, command_pass_50_enable_2,
       command_pass_50_test_3, command_pass_51_carry_3, command_pass_51_enable_2, command_pass_51_test_3,
       command_pass_52_carry_3, command_pass_52_enable_2, command_pass_52_test_3, command_pass_53_carry_3,
       command_pass_53_enable_2, command_pass_53_test_3, command_pass_54_carry_3, command_pass_54_enable_2,
       command_pass_54_test_3, command_pass_55_carry_3, command_pass_55_enable_2, command_pass_55_test_3,
       undriven, undriven_2, undriven_3, undriven_4, undriven_5, undriven_6, undriven_7, undriven_8,
       undriven_9, undriven_10, undriven_11, undriven_12, undriven_13, undriven_14, undriven_15, undriven_16,
       undriven_17, undriven_18, undriven_31, undriven_32, undriven_33, undriven_34, undriven_35,
       undriven_36, undriven_37, undriven_38, undriven_39, undriven_40, undriven_41, undriven_42,
       undriven_55, undriven_56, undriven_57, undriven_58, undriven_59, undriven_60, undriven_61,
       undriven_62, undriven_63, undriven_64, undriven_65, undriven_66, undriven_79, undriven_80,
       undriven_81, undriven_82, undriven_83, undriven_84, undriven_85, undriven_86, undriven_87,
       undriven_88, undriven_89, undriven_90, undriven_103, undriven_104, undriven_105, undriven_106,
       undriven_107, undriven_108, undriven_109, undriven_110, undriven_111, undriven_112, undriven_113,
       undriven_114, undriven_127, undriven_128, undriven_129, undriven_130, undriven_131, undriven_132,
       undriven_133, undriven_134, undriven_135, undriven_136, undriven_137, undriven_138, undriven_151,
       undriven_152, undriven_153, undriven_154, undriven_155, undriven_156, undriven_157, undriven_158,
       undriven_159, undriven_160, undriven_171, undriven_172, undriven_173, undriven_174, undriven_175,
       undriven_176, undriven_177, undriven_178, undriven_179, undriven_180, undriven_191, undriven_192,
       undriven_193, undriven_196, undriven_197, undriven_198, undriven_201, undriven_202, undriven_205,
       undriven_206, undriven_209, undriven_210, undriven_213, undriven_214, undriven_217, undriven_218,
       undriven_221, undriven_222, undriven_225, undriven_226;
  wire [3:0] command_pass_1_opcode_3, command_pass_1_register_3, command_pass_2_opcode_3,
       command_pass_2_register_3, command_pass_3_opcode_3, command_pass_3_register_3,
       command_pass_4_opcode_3, command_pass_4_register_3, command_pass_5_opcode_3,
       command_pass_5_register_3, command_pass_6_opcode_3, command_pass_6_register_3,
       command_pass_7_opcode_3, command_pass_7_register_3, command_pass_8_opcode_3,
       command_pass_8_register_3, command_pass_9_opcode_3, command_pass_9_register_3,
       command_pass_10_opcode_3, command_pass_10_register_3, command_pass_11_opcode_3,
       command_pass_11_register_3, command_pass_12_opcode_3, command_pass_12_register_3,
       command_pass_13_opcode_3, command_pass_13_register_3, command_pass_14_opcode_3,
       command_pass_14_register_3, command_pass_15_opcode_3, command_pass_15_register_3,
       command_pass_16_opcode_3, command_pass_16_register_3, command_pass_17_opcode_3,
       command_pass_17_register_3, command_pass_18_opcode_3, command_pass_18_register_3,
       command_pass_19_opcode_3, command_pass_19_register_3, command_pass_20_opcode_3,
       command_pass_20_register_3, command_pass_21_opcode_3, command_pass_21_register_3,
       command_pass_22_opcode_3, command_pass_22_register_3, command_pass_23_opcode_3,
       command_pass_23_register_3, command_pass_24_opcode_3, command_pass_24_register_3,
       command_pass_25_opcode_3, command_pass_25_register_3, command_pass_26_opcode_3,
       command_pass_26_register_3, command_pass_27_opcode_3, command_pass_27_register_3,
       command_pass_28_opcode_3, command_pass_28_register_3, command_pass_29_opcode_3,
       command_pass_29_register_3, command_pass_30_opcode_3, command_pass_30_register_3,
       command_pass_31_opcode_3, command_pass_31_register_3, command_pass_32_opcode_3,
       command_pass_32_register_3, command_pass_33_opcode_3, command_pass_33_register_3,
       command_pass_34_opcode_3, command_pass_34_register_3, command_pass_35_opcode_3,
       command_pass_35_register_3, command_pass_36_opcode_3, command_pass_36_register_3,
       command_pass_37_opcode_3, command_pass_37_register_3, command_pass_38_opcode_3,
       command_pass_38_register_3, command_pass_39_opcode_3, command_pass_39_register_3,
       command_pass_40_opcode_3, command_pass_40_register_3, command_pass_41_opcode_3,
       command_pass_41_register_3, command_pass_42_opcode_3, command_pass_42_register_3,
       command_pass_43_opcode_3, command_pass_43_register_3, command_pass_44_opcode_3,
       command_pass_44_register_3, command_pass_45_opcode_3, command_pass_45_register_3,
       command_pass_46_opcode_3, command_pass_46_register_3, command_pass_47_opcode_3,
       command_pass_47_register_3, command_pass_48_opcode_3, command_pass_48_register_3,
       command_pass_49_opcode_3, command_pass_49_register_3, command_pass_50_opcode_3,
       command_pass_50_register_3, command_pass_51_opcode_3, command_pass_51_register_3,
       command_pass_52_opcode_3, command_pass_52_register_3, command_pass_53_opcode_3,
       command_pass_53_register_3, command_pass_54_opcode_3, command_pass_54_register_3,
       command_pass_55_opcode_3, command_pass_55_register_3, undriven_19, undriven_20, undriven_21,
       undriven_22, undriven_23, undriven_24, undriven_25, undriven_26, undriven_27, undriven_28,
       undriven_29, undriven_30, undriven_43, undriven_44, undriven_45, undriven_46, undriven_47,
       undriven_48, undriven_49, undriven_50, undriven_51, undriven_52, undriven_53, undriven_54,
       undriven_67, undriven_68, undriven_69, undriven_70, undriven_71, undriven_72, undriven_73,
       undriven_74, undriven_75, undriven_76, undriven_77, undriven_78, undriven_91, undriven_92,
       undriven_93, undriven_94, undriven_95, undriven_96, undriven_97, undriven_98, undriven_99,
       undriven_100, undriven_101, undriven_102, undriven_115, undriven_116, undriven_117, undriven_118,
       undriven_119, undriven_120, undriven_121, undriven_122, undriven_123, undriven_124, undriven_125,
       undriven_126, undriven_139, undriven_140, undriven_141, undriven_142, undriven_143, undriven_144,
       undriven_145, undriven_146, undriven_147, undriven_148, undriven_149, undriven_150, undriven_161,
       undriven_162, undriven_163, undriven_164, undriven_165, undriven_166, undriven_167, undriven_168,
       undriven_169, undriven_170, undriven_181, undriven_182, undriven_183, undriven_184, undriven_185,
       undriven_186, undriven_187, undriven_188, undriven_189, undriven_190, undriven_194, undriven_195,
       undriven_199, undriven_200, undriven_203, undriven_204, undriven_207, undriven_208, undriven_211,
       undriven_212, undriven_215, undriven_216, undriven_219, undriven_220, undriven_223, undriven_224,
       undriven_227, undriven_228;

  Command_Pass command_pass_1 (
    .Enable(undriven), .Test(1'b0), .Carry(1'b0), .Register(4'b0000), .Opcode(4'b0010),
    .Enable_2(command_pass_1_enable_2), .Test_3(command_pass_1_test_3), .Carry_3(command_pass_1_carry_3),
    .Register_3(command_pass_1_register_3), .Opcode_3(command_pass_1_opcode_3), .Test_2(undriven_7),
    .Carry_2(undriven_13), .Register_2(undriven_19), .Opcode_2(undriven_25));
  Command_Pass command_pass_2 (
    .Enable(undriven_2), .Test(1'b0), .Carry(1'b0), .Register(4'b0000), .Opcode(4'b0000),
    .Enable_2(command_pass_2_enable_2), .Test_3(command_pass_2_test_3), .Carry_3(command_pass_2_carry_3),
    .Register_3(command_pass_2_register_3), .Opcode_3(command_pass_2_opcode_3), .Test_2(undriven_8),
    .Carry_2(undriven_14), .Register_2(undriven_20), .Opcode_2(undriven_26));
  Command_Pass command_pass_3 (
    .Enable(undriven_3), .Test(1'b0), .Carry(1'b0), .Register(4'b0000), .Opcode(4'b0000),
    .Enable_2(command_pass_3_enable_2), .Test_3(command_pass_3_test_3), .Carry_3(command_pass_3_carry_3),
    .Register_3(command_pass_3_register_3), .Opcode_3(command_pass_3_opcode_3), .Test_2(undriven_9),
    .Carry_2(undriven_15), .Register_2(undriven_21), .Opcode_2(undriven_27));
  Command_Pass command_pass_4 (
    .Enable(undriven_4), .Test(1'b0), .Carry(1'b0), .Register(4'b0000), .Opcode(4'b0000),
    .Enable_2(command_pass_4_enable_2), .Test_3(command_pass_4_test_3), .Carry_3(command_pass_4_carry_3),
    .Register_3(command_pass_4_register_3), .Opcode_3(command_pass_4_opcode_3), .Test_2(undriven_10),
    .Carry_2(undriven_16), .Register_2(undriven_22), .Opcode_2(undriven_28));
  Command_Pass command_pass_5 (
    .Enable(undriven_5), .Test(1'b0), .Carry(1'b0), .Register(4'b0000), .Opcode(4'b0000),
    .Enable_2(command_pass_5_enable_2), .Test_3(command_pass_5_test_3), .Carry_3(command_pass_5_carry_3),
    .Register_3(command_pass_5_register_3), .Opcode_3(command_pass_5_opcode_3), .Test_2(undriven_11),
    .Carry_2(undriven_17), .Register_2(undriven_23), .Opcode_2(undriven_29));
  Command_Pass command_pass_6 (
    .Enable(undriven_6), .Test(1'b0), .Carry(1'b0), .Register(4'b0000), .Opcode(4'b0000),
    .Enable_2(command_pass_6_enable_2), .Test_3(command_pass_6_test_3), .Carry_3(command_pass_6_carry_3),
    .Register_3(command_pass_6_register_3), .Opcode_3(command_pass_6_opcode_3), .Test_2(undriven_12),
    .Carry_2(undriven_18), .Register_2(undriven_24), .Opcode_2(undriven_30));
  Command_Pass command_pass_7 (
    .Enable(command_pass_1_enable_2), .Test(1'b0), .Carry(1'b0), .Register(4'b0000), .Opcode(4'b0010),
    .Enable_2(command_pass_7_enable_2), .Test_3(command_pass_7_test_3), .Carry_3(command_pass_7_carry_3),
    .Register_3(command_pass_7_register_3), .Opcode_3(command_pass_7_opcode_3), .Test_2(undriven_31),
    .Carry_2(undriven_37), .Register_2(undriven_43), .Opcode_2(undriven_49));
  Command_Pass command_pass_8 (
    .Enable(command_pass_2_enable_2), .Test(1'b0), .Carry(1'b0), .Register(4'b0000), .Opcode(4'b0000),
    .Enable_2(command_pass_8_enable_2), .Test_3(command_pass_8_test_3), .Carry_3(command_pass_8_carry_3),
    .Register_3(command_pass_8_register_3), .Opcode_3(command_pass_8_opcode_3), .Test_2(undriven_32),
    .Carry_2(undriven_38), .Register_2(undriven_44), .Opcode_2(undriven_50));
  Command_Pass command_pass_9 (
    .Enable(command_pass_3_enable_2), .Test(1'b0), .Carry(1'b0), .Register(4'b0000), .Opcode(4'b0000),
    .Enable_2(command_pass_9_enable_2), .Test_3(command_pass_9_test_3), .Carry_3(command_pass_9_carry_3),
    .Register_3(command_pass_9_register_3), .Opcode_3(command_pass_9_opcode_3), .Test_2(undriven_33),
    .Carry_2(undriven_39), .Register_2(undriven_45), .Opcode_2(undriven_51));
  Command_Pass command_pass_10 (
    .Enable(command_pass_4_enable_2), .Test(1'b0), .Carry(1'b0), .Register(4'b0000), .Opcode(4'b0000),
    .Enable_2(command_pass_10_enable_2), .Test_3(command_pass_10_test_3), .Carry_3(command_pass_10_carry_3),
    .Register_3(command_pass_10_register_3), .Opcode_3(command_pass_10_opcode_3), .Test_2(undriven_34),
    .Carry_2(undriven_40), .Register_2(undriven_46), .Opcode_2(undriven_52));
  Command_Pass command_pass_11 (
    .Enable(command_pass_5_enable_2), .Test(1'b0), .Carry(1'b0), .Register(4'b0000), .Opcode(4'b0000),
    .Enable_2(command_pass_11_enable_2), .Test_3(command_pass_11_test_3), .Carry_3(command_pass_11_carry_3),
    .Register_3(command_pass_11_register_3), .Opcode_3(command_pass_11_opcode_3), .Test_2(undriven_35),
    .Carry_2(undriven_41), .Register_2(undriven_47), .Opcode_2(undriven_53));
  Command_Pass command_pass_12 (
    .Enable(command_pass_6_enable_2), .Test(1'b0), .Carry(1'b0), .Register(4'b0000), .Opcode(4'b0000),
    .Enable_2(command_pass_12_enable_2), .Test_3(command_pass_12_test_3), .Carry_3(command_pass_12_carry_3),
    .Register_3(command_pass_12_register_3), .Opcode_3(command_pass_12_opcode_3), .Test_2(undriven_36),
    .Carry_2(undriven_42), .Register_2(undriven_48), .Opcode_2(undriven_54));
  Command_Pass command_pass_13 (
    .Enable(command_pass_7_enable_2), .Test(1'b0), .Carry(1'b0), .Register(4'b0000), .Opcode(4'b0001),
    .Enable_2(command_pass_13_enable_2), .Test_3(command_pass_13_test_3), .Carry_3(command_pass_13_carry_3),
    .Register_3(command_pass_13_register_3), .Opcode_3(command_pass_13_opcode_3), .Test_2(undriven_55),
    .Carry_2(undriven_61), .Register_2(undriven_67), .Opcode_2(undriven_73));
  Command_Pass command_pass_14 (
    .Enable(command_pass_8_enable_2), .Test(1'b0), .Carry(1'b0), .Register(4'b0000), .Opcode(4'b0000),
    .Enable_2(command_pass_14_enable_2), .Test_3(command_pass_14_test_3), .Carry_3(command_pass_14_carry_3),
    .Register_3(command_pass_14_register_3), .Opcode_3(command_pass_14_opcode_3), .Test_2(undriven_56),
    .Carry_2(undriven_62), .Register_2(undriven_68), .Opcode_2(undriven_74));
  Command_Pass command_pass_15 (
    .Enable(command_pass_9_enable_2), .Test(1'b0), .Carry(1'b0), .Register(4'b0000), .Opcode(4'b0000),
    .Enable_2(command_pass_15_enable_2), .Test_3(command_pass_15_test_3), .Carry_3(command_pass_15_carry_3),
    .Register_3(command_pass_15_register_3), .Opcode_3(command_pass_15_opcode_3), .Test_2(undriven_57),
    .Carry_2(undriven_63), .Register_2(undriven_69), .Opcode_2(undriven_75));
  Command_Pass command_pass_16 (
    .Enable(command_pass_10_enable_2), .Test(1'b0), .Carry(1'b0), .Register(4'b0000), .Opcode(4'b0000),
    .Enable_2(command_pass_16_enable_2), .Test_3(command_pass_16_test_3), .Carry_3(command_pass_16_carry_3),
    .Register_3(command_pass_16_register_3), .Opcode_3(command_pass_16_opcode_3), .Test_2(undriven_58),
    .Carry_2(undriven_64), .Register_2(undriven_70), .Opcode_2(undriven_76));
  Command_Pass command_pass_17 (
    .Enable(command_pass_11_enable_2), .Test(1'b0), .Carry(1'b0), .Register(4'b0000), .Opcode(4'b0000),
    .Enable_2(command_pass_17_enable_2), .Test_3(command_pass_17_test_3), .Carry_3(command_pass_17_carry_3),
    .Register_3(command_pass_17_register_3), .Opcode_3(command_pass_17_opcode_3), .Test_2(undriven_59),
    .Carry_2(undriven_65), .Register_2(undriven_71), .Opcode_2(undriven_77));
  Command_Pass command_pass_18 (
    .Enable(command_pass_12_enable_2), .Test(1'b0), .Carry(1'b0), .Register(4'b0000), .Opcode(4'b0000),
    .Enable_2(command_pass_18_enable_2), .Test_3(command_pass_18_test_3), .Carry_3(command_pass_18_carry_3),
    .Register_3(command_pass_18_register_3), .Opcode_3(command_pass_18_opcode_3), .Test_2(undriven_60),
    .Carry_2(undriven_66), .Register_2(undriven_72), .Opcode_2(undriven_78));
  Command_Pass command_pass_19 (
    .Enable(command_pass_13_enable_2), .Test(1'b0), .Carry(1'b0), .Register(4'b1110), .Opcode(4'b0100),
    .Enable_2(command_pass_19_enable_2), .Test_3(command_pass_19_test_3), .Carry_3(command_pass_19_carry_3),
    .Register_3(command_pass_19_register_3), .Opcode_3(command_pass_19_opcode_3), .Test_2(undriven_79),
    .Carry_2(undriven_85), .Register_2(undriven_91), .Opcode_2(undriven_97));
  Command_Pass command_pass_20 (
    .Enable(command_pass_14_enable_2), .Test(1'b0), .Carry(1'b0), .Register(4'b0000), .Opcode(4'b0000),
    .Enable_2(command_pass_20_enable_2), .Test_3(command_pass_20_test_3), .Carry_3(command_pass_20_carry_3),
    .Register_3(command_pass_20_register_3), .Opcode_3(command_pass_20_opcode_3), .Test_2(undriven_80),
    .Carry_2(undriven_86), .Register_2(undriven_92), .Opcode_2(undriven_98));
  Command_Pass command_pass_21 (
    .Enable(command_pass_15_enable_2), .Test(1'b0), .Carry(1'b0), .Register(4'b0000), .Opcode(4'b0000),
    .Enable_2(command_pass_21_enable_2), .Test_3(command_pass_21_test_3), .Carry_3(command_pass_21_carry_3),
    .Register_3(command_pass_21_register_3), .Opcode_3(command_pass_21_opcode_3), .Test_2(undriven_81),
    .Carry_2(undriven_87), .Register_2(undriven_93), .Opcode_2(undriven_99));
  Command_Pass command_pass_22 (
    .Enable(command_pass_16_enable_2), .Test(1'b0), .Carry(1'b0), .Register(4'b0000), .Opcode(4'b0000),
    .Enable_2(command_pass_22_enable_2), .Test_3(command_pass_22_test_3), .Carry_3(command_pass_22_carry_3),
    .Register_3(command_pass_22_register_3), .Opcode_3(command_pass_22_opcode_3), .Test_2(undriven_82),
    .Carry_2(undriven_88), .Register_2(undriven_94), .Opcode_2(undriven_100));
  Command_Pass command_pass_23 (
    .Enable(command_pass_17_enable_2), .Test(1'b0), .Carry(1'b0), .Register(4'b0000), .Opcode(4'b0000),
    .Enable_2(command_pass_23_enable_2), .Test_3(command_pass_23_test_3), .Carry_3(command_pass_23_carry_3),
    .Register_3(command_pass_23_register_3), .Opcode_3(command_pass_23_opcode_3), .Test_2(undriven_83),
    .Carry_2(undriven_89), .Register_2(undriven_95), .Opcode_2(undriven_101));
  Command_Pass command_pass_24 (
    .Enable(command_pass_18_enable_2), .Test(1'b0), .Carry(1'b0), .Register(4'b0000), .Opcode(4'b0000),
    .Enable_2(command_pass_24_enable_2), .Test_3(command_pass_24_test_3), .Carry_3(command_pass_24_carry_3),
    .Register_3(command_pass_24_register_3), .Opcode_3(command_pass_24_opcode_3), .Test_2(undriven_84),
    .Carry_2(undriven_90), .Register_2(undriven_96), .Opcode_2(undriven_102));
  Command_Pass command_pass_25 (
    .Enable(command_pass_19_enable_2), .Test(1'b0), .Carry(1'b0), .Register(4'b1100), .Opcode(4'b0101),
    .Enable_2(command_pass_25_enable_2), .Test_3(command_pass_25_test_3), .Carry_3(command_pass_25_carry_3),
    .Register_3(command_pass_25_register_3), .Opcode_3(command_pass_25_opcode_3), .Test_2(undriven_103),
    .Carry_2(undriven_109), .Register_2(undriven_115), .Opcode_2(undriven_121));
  Command_Pass command_pass_26 (
    .Enable(command_pass_20_enable_2), .Test(1'b0), .Carry(1'b0), .Register(4'b0000), .Opcode(4'b0000),
    .Enable_2(command_pass_26_enable_2), .Test_3(command_pass_26_test_3), .Carry_3(command_pass_26_carry_3),
    .Register_3(command_pass_26_register_3), .Opcode_3(command_pass_26_opcode_3), .Test_2(undriven_104),
    .Carry_2(undriven_110), .Register_2(undriven_116), .Opcode_2(undriven_122));
  Command_Pass command_pass_27 (
    .Enable(command_pass_21_enable_2), .Test(1'b0), .Carry(1'b0), .Register(4'b0000), .Opcode(4'b0000),
    .Enable_2(command_pass_27_enable_2), .Test_3(command_pass_27_test_3), .Carry_3(command_pass_27_carry_3),
    .Register_3(command_pass_27_register_3), .Opcode_3(command_pass_27_opcode_3), .Test_2(undriven_105),
    .Carry_2(undriven_111), .Register_2(undriven_117), .Opcode_2(undriven_123));
  Command_Pass command_pass_28 (
    .Enable(command_pass_22_enable_2), .Test(1'b0), .Carry(1'b0), .Register(4'b0000), .Opcode(4'b0000),
    .Enable_2(command_pass_28_enable_2), .Test_3(command_pass_28_test_3), .Carry_3(command_pass_28_carry_3),
    .Register_3(command_pass_28_register_3), .Opcode_3(command_pass_28_opcode_3), .Test_2(undriven_106),
    .Carry_2(undriven_112), .Register_2(undriven_118), .Opcode_2(undriven_124));
  Command_Pass command_pass_29 (
    .Enable(command_pass_23_enable_2), .Test(1'b0), .Carry(1'b0), .Register(4'b0000), .Opcode(4'b0000),
    .Enable_2(command_pass_29_enable_2), .Test_3(command_pass_29_test_3), .Carry_3(command_pass_29_carry_3),
    .Register_3(command_pass_29_register_3), .Opcode_3(command_pass_29_opcode_3), .Test_2(undriven_107),
    .Carry_2(undriven_113), .Register_2(undriven_119), .Opcode_2(undriven_125));
  Command_Pass command_pass_30 (
    .Enable(command_pass_24_enable_2), .Test(1'b0), .Carry(1'b0), .Register(4'b0000), .Opcode(4'b0000),
    .Enable_2(command_pass_30_enable_2), .Test_3(command_pass_30_test_3), .Carry_3(command_pass_30_carry_3),
    .Register_3(command_pass_30_register_3), .Opcode_3(command_pass_30_opcode_3), .Test_2(undriven_108),
    .Carry_2(undriven_114), .Register_2(undriven_120), .Opcode_2(undriven_126));
  Command_Pass command_pass_31 (
    .Enable(command_pass_25_enable_2), .Test(1'b0), .Carry(1'b0), .Register(4'b0000), .Opcode(4'b0000),
    .Test_3(command_pass_31_test_3), .Carry_3(command_pass_31_carry_3),
    .Register_3(command_pass_31_register_3), .Opcode_3(command_pass_31_opcode_3), .Test_2(undriven_127),
    .Carry_2(undriven_133), .Register_2(undriven_139), .Opcode_2(undriven_145));  // open: Enable_2
  Command_Pass command_pass_32 (
    .Enable(command_pass_26_enable_2), .Test(1'b0), .Carry(1'b0), .Register(4'b0000), .Opcode(4'b0000),
    .Enable_2(command_pass_32_enable_2), .Test_3(command_pass_32_test_3), .Carry_3(command_pass_32_carry_3),
    .Register_3(command_pass_32_register_3), .Opcode_3(command_pass_32_opcode_3), .Test_2(undriven_128),
    .Carry_2(undriven_134), .Register_2(undriven_140), .Opcode_2(undriven_146));
  Command_Pass command_pass_33 (
    .Enable(command_pass_27_enable_2), .Test(1'b0), .Carry(1'b0), .Register(4'b0000), .Opcode(4'b0000),
    .Enable_2(command_pass_33_enable_2), .Test_3(command_pass_33_test_3), .Carry_3(command_pass_33_carry_3),
    .Register_3(command_pass_33_register_3), .Opcode_3(command_pass_33_opcode_3), .Test_2(undriven_129),
    .Carry_2(undriven_135), .Register_2(undriven_141), .Opcode_2(undriven_147));
  Command_Pass command_pass_34 (
    .Enable(command_pass_28_enable_2), .Test(1'b0), .Carry(1'b0), .Register(4'b0000), .Opcode(4'b0000),
    .Enable_2(command_pass_34_enable_2), .Test_3(command_pass_34_test_3), .Carry_3(command_pass_34_carry_3),
    .Register_3(command_pass_34_register_3), .Opcode_3(command_pass_34_opcode_3), .Test_2(undriven_130),
    .Carry_2(undriven_136), .Register_2(undriven_142), .Opcode_2(undriven_148));
  Command_Pass command_pass_35 (
    .Enable(command_pass_29_enable_2), .Test(1'b0), .Carry(1'b0), .Register(4'b0000), .Opcode(4'b0000),
    .Enable_2(command_pass_35_enable_2), .Test_3(command_pass_35_test_3), .Carry_3(command_pass_35_carry_3),
    .Register_3(command_pass_35_register_3), .Opcode_3(command_pass_35_opcode_3), .Test_2(undriven_131),
    .Carry_2(undriven_137), .Register_2(undriven_143), .Opcode_2(undriven_149));
  Command_Pass command_pass_36 (
    .Enable(command_pass_30_enable_2), .Test(1'b0), .Carry(1'b0), .Register(4'b0000), .Opcode(4'b0000),
    .Enable_2(command_pass_36_enable_2), .Test_3(command_pass_36_test_3), .Carry_3(command_pass_36_carry_3),
    .Register_3(command_pass_36_register_3), .Opcode_3(command_pass_36_opcode_3), .Test_2(undriven_132),
    .Carry_2(undriven_138), .Register_2(undriven_144), .Opcode_2(undriven_150));
  Command_Pass command_pass_37 (
    .Enable(command_pass_32_enable_2), .Test(1'b0), .Carry(1'b0), .Register(4'b0000), .Opcode(4'b0000),
    .Enable_2(command_pass_37_enable_2), .Test_3(command_pass_37_test_3), .Carry_3(command_pass_37_carry_3),
    .Register_3(command_pass_37_register_3), .Opcode_3(command_pass_37_opcode_3), .Test_2(undriven_151),
    .Carry_2(undriven_156), .Register_2(undriven_161), .Opcode_2(undriven_166));
  Command_Pass command_pass_38 (
    .Enable(command_pass_33_enable_2), .Test(1'b0), .Carry(1'b0), .Register(4'b0000), .Opcode(4'b0000),
    .Enable_2(command_pass_38_enable_2), .Test_3(command_pass_38_test_3), .Carry_3(command_pass_38_carry_3),
    .Register_3(command_pass_38_register_3), .Opcode_3(command_pass_38_opcode_3), .Test_2(undriven_152),
    .Carry_2(undriven_157), .Register_2(undriven_162), .Opcode_2(undriven_167));
  Command_Pass command_pass_39 (
    .Enable(command_pass_34_enable_2), .Test(1'b0), .Carry(1'b0), .Register(4'b0000), .Opcode(4'b0000),
    .Enable_2(command_pass_39_enable_2), .Test_3(command_pass_39_test_3), .Carry_3(command_pass_39_carry_3),
    .Register_3(command_pass_39_register_3), .Opcode_3(command_pass_39_opcode_3), .Test_2(undriven_153),
    .Carry_2(undriven_158), .Register_2(undriven_163), .Opcode_2(undriven_168));
  Command_Pass command_pass_40 (
    .Enable(command_pass_35_enable_2), .Test(1'b0), .Carry(1'b0), .Register(4'b0000), .Opcode(4'b0000),
    .Enable_2(command_pass_40_enable_2), .Test_3(command_pass_40_test_3), .Carry_3(command_pass_40_carry_3),
    .Register_3(command_pass_40_register_3), .Opcode_3(command_pass_40_opcode_3), .Test_2(undriven_154),
    .Carry_2(undriven_159), .Register_2(undriven_164), .Opcode_2(undriven_169));
  Command_Pass command_pass_41 (
    .Enable(command_pass_36_enable_2), .Test(1'b0), .Carry(1'b0), .Register(4'b0000), .Opcode(4'b0000),
    .Enable_2(command_pass_41_enable_2), .Test_3(command_pass_41_test_3), .Carry_3(command_pass_41_carry_3),
    .Register_3(command_pass_41_register_3), .Opcode_3(command_pass_41_opcode_3), .Test_2(undriven_155),
    .Carry_2(undriven_160), .Register_2(undriven_165), .Opcode_2(undriven_170));
  Command_Pass command_pass_42 (
    .Enable(command_pass_37_enable_2), .Test(1'b0), .Carry(1'b0), .Register(4'b0000), .Opcode(4'b0000),
    .Enable_2(command_pass_42_enable_2), .Test_3(command_pass_42_test_3), .Carry_3(command_pass_42_carry_3),
    .Register_3(command_pass_42_register_3), .Opcode_3(command_pass_42_opcode_3), .Test_2(undriven_171),
    .Carry_2(undriven_176), .Register_2(undriven_181), .Opcode_2(undriven_186));
  Command_Pass command_pass_43 (
    .Enable(command_pass_38_enable_2), .Test(1'b0), .Carry(1'b0), .Register(4'b0000), .Opcode(4'b0000),
    .Enable_2(command_pass_43_enable_2), .Test_3(command_pass_43_test_3), .Carry_3(command_pass_43_carry_3),
    .Register_3(command_pass_43_register_3), .Opcode_3(command_pass_43_opcode_3), .Test_2(undriven_172),
    .Carry_2(undriven_177), .Register_2(undriven_182), .Opcode_2(undriven_187));
  Command_Pass command_pass_44 (
    .Enable(command_pass_39_enable_2), .Test(1'b0), .Carry(1'b0), .Register(4'b0000), .Opcode(4'b0000),
    .Enable_2(command_pass_44_enable_2), .Test_3(command_pass_44_test_3), .Carry_3(command_pass_44_carry_3),
    .Register_3(command_pass_44_register_3), .Opcode_3(command_pass_44_opcode_3), .Test_2(undriven_173),
    .Carry_2(undriven_178), .Register_2(undriven_183), .Opcode_2(undriven_188));
  Command_Pass command_pass_45 (
    .Enable(command_pass_40_enable_2), .Test(1'b0), .Carry(1'b0), .Register(4'b0000), .Opcode(4'b0000),
    .Enable_2(command_pass_45_enable_2), .Test_3(command_pass_45_test_3), .Carry_3(command_pass_45_carry_3),
    .Register_3(command_pass_45_register_3), .Opcode_3(command_pass_45_opcode_3), .Test_2(undriven_174),
    .Carry_2(undriven_179), .Register_2(undriven_184), .Opcode_2(undriven_189));
  Command_Pass command_pass_46 (
    .Enable(command_pass_41_enable_2), .Test(1'b0), .Carry(1'b0), .Register(4'b0000), .Opcode(4'b0000),
    .Enable_2(command_pass_46_enable_2), .Test_3(command_pass_46_test_3), .Carry_3(command_pass_46_carry_3),
    .Register_3(command_pass_46_register_3), .Opcode_3(command_pass_46_opcode_3), .Test_2(undriven_175),
    .Carry_2(undriven_180), .Register_2(undriven_185), .Opcode_2(undriven_190));
  Pull_Resistor pull_resistor_1 (.node(Test));
  Pull_Resistor pull_resistor_2 (.node(Carry_Out));
  Pull_Resistor pull_resistor_3 (.node(Register));
  Pull_Resistor pull_resistor_4 (.node(Micro_opcode));
  Command_Pass command_pass_47 (
    .Enable(undriven_191), .Test(1'b0), .Carry(1'b0), .Register(4'b0000), .Opcode(4'b0000),
    .Enable_2(command_pass_47_enable_2), .Test_3(command_pass_47_test_3), .Carry_3(command_pass_47_carry_3),
    .Register_3(command_pass_47_register_3), .Opcode_3(command_pass_47_opcode_3), .Test_2(undriven_192),
    .Carry_2(undriven_193), .Register_2(undriven_194), .Opcode_2(undriven_195));
  Command_Pass command_pass_48 (
    .Enable(undriven_196), .Test(1'b0), .Carry(1'b0), .Register(4'b0000), .Opcode(4'b0000),
    .Enable_2(command_pass_48_enable_2), .Test_3(command_pass_48_test_3), .Carry_3(command_pass_48_carry_3),
    .Register_3(command_pass_48_register_3), .Opcode_3(command_pass_48_opcode_3), .Test_2(undriven_197),
    .Carry_2(undriven_198), .Register_2(undriven_199), .Opcode_2(undriven_200));
  Command_Pass command_pass_49 (
    .Enable(command_pass_48_enable_2), .Test(1'b0), .Carry(1'b0), .Register(4'b0000), .Opcode(4'b0000),
    .Enable_2(command_pass_49_enable_2), .Test_3(command_pass_49_test_3), .Carry_3(command_pass_49_carry_3),
    .Register_3(command_pass_49_register_3), .Opcode_3(command_pass_49_opcode_3), .Test_2(undriven_201),
    .Carry_2(undriven_202), .Register_2(undriven_203), .Opcode_2(undriven_204));
  Command_Pass command_pass_50 (
    .Enable(command_pass_49_enable_2), .Test(1'b0), .Carry(1'b0), .Register(4'b0000), .Opcode(4'b0000),
    .Enable_2(command_pass_50_enable_2), .Test_3(command_pass_50_test_3), .Carry_3(command_pass_50_carry_3),
    .Register_3(command_pass_50_register_3), .Opcode_3(command_pass_50_opcode_3), .Test_2(undriven_205),
    .Carry_2(undriven_206), .Register_2(undriven_207), .Opcode_2(undriven_208));
  Command_Pass command_pass_51 (
    .Enable(command_pass_50_enable_2), .Test(1'b0), .Carry(1'b0), .Register(4'b0000), .Opcode(4'b0000),
    .Enable_2(command_pass_51_enable_2), .Test_3(command_pass_51_test_3), .Carry_3(command_pass_51_carry_3),
    .Register_3(command_pass_51_register_3), .Opcode_3(command_pass_51_opcode_3), .Test_2(undriven_209),
    .Carry_2(undriven_210), .Register_2(undriven_211), .Opcode_2(undriven_212));
  Command_Pass command_pass_52 (
    .Enable(command_pass_51_enable_2), .Test(1'b0), .Carry(1'b0), .Register(4'b0000), .Opcode(4'b0000),
    .Enable_2(command_pass_52_enable_2), .Test_3(command_pass_52_test_3), .Carry_3(command_pass_52_carry_3),
    .Register_3(command_pass_52_register_3), .Opcode_3(command_pass_52_opcode_3), .Test_2(undriven_213),
    .Carry_2(undriven_214), .Register_2(undriven_215), .Opcode_2(undriven_216));
  Command_Pass command_pass_53 (
    .Enable(command_pass_52_enable_2), .Test(1'b0), .Carry(1'b0), .Register(4'b0000), .Opcode(4'b0000),
    .Enable_2(command_pass_53_enable_2), .Test_3(command_pass_53_test_3), .Carry_3(command_pass_53_carry_3),
    .Register_3(command_pass_53_register_3), .Opcode_3(command_pass_53_opcode_3), .Test_2(undriven_217),
    .Carry_2(undriven_218), .Register_2(undriven_219), .Opcode_2(undriven_220));
  Command_Pass command_pass_54 (
    .Enable(command_pass_53_enable_2), .Test(1'b0), .Carry(1'b0), .Register(4'b0000), .Opcode(4'b0000),
    .Enable_2(command_pass_54_enable_2), .Test_3(command_pass_54_test_3), .Carry_3(command_pass_54_carry_3),
    .Register_3(command_pass_54_register_3), .Opcode_3(command_pass_54_opcode_3), .Test_2(undriven_221),
    .Carry_2(undriven_222), .Register_2(undriven_223), .Opcode_2(undriven_224));
  Command_Pass command_pass_55 (
    .Enable(command_pass_54_enable_2), .Test(1'b0), .Carry(1'b0), .Register(4'b0000), .Opcode(4'b0000),
    .Enable_2(command_pass_55_enable_2), .Test_3(command_pass_55_test_3), .Carry_3(command_pass_55_carry_3),
    .Register_3(command_pass_55_register_3), .Opcode_3(command_pass_55_opcode_3), .Test_2(undriven_225),
    .Carry_2(undriven_226), .Register_2(undriven_227), .Opcode_2(undriven_228));

  // Notes on the sheet:
  //   RS0-7
  //   C
  //   RGA
  //   OP4
  //   OP3
  //   JUMP
  //   JUMP
  //   JUMP
  //   JUMP
  //   JUMP
  //   JUMP
  //   JUMP
endmodule

module Command_Pass (
  input  Enable,
  input  Test,
  input  Carry,
  input  [3:0] Register,
  input  [3:0] Opcode,
  input  Test_2,
  input  Carry_2,
  input  [3:0] Register_2,
  input  [3:0] Opcode_2,
  output Test_3,
  output Carry_3,
  output [3:0] Register_3,
  output [3:0] Opcode_3,
  output Enable_2
);

  assign Test_2 = Enable ? Test : 1'bz;  // Controlled_Buffer controlled_buffer_1
  Controlled_Buffer controlled_buffer_2 (.in(Carry), .en(Enable));  // open: out
  assign Register_2 = Enable ? Register : 4'bz;  // Controlled_Buffer controlled_buffer_3
  assign Opcode_2 = Enable ? Opcode : 4'bz;  // Controlled_Buffer controlled_buffer_4

  assign Carry_3 = Carry_2;
  assign Enable_2 = Enable;
  assign Opcode_3 = Opcode_2;
  assign Register_3 = Register_2;
  assign Test_3 = Test_2;
endmodule

module Value_Tester (
  input  Overflow,
  input  Carry,
  input  [7:0] Flags_In,
  input  [15:0] Test_Reg,
  input  _16_bit,
  output [7:0] Flags_Out
);

  nor nor_1 (Flags_Out[0], Test_Reg[0], Test_Reg[1], Test_Reg[2], Test_Reg[3], Test_Reg[4], Test_Reg[5], Test_Reg[6], Test_Reg[7], Test_Reg[8], Test_Reg[9], Test_Reg[10], Test_Reg[11], Test_Reg[12], Test_Reg[13], Test_Reg[14], Test_Reg[15]);
  Multiplexer #(.enable("false")) multiplexer_1 (
    .in0(Test_Reg[7]), .in1(Test_Reg[15]), .out(Flags_Out[1]), .sel(_16_bit));
  not not_1 (Flags_Out[2], Test_Reg[0]);

  assign Flags_Out[7:3] = {Flags_In[7:5], Overflow, Carry};
endmodule

module Condition_Check (
  input  [3:0] Condition,
  input  [7:0] Flags,
  output Truth
);

  wire controlled_buffer_1_out, decoder_1_out0, decoder_1_out1, decoder_1_out2, decoder_1_out3,
       decoder_1_out4, decoder_1_out5, decoder_1_out6, decoder_1_out7, nor_1_out, not_1_out;

  Decoder #(.select(3)) decoder_1 (
    .out0(decoder_1_out0), .out1(decoder_1_out1), .out2(decoder_1_out2), .out3(decoder_1_out3),
    .out4(decoder_1_out4), .out5(decoder_1_out5), .out6(decoder_1_out6), .out7(decoder_1_out7),
    .sel(Condition[3:1]));  // open: en
  not not_1 (not_1_out, Flags[1]);
  nor nor_1 (nor_1_out, not_1_out, Flags[0]);
  assign controlled_buffer_1_out = decoder_1_out0 ? Flags[0] : 1'bz;  // Controlled_Buffer controlled_buffer_1
  assign controlled_buffer_1_out = decoder_1_out1 ? Flags[1] : 1'bz;  // Controlled_Buffer controlled_buffer_2
  assign controlled_buffer_1_out = decoder_1_out2 ? Flags[2] : 1'bz;  // Controlled_Buffer controlled_buffer_3
  assign controlled_buffer_1_out = decoder_1_out3 ? Flags[3] : 1'bz;  // Controlled_Buffer controlled_buffer_4
  assign controlled_buffer_1_out = decoder_1_out4 ? Flags[4] : 1'bz;  // Controlled_Buffer controlled_buffer_5
  assign controlled_buffer_1_out = decoder_1_out5 ? nor_1_out : 1'bz;  // Controlled_Buffer controlled_buffer_6
  assign controlled_buffer_1_out = decoder_1_out6 ? 1'b1 : 1'bz;  // Controlled_Buffer controlled_buffer_7
  assign controlled_buffer_1_out = decoder_1_out7 ? 1'b1 : 1'bz;  // Controlled_Buffer controlled_buffer_8
  xor xor_1 (Truth, Condition[0], controlled_buffer_1_out);
endmodule

module RAM_Register (
  input  [7:0] RAM_Input,
  input  Clock,
  input  Reverse,
  input  _16_bit,
  input  Load,
  output [15:0] RAM_Buffer,
  output Loading
);

  wire and_1_out, and_2_out, and_3_out, d_ff_1_qn, d_ff_2_q, d_ff_3_q, d_ff_3_qn, d_ff_4_q, d_ff_5_q,
       decoder_1_out0, decoder_1_out1, multiplexer_1_out, not_1_out, not_2_out, not_3_out, not_4_out,
       not_5_out, not_6_out, not_7_out, not_8_out, or_1_out, or_2_out, t_ff_1_q, xnor_1_out;

  and and_1 (and_1_out, not_2_out, or_2_out);
  T_Flip_Flop t_ff_1 (.clk(and_1_out), .T(1'b1), .Q(t_ff_1_q), .reset(not_1_out));  // open: Qn, preset, en
  not not_1 (not_1_out, or_2_out);
  not not_2 (not_2_out, Clock);
  xnor xnor_1 (xnor_1_out, t_ff_1_q, Reverse);
  Decoder #(.disabled(0)) decoder_1 (.out0(decoder_1_out0), .out1(decoder_1_out1), .sel(and_2_out), .en(and_3_out));
  and and_2 (and_2_out, _16_bit, xnor_1_out);
  and and_3 (and_3_out, Clock, or_2_out);
  Register #(.trigger("high")) register_1 (.D(RAM_Input), .Q(RAM_Buffer[7:0]), .clk(decoder_1_out0));  // open: en, clr
  Register #(.trigger("high")) Hig (
    .D(RAM_Input), .Q(RAM_Buffer[15:8]), .clk(decoder_1_out1), .clr(not_3_out));  // open: en
  not not_3 (not_3_out, _16_bit);
  D_Flip_Flop #(.trigger("high")) d_ff_1 (
    .clk(not_4_out), .D(d_ff_2_q), .Qn(d_ff_1_qn), .reset(not_6_out));  // open: Q, preset, en
  not not_4 (not_4_out, Clock);
  D_Flip_Flop #(.trigger("high")) d_ff_2 (
    .clk(Clock), .D(d_ff_3_q), .Q(d_ff_2_q), .reset(not_6_out));  // open: Qn, preset, en
  not not_5 (not_5_out, Clock);
  D_Flip_Flop #(.trigger("high")) d_ff_3 (
    .clk(not_5_out), .D(d_ff_4_q), .Q(d_ff_3_q), .Qn(d_ff_3_qn), .reset(not_6_out));  // open: preset, en
  D_Flip_Flop #(.trigger("high")) d_ff_4 (
    .clk(Clock), .D(or_2_out), .Q(d_ff_4_q), .reset(not_6_out));  // open: Qn, preset, en
  not not_6 (not_6_out, or_2_out);
  Multiplexer #(.enable("false")) multiplexer_1 (
    .in0(d_ff_1_qn), .in1(d_ff_3_qn), .out(multiplexer_1_out), .sel(not_7_out));
  not not_7 (not_7_out, _16_bit);
  and and_4 (Loading, multiplexer_1_out, or_2_out);
  or or_1 (or_1_out, not_8_out, Load);
  not not_8 (not_8_out, Clock);
  or or_2 (or_2_out, d_ff_5_q, Load);
  D_Flip_Flop #(.trigger("high")) d_ff_5 (.clk(or_1_out), .D(Loading), .Q(d_ff_5_q));  // open: Qn, preset, en, reset
endmodule

module Y_Register (
  input  Clock,
  input  Update,
  input  Selector,
  input  [15:0] _0,
  input  [15:0] _1,
  output [15:0] Y_in,
  output [15:0] Y_out
);

  wire not_1_out, or_1_out;
  wire [15:0] Y_in_q;

  Multiplexer #(.width(16), .disabled(0), .enable("false")) multiplexer_1 (
    .in0(_0), .in1(_1), .out(Y_in), .sel(Selector));
  Register #(.width(16), .trigger("high")) u_Y_in (.D(Y_in), .Q(Y_in_q), .clk(or_1_out));  // open: en, clr
  or or_1 (or_1_out, Clock, Update);
  Register #(.width(16), .trigger("high")) u_Y_out (.D(Y_in_q), .Q(Y_out), .clk(not_1_out));  // open: en, clr
  not not_1 (not_1_out, Clock);
endmodule
