// Logisim project computer.circ as structural Verilog: 16 circuits, main circuit PC
module PC (
);

  wire clock_1_out, cpu_1_out_of_bounds_exception, cpu_1_read_ram, cpu_1_request_input, cpu_1_write_ram,
       gpu_1_clear, gpu_1_clock_2, gpu_1_done, gpu_1_in_use, gpu_1_load, gpu_1_load_2, gpu_1_load_3,
       gpu_1_load_4, gpu_1_load_5, gpu_1_load_6, gpu_1_load_7, gpu_1_load_8, gpu_1_on,
       input_decoder_1_gate_0, input_decoder_1_gate_1, input_decoder_1_gate_2, input_decoder_1_gate_3,
       input_decoder_1_gate_4, input_decoder_1_gate_5, input_decoder_1_gate_6, input_decoder_1_gate_7,
       input_decoder_1_gate_8, input_decoder_1_gate_9, input_decoder_1_gate_10, input_decoder_1_gate_11,
       input_decoder_1_gate_12, input_decoder_1_gate_13, input_decoder_1_gate_14, input_decoder_1_gate_15,
       keyboard_1_avail, mch_1_done, mch_1_write, mch_1_write_2, mch_1_write_3, mch_1_write_4, pit_1_done,
       ram_interface_1_in_use, undriven_2, undriven_3, undriven_5, undriven_6, undriven_7, undriven_8,
       undriven_9, undriven_10, undriven_11, undriven_12, undriven_13, undriven_14, undriven_15, undriven_16;
  wire [1:0] ram_interface_1_mode, undriven_4;
  wire [6:0] keyboard_1_data;
  wire [7:0] gpu_1_data_out_2, gpu_1_data_out_3, gpu_1_data_out_4, gpu_1_data_out_5, gpu_1_data_out_6,
       gpu_1_data_out_7, gpu_1_data_out_8, gpu_1_data_out_9, ram_1_output_8;
  wire [15:0] cpu_1_input_gate, cpu_1_output_1, ram_1_output_16;
  wire [16:0] gpu_1_address_2;
  wire [17:0] cpu_1_address, mch_1_address, mch_1_address_3, ram_interface_1_address_3;
  wire [19:0] gpu_1_display_address;
  wire [23:0] mch_1_address_2;
  wire [31:0] cpu_1_data_out, gpu_1_data_out, mch_1_data_out, mch_1_data_out_2, mch_1_data_out_3,
       mch_1_data_out_4, ram_1_output_32, ram_interface_1_data_out, ram_interface_1_data_out_2,
       ram_interface_1_input, undriven;
  wire [31:16] mch_1_status;

  RAM ram_1 (
    .Clock(clock_1_out), .Address(ram_interface_1_address_3), .Mode(ram_interface_1_mode),
    .Input(ram_interface_1_input), .Output_32(ram_1_output_32), .Output_16(ram_1_output_16),
    .Output_8(ram_1_output_8));
  RAM_interface ram_interface_1 (
    .Read_RAM(cpu_1_read_ram), .Write_RAM(cpu_1_write_ram), .Data_Size(undriven_4), .Data_In(cpu_1_data_out),
    .Data_Out(ram_interface_1_data_out), .Address(cpu_1_address), .Address_3(ram_interface_1_address_3),
    .Mode(ram_interface_1_mode), .Input(ram_interface_1_input), .Output_32(ram_1_output_32),
    .Output_16(ram_1_output_16), .Output_8(ram_1_output_8), .Address_2(mch_1_address),
    .Write_RAM_2(mch_1_write), .Data_In_2(mch_1_data_out), .Data_Out_2(ram_interface_1_data_out_2),
    .In_Use(ram_interface_1_in_use));
  MCH mch_1 (
    .Length({mch_1_status, mch_1_status}), .Write_To_Address({mch_1_status, mch_1_status}),
    .Read_From_Address({mch_1_status, mch_1_status}), .Storage_Devices(mch_1_status),
    .Command(cpu_1_output_1), .Address(mch_1_address), .Data_Out(mch_1_data_out),
    .Data_In(ram_interface_1_data_out_2), .In_Use(ram_interface_1_in_use), .Done(mch_1_done),
    .Selected(input_decoder_1_gate_4), .Status(mch_1_status), .Address_2(mch_1_address_2),
    .Write_2(mch_1_write_2), .Data_Out_2(mch_1_data_out_2), .Data_In_2(undriven), .In_Use_2(undriven_2),
    .Write_3(mch_1_write_3), .Data_Out_3(mch_1_data_out_3), .In_Use_3(undriven_3), .Write(mch_1_write),
    .Data_In_3(gpu_1_data_out), .Data_Out_4(mch_1_data_out_4), .Address_3(mch_1_address_3),
    .In_Use_4(gpu_1_in_use), .Write_4(mch_1_write_4), .Clock(clock_1_out));
  CPU cpu_1 (
    .Read_RAM(cpu_1_read_ram), .Write_RAM(cpu_1_write_ram), .Data_Size(undriven_4),
    .Data_Out(cpu_1_data_out), .Data_In(ram_interface_1_data_out), .Address(cpu_1_address),
    .Segment_Base(cpu_1_output_1), .Segment_Limit(mch_1_status), .Write_Segment(input_decoder_1_gate_15),
    .Segment_ID(mch_1_status[20:16]), .Input_Gate(cpu_1_input_gate), .Request_Input(cpu_1_request_input),
    .Interrupt_Request(undriven_5), .Out_Of_Bounds_Exception(cpu_1_out_of_bounds_exception),
    .Clock(clock_1_out), .Output_1(cpu_1_output_1), .Output_2(mch_1_status), .Output_3(mch_1_status),
    .Output_4(mch_1_status), .Output_5(mch_1_status), .Output_6(mch_1_status), .Output_7(mch_1_status),
    .Output_8(mch_1_status), .Input(mch_1_status));
  Input_Gate_Decoder input_decoder_1 (
    .Input_Gate(cpu_1_input_gate), .Request_Input(cpu_1_request_input), .Gate_15(input_decoder_1_gate_15),
    .Gate_14(input_decoder_1_gate_14), .Gate_13(input_decoder_1_gate_13), .Gate_12(input_decoder_1_gate_12),
    .Gate_11(input_decoder_1_gate_11), .Gate_10(input_decoder_1_gate_10), .Gate_9(input_decoder_1_gate_9),
    .Gate_8(input_decoder_1_gate_8), .Gate_7(input_decoder_1_gate_7), .Gate_6(input_decoder_1_gate_6),
    .Gate_5(input_decoder_1_gate_5), .Gate_4(input_decoder_1_gate_4), .Gate_3(input_decoder_1_gate_3),
    .Gate_2(input_decoder_1_gate_2), .Gate_1(input_decoder_1_gate_1), .Gate_0(input_decoder_1_gate_0));
  GPU gpu_1 (
    .Clock_2(gpu_1_clock_2), .On(gpu_1_on), .Clear(gpu_1_clear), .Address_2(gpu_1_address_2),
    .Display_Address(gpu_1_display_address), .In_Use(gpu_1_in_use), .Data_Out(gpu_1_data_out),
    .Data_In(mch_1_data_out_4), .Write(mch_1_write_4), .Address(mch_1_address_3), .Clock(clock_1_out),
    .Input_1(cpu_1_output_1), .Input_2(mch_1_status), .Input_3(mch_1_status), .Input_4(mch_1_status),
    .Input_5(mch_1_status), .Input_6(mch_1_status), .Input_7(mch_1_status), .Input_8(mch_1_status),
    .Output(mch_1_status), .Select_2(input_decoder_1_gate_6), .Select_1(input_decoder_1_gate_5),
    .Done(gpu_1_done), .Load(gpu_1_load), .Data_Out_2(gpu_1_data_out_2), .Data_In_2(gpu_1_data_out_2),
    .Load_2(gpu_1_load_2), .Data_Out_3(gpu_1_data_out_3), .Data_In_3(gpu_1_data_out_3),
    .Load_3(gpu_1_load_3), .Data_Out_4(gpu_1_data_out_4), .Data_In_4(gpu_1_data_out_4),
    .Load_4(gpu_1_load_4), .Data_Out_5(gpu_1_data_out_5), .Data_In_5(gpu_1_data_out_5),
    .Load_5(gpu_1_load_5), .Data_Out_6(gpu_1_data_out_6), .Data_In_6(gpu_1_data_out_6),
    .Load_6(gpu_1_load_6), .Data_Out_7(gpu_1_data_out_7), .Data_In_7(gpu_1_data_out_7),
    .Load_7(gpu_1_load_7), .Data_Out_8(gpu_1_data_out_8), .Data_In_8(gpu_1_data_out_8),
    .Load_8(gpu_1_load_8), .Data_Out_9(gpu_1_data_out_9), .Data_In_9(gpu_1_data_out_9));
  // VRam_with_screen vram_with_screen_1: pin names not known; wires that end beside it: gpu_1_clock_2, gpu_1_on, gpu_1_clear, gpu_1_address_2, gpu_1_display_address, gpu_1_load, gpu_1_data_out_2, gpu_1_load_2, gpu_1_data_out_3, gpu_1_load_3, gpu_1_data_out_4, gpu_1_load_4, gpu_1_data_out_5, gpu_1_load_5, gpu_1_data_out_6, gpu_1_load_6, gpu_1_data_out_7, gpu_1_load_7, gpu_1_data_out_8, gpu_1_load_8, gpu_1_data_out_9
  Clock clock_1 (.out(clock_1_out));
  PIC pic_1 (
    .Interrupt_Request(input_decoder_1_gate_0), .Selected(cpu_1_out_of_bounds_exception),
    .Output(mch_1_status), .Command_Input(cpu_1_output_1), .Data_Input(mch_1_status),
    .Interrupt_Request_15(undriven_5), .Interrupt_Request_14(undriven_6), .Interrupt_Request_13(undriven_7),
    .Interrupt_Request_12(undriven_8), .Interrupt_Request_11(undriven_9), .Interrupt_Request_10(undriven_10),
    .Interrupt_Request_9(undriven_11), .Interrupt_Request_8(undriven_12), .Interrupt_Request_7(undriven_13),
    .Interrupt_Request_6(undriven_14), .Interrupt_Request_5(undriven_15), .Interrupt_Request_4(undriven_16),
    .Interrupt_Request_3(gpu_1_done), .Interrupt_Request_2(mch_1_done),
    .Interrupt_Request_1(keyboard_1_avail), .Interrupt_Request_0(pit_1_done), .Clock(clock_1_out));
  Keyboard keyboard_1 (
    .clk(clock_1_out), .re(input_decoder_1_gate_1), .avail(keyboard_1_avail), .data(keyboard_1_data));  // open: clr
  assign mch_1_status = input_decoder_1_gate_1 ? {{9{1'b0}}, keyboard_1_data} : 16'bz;  // Controlled_Buffer controlled_buffer_1
  PIT pit_1 (
    .Done(pit_1_done), .Selected(input_decoder_1_gate_2), .Data_Out(mch_1_status), .Data_In(cpu_1_output_1),
    .Control(mch_1_status), .Clock(clock_1_out));

  // Notes on the sheet:
  //   Keyboard
  //   Annoying Buzzer
endmodule

module CPU (
  input  Clock,
  input  [1:0] Data_Size,
  input  [31:0] Data_In,
  input  [15:0] Segment_Base,
  input  [15:0] Segment_Limit,
  input  Write_Segment,
  input  Interrupt_Request,
  input  [4:0] Segment_ID,
  input  [15:0] Input,
  output Read_RAM,
  output Write_RAM,
  output [15:0] Input_Gate,
  output [31:0] Data_Out,
  output [17:0] Address,
  output Request_Input,
  output Out_Of_Bounds_Exception,
  output [15:0] Output_1,
  output [15:0] Output_2,
  output [15:0] Output_3,
  output [15:0] Output_4,
  output [15:0] Output_5,
  output [15:0] Output_6,
  output [15:0] Output_7,
  output [15:0] Output_8
);

  wire alu_1_carry_out, alu_1_overflow_out, alu_1_parity_out, alu_1_set_carry_overflow, alu_1_sign_out,
       alu_1_zero_out, cu_1__16_bit, cu_1__16_bit_2, cu_1_a_from_4, cu_1_a_from_reg, cu_1_b_from_reg,
       cu_1_backup, cu_1_get_a, cu_1_get_b, cu_1_get_instruction, cu_1_get_y, cu_1_internal_reg_input,
       cu_1_internal_reg_output, cu_1_not_a, cu_1_not_b, cu_1_partial_restore, cu_1_restore, cu_1_save_y,
       cu_1_start_interrupt, cu_1_test, cu_1_use_immidiate, cu_1_write, cu_1_write_enable_interrupts,
       cu_1_write_to_output, flag_registery_1_carry_out, flag_registery_1_enable_interrupts_out,
       flag_registery_1_thruth, multiplexer_2_out, registery_1_write_bs, registery_1_write_bs_2,
       registery_1_write_is;
  wire [1:0] cu_1_carry_mode;
  wire [2:0] cu_1_alu_micro_operation, cu_1_output_base_reg;
  wire [3:0] cu_1_condition, cu_1_input_reg, cu_1_output_a_reg, cu_1_output_b_reg;
  wire [4:0] cu_1_read_segment_id;
  wire [5:0] flag_registery_1_bs_output, registery_1_bs_input;
  wire [9:0] cu_1_segment_output, registery_1_segment_input;
  wire [15:0] alu_1_result, mmu_1_a_out, mmu_1_b_out, mmu_1_instruction, multiplexer_3_out,
       multiplexer_4_out, multiplexer_5_out, registery_1_output_a, registery_1_output_b,
       registery_1_output_base;

  Output_Registery output_registery_1 (
    .Write(cu_1_write_to_output), .Clock(Clock), .Data(Input_Gate), .Register(cu_1_output_a_reg[2:0]),
    .O1(Output_1), .O2(Output_2), .O3(Output_3), .O4(Output_4), .O5(Output_5), .O6(Output_6), .O7(Output_7),
    .O8(Output_8));
  MMU mmu_1 (
    .Data_Out(Data_Out), .Data_In(Data_In), .Address_Out(Address), .Segment_Base(Segment_Base),
    .Segment_Limit(Segment_Limit), .Write_Segment(Write_Segment), .Write_Segment_ID(Segment_ID),
    .Y_in(multiplexer_5_out), .B_out(mmu_1_b_out), .A_out(mmu_1_a_out), .Base_In(registery_1_output_base),
    .Clock(Clock), .Read_Segment_ID(cu_1_read_segment_id), .Get_Y(cu_1_get_y),
    .Get_Instruction(cu_1_get_instruction), .Use_Imidiate(cu_1_use_immidiate),
    .Instruction(mmu_1_instruction), .Get_B(cu_1_get_b), .Get_A(cu_1_get_a),
    .Out_Of_Bounds(Out_Of_Bounds_Exception), .Save_Y(cu_1_save_y), .Write_RAM(Write_RAM),
    .Read_RAM(Read_RAM), .Data_Size(Data_Size), ._16_bit(cu_1__16_bit));
  CU cu_1 (
    .Carry_Mode(cu_1_carry_mode), ._16_bit_2(cu_1__16_bit_2), .B_From_Reg(cu_1_b_from_reg),
    .Not_B(cu_1_not_b), .A_From_Reg(cu_1_a_from_reg), .Not_A(cu_1_not_a),
    .ALU_Micro_Operation(cu_1_alu_micro_operation), .Truth(flag_registery_1_thruth),
    .Condition(cu_1_condition), .Enable_Interrupts_Out(flag_registery_1_enable_interrupts_out),
    .Write_Enable_Interrupts(cu_1_write_enable_interrupts), .Test(cu_1_test), .Y_From_Input(Request_Input),
    .Input_Reg(cu_1_input_reg), .Write(cu_1_write), .Restore(cu_1_restore), .Backup(cu_1_backup),
    .Output_A_Reg(cu_1_output_a_reg), .Output_B_Reg(cu_1_output_b_reg),
    .Output_Base_Reg(cu_1_output_base_reg), .Read_Segment_ID(cu_1_read_segment_id), .Get_Y(cu_1_get_y),
    .Get_Instruction(cu_1_get_instruction), .Use_Immidiate(cu_1_use_immidiate),
    .Instruction(mmu_1_instruction), .Get_B(cu_1_get_b), .Get_A(cu_1_get_a), .Clock(Clock),
    .Save_Y(cu_1_save_y), .Interrupt_Request(Interrupt_Request), .Write_To_Output(cu_1_write_to_output),
    .A_From_4(cu_1_a_from_4), .Start_Interrupt(cu_1_start_interrupt), .Segment_Output(cu_1_segment_output),
    .Segment_Input(registery_1_segment_input), .Write_BS(registery_1_write_bs_2),
    .Write_IS(registery_1_write_is), .Internal_Reg_Input(cu_1_internal_reg_input),
    .Internal_Reg_Output(cu_1_internal_reg_output), .Partial_Restore(cu_1_partial_restore),
    ._16_bit(cu_1__16_bit));
  Multiplexer #(.width(16), .enable("false")) multiplexer_1 (
    .in0(mmu_1_a_out), .in1(registery_1_output_b), .out(Input_Gate), .sel(cu_1_b_from_reg));
  ALU alu_1 (
    .Carry_In(multiplexer_2_out), ._16_bit(cu_1__16_bit_2), .B(multiplexer_3_out), .Not_B(cu_1_not_b),
    .A(multiplexer_4_out), .Not_A(cu_1_not_a), .Micro_Operation(cu_1_alu_micro_operation),
    .Carry_Out(alu_1_carry_out), .Overflow_Out(alu_1_overflow_out),
    .Set_Carry_Overflow(alu_1_set_carry_overflow), .Parity_Out(alu_1_parity_out), .Sign_Out(alu_1_sign_out),
    .Zero_Out(alu_1_zero_out), .Result(alu_1_result));
  Multiplexer #(.select(2), .enable("false")) multiplexer_2 (
    .in0(1'b0), .in1(1'b1), .in2(flag_registery_1_carry_out), .in3(alu_1_carry_out), .out(multiplexer_2_out),
    .sel(cu_1_carry_mode));
  Multiplexer #(.width(16), .enable("false")) multiplexer_3 (
    .in0(Input_Gate), .in1(16'h4), .out(multiplexer_3_out), .sel(cu_1_a_from_4));
  Multiplexer #(.width(16), .enable("false")) multiplexer_4 (
    .in0(mmu_1_b_out), .in1(registery_1_output_a), .out(multiplexer_4_out), .sel(cu_1_a_from_reg));
  Flag_Registery flag_registery_1 (
    .Condition(cu_1_condition), .Enable_Interrupts_Out(flag_registery_1_enable_interrupts_out),
    .Enable_Interrupts_In(Input_Gate[0]), .Write_Enable_Interrupts(cu_1_write_enable_interrupts),
    .Carry_In(alu_1_carry_out), .Overflow_In(alu_1_overflow_out),
    .Set_Carry_Overflow(alu_1_set_carry_overflow), .Parity_In(alu_1_parity_out), .Sign_In(alu_1_sign_out),
    .Zero_In(alu_1_zero_out), .Thruth(flag_registery_1_thruth), .Carry_Out(flag_registery_1_carry_out),
    .Clock(Clock), .Restore(cu_1_partial_restore), .Backup(cu_1_backup), .Test(cu_1_test),
    .Write_BS(registery_1_write_bs), .BS_output(flag_registery_1_bs_output), .BS_input(registery_1_bs_input));
  Registery registery_1 (
    .Output_A(registery_1_output_a), .Output_A_Reg(cu_1_output_a_reg), .Output_B(registery_1_output_b),
    .Output_B_Reg(cu_1_output_b_reg), .Output_Base(registery_1_output_base),
    .Output_Base_Reg(cu_1_output_base_reg), .Clock(Clock), .Backup(cu_1_backup), .Restore(cu_1_restore),
    .Input(multiplexer_5_out), .Write(cu_1_write), .Input_Reg(cu_1_input_reg),
    .Write_BS(registery_1_write_bs), .BS_output(flag_registery_1_bs_output), .BS_input(registery_1_bs_input),
    .Start_Interrupt(cu_1_start_interrupt), .Segment_Output(cu_1_segment_output),
    .Segment_Input(registery_1_segment_input), .Write_BS_2(registery_1_write_bs_2),
    .Write_IS(registery_1_write_is), .Internal_Reg_Input(cu_1_internal_reg_input),
    .Internal_Reg_Output(cu_1_internal_reg_output), .Partial_Restore(cu_1_partial_restore));
  Pull_Resistor pull_resistor_1 (.node(Input));
  Multiplexer #(.width(16), .enable("false")) multiplexer_5 (
    .in0(alu_1_result), .in1(Input), .out(multiplexer_5_out), .sel(Request_Input));

  // Notes on the sheet:
  //   Segment_ID: pull=down
  //   Read_RAM: pull=down
  //   Data_Out: pull=down
  //   Write_Segment: pull=down
  //   Out_Of_Bounds_Exception: pull=down
  //   Write_RAM: pull=down
  //   Input_Gate: pull=down
  //   Segment_Base: pull=down
  //   Interrupt_Request: pull=down
  //   Request_Input: pull=down
  //   Data_Size: pull=down
  //   Clock: pull=down
  //   Segment_Limit: pull=down
  //   Address: pull=down
  //   Data_In: pull=down
endmodule

module CU (
  input  [15:0] Instruction,
  input  Truth,
  input  Enable_Interrupts_Out,
  input  Interrupt_Request,
  input  Clock,
  input  [9:0] Segment_Input,
  input  Write_BS,
  input  Write_IS,
  output [4:0] Read_Segment_ID,
  output _16_bit,
  output Save_Y,
  output Get_Y,
  output Get_Instruction,
  output Use_Immidiate,
  output Get_B,
  output Get_A,
  output [1:0] Carry_Mode,
  output _16_bit_2,
  output B_From_Reg,
  output A_From_4,
  output Not_B,
  output A_From_Reg,
  output Not_A,
  output [2:0] ALU_Micro_Operation,
  output [3:0] Condition,
  output Write_Enable_Interrupts,
  output Test,
  output Y_From_Input,
  output Partial_Restore,
  output Restore,
  output Backup,
  output [3:0] Output_A_Reg,
  output [3:0] Output_B_Reg,
  output Internal_Reg_Output,
  output [2:0] Output_Base_Reg,
  output Start_Interrupt,
  output [9:0] Segment_Output,
  output Internal_Reg_Input,
  output [3:0] Input_Reg,
  output Write,
  output Write_To_Output
);

  wire and_1_out, and_2_out, and_3_out, and_4_out, and_5_out, and_6_out, and_7_out, and_9_out, and_10_out,
       and_13_out, decoder_1_out8, decoder_1_out10, decoder_1_out11, decoder_1_out13, Int_Req_Buf_q,
       nand_1_out, nand_2_out, nand_3_out, nand_4_out, nand_5_out, nand_6_out, nand_7_out, nand_8_out,
       nand_9_out, nand_10_out, nand_11_out, nor_1_out, nor_2_out, or_1_out, or_2_out, or_3_out, or_4_out,
       or_5_out, s_r_ff_1_qn;
  wire [1:0] multiplexer_8_out;
  wire [1:1] and_12_out;
  wire [2:0] multiplexer_5_out, nand_12_out;
  wire [4:0] S_q, S_q_2;
  wire [9:0] BS_q, IS_q, multiplexer_2_out, multiplexer_4_out;

  Register #(.width(10), .trigger("falling")) IS (
    .D(Segment_Input), .en(Write_IS), .Q(IS_q), .clk(Clock));  // open: clr
  Multiplexer #(.width(5), .enable("false")) multiplexer_1 (
    .in0(S_q_2), .in1(S_q), .out(Read_Segment_ID), .sel(A_From_4));
  Multiplexer #(.width(10), .enable("false")) multiplexer_2 (
    .in0(IS_q), .in1(BS_q), .out(multiplexer_2_out), .sel(Partial_Restore));
  or or_1 (or_1_out, Partial_Restore, Start_Interrupt);
  Multiplexer #(.width(10), .enable("false")) multiplexer_3 (
    .in0(IS_q), .in1(BS_q), .out(Segment_Output), .sel(Instruction[12]));
  Register #(.width(10), .trigger("falling")) S (
    .D(multiplexer_2_out), .en(or_1_out), .Q({S_q_2, S_q}), .clk(Clock));  // open: clr
  Multiplexer #(.width(10), .enable("false")) multiplexer_4 (
    .in0({S_q_2, S_q}), .in1(Segment_Input), .out(multiplexer_4_out), .sel(Write_BS));
  Register #(.width(10), .trigger("falling")) BS (
    .D(multiplexer_4_out), .en(or_2_out), .Q(BS_q), .clk(Clock));  // open: clr
  or or_2 (or_2_out, Write_BS, Backup);
  Stage_Counter stage_counter_1 (
    .Clock(Clock), .Start_Interrupt(Start_Interrupt), .Use_Start_Interrupt(and_3_out), .Save_A(Save_Y),
    .Use_Save_A(and_1_out), .Execute(Get_Y), .Use_Execute(nor_1_out), .Fetch_B(Get_B),
    .Use_Fetch_B(and_6_out), .Fetch_A(Get_A), .Use_Fetch_A(and_2_out), .Fetch_Instruction(A_From_4));  // open: Update_State
  and and_1 (and_1_out, nand_1_out, and_7_out);
  and and_2 (and_2_out, and_4_out, and_7_out);
  and and_3 (and_3_out, Enable_Interrupts_Out, Int_Req_Buf_q, s_r_ff_1_qn);
  S_R_Flip_Flop s_r_ff_1 (
    .S(Start_Interrupt), .clk(Clock), .R(or_3_out), .Qn(s_r_ff_1_qn));  // open: Q, preset, reset, en
  or or_3 (or_3_out, Restore, decoder_1_out10);
  nand nand_1 (nand_1_out, ~Instruction[5], Instruction[4], Instruction[3]);  // NAND_Gate
  or or_4 (or_4_out, Instruction[5], Instruction[4]);
  nand nand_2 (nand_2_out, Instruction[5], Instruction[4], Instruction[3]);
  and and_4 (and_4_out, or_4_out, nand_2_out, and_10_out);
  nand nand_3 (nand_3_out, Instruction[11], Instruction[12], Instruction[13], Instruction[14]);
  and and_5 (and_5_out, nand_3_out, Instruction[15]);
  nor nor_1 (nor_1_out, nor_2_out, decoder_1_out13);
  and and_6 (and_6_out, nor_1_out, and_5_out);
  and and_7 (and_7_out, nor_1_out, Instruction[10]);
  and and_8 (Use_Immidiate, Get_B, Instruction[14]);
  nor nor_2 (nor_2_out, Instruction[5], Instruction[4], Truth);
  D_Flip_Flop Int_Req_Buf (.clk(Clock), .D(Interrupt_Request), .Q(Int_Req_Buf_q));  // open: Qn, preset, en, reset
  nand nand_4 (nand_4_out, Instruction[4], ~Instruction[3]);  // NAND_Gate
  nand nand_5 (nand_5_out, Instruction[4], Instruction[3], Instruction[2], Instruction[1], ~Instruction[0]);  // NAND_Gate
  nand nand_6 (nand_6_out, Instruction[5], Instruction[3]);
  nand nand_7 (nand_7_out, Instruction[5], Instruction[4]);
  nand nand_8 (nand_8_out, ~Instruction[5], Instruction[4], Instruction[3], Instruction[2], Instruction[1]);  // NAND_Gate
  nand nand_9 (nand_9_out, Instruction[5], ~Instruction[4]);  // NAND_Gate
  nand nand_10 (nand_10_out, Instruction[5], ~Instruction[3]);  // NAND_Gate
  and and_9 (and_9_out, Instruction[1], Instruction[2], Instruction[3], Instruction[4]);
  and and_10 (and_10_out, Instruction[4], ~Instruction[5], Get_Y);  // AND_Gate
  Decoder #(.select(4), .disabled(0)) decoder_1 (
    .out2(Write_Enable_Interrupts), .out4(Internal_Reg_Input), .out5(Internal_Reg_Output),
    .out6(Write_To_Output), .out7(Y_From_Input), .out8(decoder_1_out8), .out9(Restore),
    .out10(decoder_1_out10), .out11(decoder_1_out11), .out13(decoder_1_out13), .sel(Instruction[3:0]),
    .en(and_10_out));  // open: out0, out1, out3, out12, out14, out15
  Multiplexer #(.width(3), .enable("false")) multiplexer_5 (
    .in0(Instruction[8:6]), .in1(Instruction[13:11]), .out(multiplexer_5_out), .sel(Get_B));
  Multiplexer #(.width(4), .enable("false")) multiplexer_6 (
    .in0(Instruction[9:6]), .in1(4'b1110), .out(Input_Reg), .sel(A_From_4));
  not not_1 (B_From_Reg, Instruction[15]);
  nand nand_11 (nand_11_out, Instruction[3], Instruction[4]);
  nand nand_12 (nand_12_out[0], Instruction[5], ~Instruction[2], nand_4_out);  // NAND_Gate
  nand nand_13 (nand_12_out[1], nand_5_out, nand_6_out, nand_7_out);
  nand nand_14 (nand_12_out[2], nand_8_out, nand_9_out, nand_10_out);
  or or_5 (or_5_out, and_9_out, Instruction[5]);
  and and_11 (Test, or_5_out, Get_Y);
  Multiplexer #(.width(3), .enable("false")) multiplexer_7 (
    .in0(multiplexer_5_out), .in1(3'b101), .out(Output_Base_Reg), .sel(A_From_4));
  Multiplexer #(.width(2), .enable("false")) multiplexer_8 (
    .in0(Instruction[3:2]), .in1(Instruction[1:0]), .out(multiplexer_8_out), .sel(nand_11_out));
  and and_12 (and_12_out[1], Instruction[5], Get_Y);
  and and_13 (and_13_out, nand_11_out, Get_Y, Instruction[5]);
  assign Carry_Mode = multiplexer_8_out & {2{and_12_out[1]}};  // AND_Gate and_14, 2 bits wide
  or or_6 (_16_bit_2, Instruction[9], A_From_4);
  and and_15 (Not_B, Instruction[1], and_13_out);
  or or_7 (A_From_Reg, A_From_4, ~Instruction[10]);  // OR_Gate
  and and_16 (Not_A, Instruction[0], and_13_out);
  assign ALU_Micro_Operation = {3{A_From_4}} | nand_12_out;  // OR_Gate or_8, 3 bits wide
  or or_9 (Partial_Restore, decoder_1_out11, decoder_1_out10, Restore);
  or or_10 (Backup, decoder_1_out8, Start_Interrupt);
  or or_11 (Write, A_From_4, Get_Y);

  assign _16_bit = Instruction[9];
  assign Condition = Instruction[3:0];
  assign Get_Instruction = A_From_4;
  assign Output_A_Reg = Input_Reg;
  assign Output_B_Reg = Instruction[14:11];
endmodule

module Stage_Counter (
  input  Use_Start_Interrupt,
  input  Use_Save_A,
  input  Use_Execute,
  input  Use_Fetch_B,
  input  Use_Fetch_A,
  input  Clock,
  input  Update_State,
  output Start_Interrupt,
  output Save_A,
  output Execute,
  output Fetch_B,
  output Fetch_A,
  output Fetch_Instruction
);

  wire and_1_out, demultiplexer_1_out0, demultiplexer_1_out1, demultiplexer_2_out0, demultiplexer_2_out1,
       demultiplexer_3_out0, demultiplexer_3_out1, demultiplexer_4_out0, demultiplexer_4_out1, nor_1_out,
       or_1_out, or_2_out, or_3_out, or_4_out;

  nor nor_1 (nor_1_out, and_1_out, demultiplexer_1_out1, demultiplexer_2_out1, demultiplexer_3_out1, demultiplexer_4_out1);
  and and_1 (and_1_out, or_1_out, Use_Start_Interrupt);
  or or_1 (or_1_out, demultiplexer_1_out0, Save_A);
  Demultiplexer #(.enable("false")) demultiplexer_1 (
    .out0(demultiplexer_1_out0), .out1(demultiplexer_1_out1), .in(or_2_out), .sel(Use_Save_A));
  or or_2 (or_2_out, demultiplexer_2_out0, Execute);
  Demultiplexer #(.enable("false")) demultiplexer_2 (
    .out0(demultiplexer_2_out0), .out1(demultiplexer_2_out1), .in(or_3_out), .sel(Use_Execute));
  or or_3 (or_3_out, demultiplexer_3_out0, Fetch_B);
  Demultiplexer #(.enable("false")) demultiplexer_3 (
    .out0(demultiplexer_3_out0), .out1(demultiplexer_3_out1), .in(or_4_out), .sel(Use_Fetch_B));
  or or_4 (or_4_out, demultiplexer_4_out0, Fetch_A);
  Demultiplexer #(.enable("false")) demultiplexer_4 (
    .out0(demultiplexer_4_out0), .out1(demultiplexer_4_out1), .in(Fetch_Instruction), .sel(Use_Fetch_A));
  D_Flip_Flop #(.trigger("falling")) d_ff_1 (
    .clk(Clock), .D(and_1_out), .Q(Start_Interrupt), .en(Update_State));  // open: Qn, preset, reset
  D_Flip_Flop #(.trigger("falling")) d_ff_2 (
    .clk(Clock), .D(demultiplexer_1_out1), .Q(Save_A), .en(Update_State));  // open: Qn, preset, reset
  D_Flip_Flop #(.trigger("falling")) d_ff_3 (
    .clk(Clock), .D(demultiplexer_2_out1), .Q(Execute), .en(Update_State));  // open: Qn, preset, reset
  D_Flip_Flop #(.trigger("falling")) d_ff_4 (
    .clk(Clock), .D(demultiplexer_3_out1), .Q(Fetch_B), .en(Update_State));  // open: Qn, preset, reset
  D_Flip_Flop #(.trigger("falling")) d_ff_5 (
    .clk(Clock), .D(demultiplexer_4_out1), .Q(Fetch_A), .en(Update_State));  // open: Qn, preset, reset
  D_Flip_Flop #(.trigger("falling")) d_ff_6 (
    .clk(Clock), .D(nor_1_out), .Q(Fetch_Instruction), .en(Update_State));  // open: Qn, preset, reset

  // Notes on the sheet:
  //   Start Interrupt
  //   Save A
  //   Execute
  //   Fetch B
  //   Fetch A
  //   Fetch Instruction
endmodule

module ALU (
  input  Carry_In,
  input  _16_bit,
  input  [15:0] B,
  input  Not_B,
  input  [15:0] A,
  input  Not_A,
  input  [2:0] Micro_Operation,
  output [15:0] Result,
  output Carry_Out,
  output Overflow_Out,
  output Set_Carry_Overflow,
  output Parity_Out,
  output Sign_Out,
  output Zero_Out
);

  wire adder_1_cout, adder_2_cout, adder_3_cout, adder_4_cout, decoder_1_out0, decoder_1_out1,
       decoder_1_out2, decoder_1_out3, decoder_1_out4, decoder_1_out5, decoder_1_out6, decoder_1_out7,
       multiplexer_2_out, multiplexer_3_out, multiplexer_4_out, multiplexer_6_out, multiplexer_7_out,
       nand_1_out, not_1_out, not_2_out, xor_1_out, xor_2_out, xor_4_out, xor_5_out, xor_6_out;
  wire [6:0] adder_1_out, adder_3_out, xnor_1_out, xnor_1_out_2, xnor_2_out, xnor_2_out_3;
  wire [7:7] multiplexer_5_out;
  wire [15:0] and_1_out, bit_extender_1_out, bit_extender_2_out, or_2_out, xor_3_out;
  wire [15:7] adder_2_out, xnor_1_out_3, xnor_2_out_2;

  not not_1 (not_1_out, Not_B);
  not not_2 (not_2_out, Not_A);
  Decoder #(.select(3), .enable("false")) decoder_1 (
    .out0(decoder_1_out0), .out1(decoder_1_out1), .out2(decoder_1_out2), .out3(decoder_1_out3),
    .out4(decoder_1_out4), .out5(decoder_1_out5), .out6(decoder_1_out6), .out7(decoder_1_out7),
    .sel(Micro_Operation));
  or or_1 (Set_Carry_Overflow, decoder_1_out2, decoder_1_out3, decoder_1_out7);
  not not_3 (Parity_Out, Result[0]);
  nand nand_1 (nand_1_out, not_2_out, not_1_out);
  assign bit_extender_1_out = {{15{not_1_out}}, not_1_out};  // Bit_Extender bit_extender_1
  assign bit_extender_2_out = {{15{not_2_out}}, not_2_out};  // Bit_Extender bit_extender_2
  Multiplexer #(.enable("false")) multiplexer_1 (.in0(Result[7]), .in1(Result[15]), .out(Sign_Out), .sel(_16_bit));
  assign {xnor_1_out_3[15], xnor_1_out_2, xnor_1_out_3[7], xnor_1_out} = ~(B ^ bit_extender_1_out);  // XNOR_Gate xnor_1, 16 bits wide
  assign {xnor_2_out_2[15], xnor_2_out_3, xnor_2_out_2[7], xnor_2_out} = ~(A ^ bit_extender_2_out);  // XNOR_Gate xnor_2, 16 bits wide
  Pull_Resistor pull_resistor_1 (.node(Carry_Out));
  Pull_Resistor pull_resistor_2 (.node(Overflow_Out));
  assign Result = decoder_1_out0 ? {xnor_1_out_3[15], xnor_1_out_2, xnor_1_out_3[7], xnor_1_out} : 16'bz;  // Controlled_Buffer controlled_buffer_1
  assign Result = decoder_1_out1 ? {xnor_2_out_2[15], xnor_2_out_3, xnor_2_out_2[7], xnor_2_out} : 16'bz;  // Controlled_Buffer controlled_buffer_2
  nor nor_1 (Zero_Out, Result[15], Result[14], Result[13], Result[12], Result[11], Result[10], Result[9], Result[8], Result[7], Result[6], Result[5], Result[4], Result[3], Result[2], Result[1], Result[0]);
  Multiplexer #(.enable("false")) multiplexer_2 (
    .in0(xnor_1_out[6]), .in1(xnor_1_out_2[6]), .out(multiplexer_2_out), .sel(_16_bit));
  Multiplexer #(.enable("false")) multiplexer_3 (
    .in0(xnor_1_out_3[7]), .in1(xnor_1_out_3[15]), .out(multiplexer_3_out), .sel(_16_bit));
  xor xor_1 (xor_1_out, multiplexer_3_out, multiplexer_2_out);
  assign Overflow_Out = decoder_1_out2 ? xor_1_out : 1'bz;  // Controlled_Buffer controlled_buffer_3
  assign Carry_Out = decoder_1_out2 ? multiplexer_3_out : 1'bz;  // Controlled_Buffer controlled_buffer_4
  assign Result = decoder_1_out2 ? {xnor_1_out_2, xnor_1_out_3[7], xnor_1_out, Carry_In} : 16'bz;  // Controlled_Buffer controlled_buffer_5
  Multiplexer #(.enable("false")) multiplexer_4 (
    .in0(xnor_1_out_3[7]), .in1(xnor_1_out_3[15]), .out(multiplexer_4_out), .sel(_16_bit));
  xor xor_2 (xor_2_out, Carry_In, multiplexer_4_out);
  assign Overflow_Out = decoder_1_out3 ? xor_2_out : 1'bz;  // Controlled_Buffer controlled_buffer_6
  Multiplexer #(.enable("false")) multiplexer_5 (
    .in0(Carry_In), .in1(xnor_1_out_2[0]), .out(multiplexer_5_out[7]), .sel(_16_bit));
  assign Result = decoder_1_out3 ? {Carry_In, xnor_1_out_3[15], xnor_1_out_2[6:1], multiplexer_5_out[7], xnor_1_out_3[7], xnor_1_out[6:1]} : 16'bz;  // Controlled_Buffer controlled_buffer_7
  assign or_2_out = {xnor_2_out_2[15], xnor_2_out_3, xnor_2_out_2[7], xnor_2_out} | {xnor_1_out_3[15], xnor_1_out_2, xnor_1_out_3[7], xnor_1_out};  // OR_Gate or_2, 16 bits wide
  assign Carry_Out = decoder_1_out3 ? xnor_1_out[0] : 1'bz;  // Controlled_Buffer controlled_buffer_8
  assign Result = decoder_1_out4 ? or_2_out : 16'bz;  // Controlled_Buffer controlled_buffer_9
  assign and_1_out = {xnor_2_out_2[15], xnor_2_out_3, xnor_2_out_2[7], xnor_2_out} & {xnor_1_out_3[15], xnor_1_out_2, xnor_1_out_3[7], xnor_1_out};  // AND_Gate and_1, 16 bits wide
  assign Result = decoder_1_out5 ? and_1_out : 16'bz;  // Controlled_Buffer controlled_buffer_10
  assign xor_3_out = {xnor_2_out_2[15], xnor_2_out_3, xnor_2_out_2[7], xnor_2_out} ^ {xnor_1_out_3[15], xnor_1_out_2, xnor_1_out_3[7], xnor_1_out};  // XOR_Gate xor_3, 16 bits wide
  assign Result = decoder_1_out6 ? xor_3_out : 16'bz;  // Controlled_Buffer controlled_buffer_11
  xor xor_4 (xor_4_out, nand_1_out, Carry_In);
  Adder #(.width(7)) adder_1 (.a(xnor_1_out), .b(xnor_2_out), .out(adder_1_out), .cin(xor_4_out), .cout(adder_1_cout));
  Adder #(.width(1)) adder_2 (
    .a(xnor_1_out_3[7]), .b(xnor_2_out_2[7]), .out(adder_2_out[7]), .cin(adder_1_cout), .cout(adder_2_cout));
  Adder #(.width(7)) adder_3 (
    .a(xnor_1_out_2), .b(xnor_2_out_3), .out(adder_3_out), .cin(adder_2_cout), .cout(adder_3_cout));
  Adder #(.width(1)) adder_4 (
    .a(xnor_1_out_3[15]), .b(xnor_2_out_2[15]), .out(adder_2_out[15]), .cin(adder_3_cout), .cout(adder_4_cout));
  // Probe on {adder_2_out[15], adder_3_out, adder_2_out[7], adder_1_out}
  // Probe on {adder_2_out[15], adder_3_out, adder_2_out[7], adder_1_out}
  Multiplexer #(.enable("false")) multiplexer_6 (
    .in0(adder_2_cout), .in1(adder_4_cout), .out(multiplexer_6_out), .sel(_16_bit));
  xor xor_5 (xor_5_out, nand_1_out, multiplexer_6_out);
  assign Carry_Out = decoder_1_out7 ? xor_5_out : 1'bz;  // Controlled_Buffer controlled_buffer_12
  assign Result = decoder_1_out7 ? {adder_2_out[15], adder_3_out, adder_2_out[7], adder_1_out} : 16'bz;  // Controlled_Buffer controlled_buffer_13
  Multiplexer #(.enable("false")) multiplexer_7 (
    .in0(adder_1_cout), .in1(adder_3_cout), .out(multiplexer_7_out), .sel(_16_bit));
  xor xor_6 (xor_6_out, multiplexer_6_out, multiplexer_7_out);
  assign Overflow_Out = decoder_1_out7 ? xor_6_out : 1'bz;  // Controlled_Buffer controlled_buffer_14

  // Notes on the sheet:
  //   PASS A
  //   PASS B
  //   RSH
  //   LSH
  //   OR
  //   AND
  //   XOR
  //   ADD
endmodule

module MMU (
  input  [15:0] Y_in,
  input  [31:0] Data_In,
  input  [15:0] Base_In,
  input  Clock,
  input  [15:0] Segment_Base,
  input  [15:0] Segment_Limit,
  input  Write_Segment,
  input  [4:0] Write_Segment_ID,
  input  [4:0] Read_Segment_ID,
  input  _16_bit,
  input  Save_Y,
  input  Get_Y,
  input  Get_Instruction,
  input  Use_Imidiate,
  input  Get_B,
  input  Get_A,
  output Read_RAM,
  output Write_RAM,
  output [1:0] Data_Size,
  output [31:0] Data_Out,
  output [15:0] B_out,
  output [15:0] A_out,
  output [17:0] Address_Out,
  output Out_Of_Bounds,
  output [15:0] Instruction
);

  wire not_1_out, or_1_out, or_2_out, or_3_out;
  wire [4:0] multiplexer_1_out;
  wire [15:0] adder_2_out, Imidiate_q, multiplexer_2_out, multiplexer_3_out, ram_1_data, ram_2_data, Y_q;

  Multiplexer #(.width(5), .enable("false")) multiplexer_1 (
    .in0(Read_Segment_ID), .in1(Write_Segment_ID), .out(multiplexer_1_out), .sel(Write_Segment));
  not not_1 (not_1_out, Write_Segment);
  RAM_part #(.addrWidth(5), .dataWidth(16)) ram_1 (
    .addr(multiplexer_1_out), .data(ram_1_data), .clk(Clock), .ld(not_1_out));  // open: sel, clr
  RAM_part #(.addrWidth(5), .dataWidth(16)) ram_2 (
    .addr(multiplexer_1_out), .data(ram_2_data), .clk(Clock), .ld(not_1_out));  // open: sel, clr
  assign ram_1_data = Write_Segment ? Segment_Base : 16'bz;  // Controlled_Buffer controlled_buffer_1
  assign ram_2_data = Write_Segment ? {Segment_Limit[15:2], 2'b11} : 16'bz;  // Controlled_Buffer controlled_buffer_2
  Adder #(.width(18)) adder_1 (
    .a({ram_1_data, 2'b00}), .b({2'b00, adder_2_out}), .out(Address_Out));  // open: cin, cout
  Comparator #(.width(16), .mode("unsigned")) comparator_1 (
    .a(adder_2_out), .b(ram_2_data), .gt(Out_Of_Bounds));  // open: eq, lt
  nor nor_1 (Read_RAM, ~or_1_out, Use_Imidiate);  // NOR_Gate
  or or_1 (or_1_out, Get_B, Get_A, Get_Instruction);
  Register #(.width(16), .trigger("falling")) Y (.D(Y_in), .en(Get_Y), .Q(Y_q), .clk(Clock));  // open: clr
  assign Data_Out = {{16{1'b0}}, Y_q};  // Bit_Extender bit_extender_1
  Multiplexer #(.width(16), .enable("false")) multiplexer_2 (
    .in0(Data_In[15:0]), .in1(Data_In[31:16]), .out(multiplexer_2_out), .sel(Get_Instruction));
  Register #(.width(16), .trigger("falling")) Imidiate (
    .D(Data_In[31:16]), .en(Get_Instruction), .Q(Imidiate_q), .clk(Clock));  // open: clr
  Register #(.width(16), .trigger("falling")) u_Instruction (
    .D(Data_In[15:0]), .en(Get_Instruction), .Q(Instruction), .clk(Clock));  // open: clr
  Adder #(.width(16)) adder_2 (.a(Imidiate_q), .b(Base_In), .out(adder_2_out));  // open: cin, cout
  Multiplexer #(.width(16), .enable("false")) multiplexer_3 (
    .in0(multiplexer_2_out), .in1(adder_2_out), .out(multiplexer_3_out), .sel(Use_Imidiate));
  or or_2 (or_2_out, Get_B, Get_Instruction);
  or or_3 (or_3_out, Get_Instruction, Get_A);
  Register #(.width(16), .trigger("falling")) B (
    .D(multiplexer_3_out), .en(or_2_out), .Q(B_out), .clk(Clock));  // open: clr
  Register #(.width(16), .trigger("falling")) A (
    .D(multiplexer_3_out), .en(or_3_out), .Q(A_out), .clk(Clock));  // open: clr

  assign Data_Size = {Get_Instruction, _16_bit};
  assign Write_RAM = Save_Y;
endmodule

// Regs
module Registery (
  input  [5:0] BS_output,
  input  [3:0] Output_A_Reg,
  input  [3:0] Output_B_Reg,
  input  Internal_Reg_Output,
  input  [2:0] Output_Base_Reg,
  input  Clock,
  input  Backup,
  input  Start_Interrupt,
  input  Restore,
  input  Partial_Restore,
  input  [9:0] Segment_Output,
  input  [15:0] Input,
  input  Write,
  input  [3:0] Input_Reg,
  input  Internal_Reg_Input,
  output Write_BS,
  output [5:0] BS_input,
  output [15:0] Output_A,
  output [15:0] Output_B,
  output [15:0] Output_Base,
  output [9:0] Segment_Input,
  output Write_BS_2,
  output Write_IS
);

  wire decoder_1_out0, decoder_1_out1, decoder_1_out2, decoder_1_out3, decoder_1_out4, decoder_1_out5,
       decoder_1_out6, decoder_1_out7, decoder_1_out8, decoder_1_out9, decoder_1_out10, decoder_1_out11,
       decoder_1_out12, decoder_1_out13, decoder_1_out14, decoder_1_out15, decoder_1_out24, decoder_1_out26,
       not_1_out, or_1_out, or_2_out, or_3_out, or_4_out, or_5_out, or_6_out, or_7_out, or_8_out, or_9_out,
       or_10_out, or_11_out, or_12_out, or_13_out;
  wire [7:0] AH_q, AL_q, BH_q, BL_q, CH_q, CL_q, DH_q, DL_q, multiplexer_10_out, multiplexer_11_out,
       multiplexer_12_out, multiplexer_13_out, multiplexer_14_out, multiplexer_15_out, multiplexer_16_out,
       multiplexer_17_out, multiplexer_18_out, multiplexer_19_out, multiplexer_20_out, multiplexer_21_out,
       register_4_q, register_5_q, register_6_q, register_7_q, register_8_q, register_9_q, register_10_q,
       register_11_q;
  wire [15:0] BPC_q, EX_q, FX_q, IPC_q, multiplexer_4_out, multiplexer_5_out, multiplexer_6_out,
       multiplexer_7_out, multiplexer_8_out, multiplexer_9_out, PC_q, register_1_q, register_2_q,
       register_3_q, SP_q;

  Multiplexer #(.select(4), .width(16), .enable("false")) multiplexer_1 (
    .in0({{8{1'b0}}, AL_q}), .in1({{8{1'b0}}, AH_q}), .in2({{8{1'b0}}, BL_q}), .in3({{8{1'b0}}, BH_q}),
    .in4({{8{1'b0}}, CL_q}), .in5({{8{1'b0}}, CH_q}), .in6({{8{1'b0}}, DL_q}), .in7({{8{1'b0}}, DH_q}),
    .in8({AH_q, AL_q}), .in9({BH_q, BL_q}), .in10({CH_q, CL_q}), .in11({DH_q, DL_q}), .in12(EX_q),
    .in13(FX_q), .in14(SP_q), .in15(PC_q), .out(Output_A), .sel(Output_A_Reg));
  Multiplexer #(.select(5), .width(16), .enable("false")) multiplexer_2 (
    .in0({{8{1'b0}}, AL_q}), .in1({{8{1'b0}}, AH_q}), .in2({{8{1'b0}}, BL_q}), .in3({{8{1'b0}}, BH_q}),
    .in4({{8{1'b0}}, CL_q}), .in5({{8{1'b0}}, CH_q}), .in6({{8{1'b0}}, DL_q}), .in7({{8{1'b0}}, DH_q}),
    .in8({AH_q, AL_q}), .in9({BH_q, BL_q}), .in10({CH_q, CL_q}), .in11({DH_q, DL_q}), .in12(EX_q),
    .in13(FX_q), .in14(SP_q), .in15(PC_q), .in16({16{1'b0}}), .in17({16{1'b0}}), .in18({16{1'b0}}),
    .in19({16{1'b0}}), .in20({16{1'b0}}), .in21({16{1'b0}}), .in22({16{1'b0}}), .in23({16{1'b0}}),
    .in24(BPC_q), .in25({BS_output, Segment_Output}), .in26(IPC_q), .in27({{6{1'b0}}, Segment_Output}),
    .in28({16{1'b0}}), .in29({16{1'b0}}), .in30({16{1'b0}}), .in31({16{1'b0}}), .out(Output_B),
    .sel({Internal_Reg_Output, Output_B_Reg}));
  Multiplexer #(.select(3), .width(16), .enable("false")) multiplexer_3 (
    .in0({AH_q, AL_q}), .in1({BH_q, BL_q}), .in2({CH_q, CL_q}), .in3({DH_q, DL_q}), .in4(EX_q), .in5(SP_q),
    .in6(PC_q), .in7({16{1'b0}}), .out(Output_Base), .sel(Output_Base_Reg));
  Register #(.width(16), .trigger("falling")) IPC (
    .D(Input), .en(decoder_1_out26), .Q(IPC_q), .clk(Clock));  // open: clr
  not not_1 (not_1_out, Start_Interrupt);
  Multiplexer #(.width(16), .enable("false")) multiplexer_4 (
    .in0(Input), .in1(BPC_q), .out(multiplexer_4_out), .sel(Partial_Restore));
  Multiplexer #(.width(16), .enable("false")) multiplexer_5 (
    .in0(IPC_q), .in1(multiplexer_4_out), .out(multiplexer_5_out), .sel(not_1_out));
  Register #(.width(16), .trigger("falling")) PC (
    .D(multiplexer_5_out), .en(or_1_out), .Q(PC_q), .clk(Clock));  // open: clr
  or or_1 (or_1_out, Start_Interrupt, decoder_1_out15, Partial_Restore);
  Multiplexer #(.width(16), .enable("false")) multiplexer_6 (
    .in0(PC_q), .in1(Input), .out(multiplexer_6_out), .sel(decoder_1_out24));
  or or_2 (or_2_out, decoder_1_out24, Backup);
  Register #(.width(16), .trigger("falling")) BPC (
    .D(multiplexer_6_out), .en(or_2_out), .Q(BPC_q), .clk(Clock));  // open: clr
  Multiplexer #(.width(16), .enable("false")) multiplexer_7 (
    .in0(Input), .in1(register_1_q), .out(multiplexer_7_out), .sel(Restore));
  or or_3 (or_3_out, decoder_1_out14, Restore);
  Register #(.width(16), .trigger("falling")) SP (
    .D(multiplexer_7_out), .en(or_3_out), .Q(SP_q), .clk(Clock));  // open: clr
  Register #(.width(16), .trigger("falling")) register_1 (
    .D(SP_q), .en(Backup), .Q(register_1_q), .clk(Clock));  // open: clr
  Multiplexer #(.width(16), .enable("false")) multiplexer_8 (
    .in0(Input), .in1(register_2_q), .out(multiplexer_8_out), .sel(Restore));
  Register #(.width(16), .trigger("falling")) FX (
    .D(multiplexer_8_out), .en(or_4_out), .Q(FX_q), .clk(Clock));  // open: clr
  or or_4 (or_4_out, decoder_1_out13, Restore);
  Register #(.width(16), .trigger("falling")) register_2 (
    .D(FX_q), .en(Backup), .Q(register_2_q), .clk(Clock));  // open: clr
  Multiplexer #(.width(16), .enable("false")) multiplexer_9 (
    .in0(Input), .in1(register_3_q), .out(multiplexer_9_out), .sel(Restore));
  Register #(.width(16), .trigger("falling")) EX (
    .D(multiplexer_9_out), .en(or_5_out), .Q(EX_q), .clk(Clock));  // open: clr
  or or_5 (or_5_out, decoder_1_out12, Restore);
  Register #(.width(16), .trigger("falling")) register_3 (
    .D(EX_q), .en(Backup), .Q(register_3_q), .clk(Clock));  // open: clr
  or or_6 (or_6_out, decoder_1_out7, decoder_1_out11, Restore);
  Multiplexer #(.width(8), .enable("false")) multiplexer_10 (
    .in0(multiplexer_11_out), .in1(register_4_q), .out(multiplexer_10_out), .sel(Restore));
  Register #(.trigger("falling")) DH (.D(multiplexer_10_out), .en(or_6_out), .Q(DH_q), .clk(Clock));  // open: clr
  Multiplexer #(.width(8), .enable("false")) multiplexer_11 (
    .in0(Input[7:0]), .in1(Input[15:8]), .out(multiplexer_11_out), .sel(decoder_1_out11));
  Register #(.trigger("falling")) register_4 (.D(DH_q), .en(Backup), .Q(register_4_q), .clk(Clock));  // open: clr
  Multiplexer #(.width(8), .enable("false")) multiplexer_12 (
    .in0(Input[7:0]), .in1(register_5_q), .out(multiplexer_12_out), .sel(Restore));
  or or_7 (or_7_out, decoder_1_out6, decoder_1_out11, Restore);
  Register #(.trigger("falling")) register_5 (.D(DL_q), .en(Backup), .Q(register_5_q), .clk(Clock));  // open: clr
  Register #(.trigger("falling")) DL (.D(multiplexer_12_out), .en(or_7_out), .Q(DL_q), .clk(Clock));  // open: clr
  Multiplexer #(.width(8), .enable("false")) multiplexer_13 (
    .in0(multiplexer_14_out), .in1(register_6_q), .out(multiplexer_13_out), .sel(Restore));
  Register #(.trigger("falling")) CH (.D(multiplexer_13_out), .en(or_8_out), .Q(CH_q), .clk(Clock));  // open: clr
  or or_8 (or_8_out, decoder_1_out5, decoder_1_out10, Restore);
  Multiplexer #(.width(8), .enable("false")) multiplexer_14 (
    .in0(Input[7:0]), .in1(Input[15:8]), .out(multiplexer_14_out), .sel(decoder_1_out10));
  Register #(.trigger("falling")) register_6 (.D(CH_q), .en(Backup), .Q(register_6_q), .clk(Clock));  // open: clr
  Multiplexer #(.width(8), .enable("false")) multiplexer_15 (
    .in0(Input[7:0]), .in1(register_7_q), .out(multiplexer_15_out), .sel(Restore));
  or or_9 (or_9_out, decoder_1_out4, decoder_1_out10, Restore);
  Register #(.trigger("falling")) CL (.D(multiplexer_15_out), .en(or_9_out), .Q(CL_q), .clk(Clock));  // open: clr
  Register #(.trigger("falling")) register_7 (.D(CL_q), .en(Backup), .Q(register_7_q), .clk(Clock));  // open: clr
  Multiplexer #(.width(8), .enable("false")) multiplexer_16 (
    .in0(multiplexer_17_out), .in1(register_8_q), .out(multiplexer_16_out), .sel(Restore));
  or or_10 (or_10_out, decoder_1_out3, decoder_1_out9, Restore);
  Register #(.trigger("falling")) BH (.D(multiplexer_16_out), .en(or_10_out), .Q(BH_q), .clk(Clock));  // open: clr
  Multiplexer #(.width(8), .enable("false")) multiplexer_17 (
    .in0(Input[7:0]), .in1(Input[15:8]), .out(multiplexer_17_out), .sel(decoder_1_out9));
  Register #(.trigger("falling")) register_8 (.D(BH_q), .en(Backup), .Q(register_8_q), .clk(Clock));  // open: clr
  Multiplexer #(.width(8), .enable("false")) multiplexer_18 (
    .in0(Input[7:0]), .in1(register_9_q), .out(multiplexer_18_out), .sel(Restore));
  Register #(.trigger("falling")) BL (.D(multiplexer_18_out), .en(or_11_out), .Q(BL_q), .clk(Clock));  // open: clr
  or or_11 (or_11_out, decoder_1_out2, decoder_1_out9, Restore);
  Register #(.trigger("falling")) register_9 (.D(BL_q), .en(Backup), .Q(register_9_q), .clk(Clock));  // open: clr
  Multiplexer #(.width(8), .enable("false")) multiplexer_19 (
    .in0(multiplexer_20_out), .in1(register_10_q), .out(multiplexer_19_out), .sel(Restore));
  Register #(.trigger("falling")) AH (.D(multiplexer_19_out), .en(or_12_out), .Q(AH_q), .clk(Clock));  // open: clr
  or or_12 (or_12_out, decoder_1_out1, decoder_1_out8, Restore);
  Multiplexer #(.width(8), .enable("false")) multiplexer_20 (
    .in0(Input[7:0]), .in1(Input[15:8]), .out(multiplexer_20_out), .sel(decoder_1_out8));
  Register #(.trigger("falling")) register_10 (.D(AH_q), .en(Backup), .Q(register_10_q), .clk(Clock));  // open: clr
  Multiplexer #(.width(8), .enable("false")) multiplexer_21 (
    .in0(Input[7:0]), .in1(register_11_q), .out(multiplexer_21_out), .sel(Restore));
  or or_13 (or_13_out, decoder_1_out0, decoder_1_out8, Restore);
  Register #(.trigger("falling")) AL (.D(multiplexer_21_out), .en(or_13_out), .Q(AL_q), .clk(Clock));  // open: clr
  Decoder #(.select(5), .disabled(0)) decoder_1 (
    .out0(decoder_1_out0), .out1(decoder_1_out1), .out2(decoder_1_out2), .out3(decoder_1_out3),
    .out4(decoder_1_out4), .out5(decoder_1_out5), .out6(decoder_1_out6), .out7(decoder_1_out7),
    .out8(decoder_1_out8), .out9(decoder_1_out9), .out10(decoder_1_out10), .out11(decoder_1_out11),
    .out12(decoder_1_out12), .out13(decoder_1_out13), .out14(decoder_1_out14), .out15(decoder_1_out15),
    .out24(decoder_1_out24), .out25(Write_BS), .out26(decoder_1_out26), .out27(Write_IS),
    .sel({Internal_Reg_Input, Input_Reg}), .en(Write));  // open: out16, out17, out18, out19, out20, out21, out22, out23, out28, out29, out30, out31
  Register #(.trigger("falling")) register_11 (.D(AL_q), .en(Backup), .Q(register_11_q), .clk(Clock));  // open: clr

  assign BS_input = Input[15:10];
  assign Segment_Input = Input[9:0];
  assign Write_BS_2 = Write_BS;
endmodule

// F
module Flag_Registery (
  input  Clock,
  input  [3:0] Condition,
  input  Enable_Interrupts_In,
  input  Write_Enable_Interrupts,
  input  Carry_In,
  input  Overflow_In,
  input  Set_Carry_Overflow,
  input  Parity_In,
  input  Sign_In,
  input  Zero_In,
  input  Write_BS,
  input  [5:0] BS_input,
  input  Restore,
  input  Backup,
  input  Test,
  output Thruth,
  output Carry_Out,
  output Enable_Interrupts_Out,
  output [5:0] BS_output
);

  wire and_1_out, d_ff_3_q, d_ff_4_q, d_ff_5_q, d_ff_6_q, multiplexer_1_out, multiplexer_2_out,
       multiplexer_3_out, multiplexer_4_out, multiplexer_5_out, multiplexer_6_out, multiplexer_7_out,
       multiplexer_8_out, multiplexer_9_out, multiplexer_10_out, multiplexer_11_out, multiplexer_12_out,
       multiplexer_13_out, nor_1_out, or_1_out, or_2_out, or_3_out, or_4_out, or_5_out, or_6_out, or_7_out,
       or_8_out, xor_2_out;

  xor xor_1 (Thruth, Condition[0], multiplexer_1_out);
  Multiplexer #(.select(3), .enable("false")) multiplexer_1 (
    .in0(d_ff_6_q), .in1(d_ff_5_q), .in2(d_ff_4_q), .in3(d_ff_3_q), .in4(Carry_Out), .in5(or_1_out),
    .in6(nor_1_out), .in7(xor_2_out), .out(multiplexer_1_out), .sel(Condition[3:1]));
  or or_1 (or_1_out, d_ff_6_q, Carry_Out);
  nor nor_1 (nor_1_out, d_ff_6_q, ~xor_2_out);  // NOR_Gate
  xor xor_2 (xor_2_out, d_ff_5_q, d_ff_3_q);
  Multiplexer #(.enable("false")) multiplexer_2 (
    .in0(Enable_Interrupts_In), .in1(BS_output[5]), .out(multiplexer_2_out), .sel(Restore));
  or or_2 (or_2_out, Restore, Write_Enable_Interrupts);
  Multiplexer #(.enable("false")) multiplexer_3 (
    .in0(Carry_In), .in1(BS_output[4]), .out(multiplexer_3_out), .sel(Restore));
  or or_3 (or_3_out, Restore, and_1_out);
  Multiplexer #(.enable("false")) multiplexer_4 (
    .in0(Overflow_In), .in1(BS_output[3]), .out(multiplexer_4_out), .sel(Restore));
  or or_4 (or_4_out, Restore, and_1_out);
  Multiplexer #(.enable("false")) multiplexer_5 (
    .in0(Parity_In), .in1(BS_output[2]), .out(multiplexer_5_out), .sel(Restore));
  or or_5 (or_5_out, Restore, Test);
  Multiplexer #(.enable("false")) multiplexer_6 (
    .in0(Sign_In), .in1(BS_output[1]), .out(multiplexer_6_out), .sel(Restore));
  or or_6 (or_6_out, Restore, Test);
  Multiplexer #(.enable("false")) multiplexer_7 (
    .in0(Zero_In), .in1(BS_output[0]), .out(multiplexer_7_out), .sel(Restore));
  or or_7 (or_7_out, Restore, Test);
  D_Flip_Flop #(.trigger("falling")) d_ff_1 (
    .clk(Clock), .D(multiplexer_2_out), .Q(Enable_Interrupts_Out), .en(or_2_out));  // open: Qn, preset, reset
  D_Flip_Flop #(.trigger("falling")) d_ff_2 (
    .clk(Clock), .D(multiplexer_3_out), .Q(Carry_Out), .en(or_3_out));  // open: Qn, preset, reset
  D_Flip_Flop #(.trigger("falling")) d_ff_3 (
    .clk(Clock), .D(multiplexer_4_out), .Q(d_ff_3_q), .en(or_4_out));  // open: Qn, preset, reset
  D_Flip_Flop #(.trigger("falling")) d_ff_4 (
    .clk(Clock), .D(multiplexer_5_out), .Q(d_ff_4_q), .en(or_5_out));  // open: Qn, preset, reset
  D_Flip_Flop #(.trigger("falling")) d_ff_5 (
    .clk(Clock), .D(multiplexer_6_out), .Q(d_ff_5_q), .en(or_6_out));  // open: Qn, preset, reset
  D_Flip_Flop #(.trigger("falling")) d_ff_6 (
    .clk(Clock), .D(multiplexer_7_out), .Q(d_ff_6_q), .en(or_7_out));  // open: Qn, preset, reset
  Multiplexer #(.enable("false")) multiplexer_8 (
    .in0(Enable_Interrupts_Out), .in1(BS_input[5]), .out(multiplexer_8_out), .sel(Write_BS));
  Multiplexer #(.enable("false")) multiplexer_9 (
    .in0(Carry_Out), .in1(BS_input[4]), .out(multiplexer_9_out), .sel(Write_BS));
  Multiplexer #(.enable("false")) multiplexer_10 (
    .in0(d_ff_3_q), .in1(BS_input[3]), .out(multiplexer_10_out), .sel(Write_BS));
  Multiplexer #(.enable("false")) multiplexer_11 (
    .in0(d_ff_4_q), .in1(BS_input[2]), .out(multiplexer_11_out), .sel(Write_BS));
  Multiplexer #(.enable("false")) multiplexer_12 (
    .in0(d_ff_5_q), .in1(BS_input[1]), .out(multiplexer_12_out), .sel(Write_BS));
  Multiplexer #(.enable("false")) multiplexer_13 (
    .in0(d_ff_6_q), .in1(BS_input[0]), .out(multiplexer_13_out), .sel(Write_BS));
  or or_8 (or_8_out, Write_BS, Backup);
  D_Flip_Flop #(.trigger("falling")) d_ff_7 (
    .clk(Clock), .D(multiplexer_8_out), .Q(BS_output[5]), .en(or_8_out));  // open: Qn, preset, reset
  D_Flip_Flop #(.trigger("falling")) d_ff_8 (
    .clk(Clock), .D(multiplexer_9_out), .Q(BS_output[4]), .en(or_8_out));  // open: Qn, preset, reset
  D_Flip_Flop #(.trigger("falling")) d_ff_9 (
    .clk(Clock), .D(multiplexer_10_out), .Q(BS_output[3]), .en(or_8_out));  // open: Qn, preset, reset
  D_Flip_Flop #(.trigger("falling")) d_ff_10 (
    .clk(Clock), .D(multiplexer_11_out), .Q(BS_output[2]), .en(or_8_out));  // open: Qn, preset, reset
  and and_1 (and_1_out, Test, Set_Carry_Overflow);
  D_Flip_Flop #(.trigger("falling")) d_ff_11 (
    .clk(Clock), .D(multiplexer_12_out), .Q(BS_output[1]), .en(or_8_out));  // open: Qn, preset, reset
  D_Flip_Flop #(.trigger("falling")) d_ff_12 (
    .clk(Clock), .D(multiplexer_13_out), .Q(BS_output[0]), .en(or_8_out));  // open: Qn, preset, reset

  // Notes on the sheet:
  //   I
  //   C
  //   O
  //   P
  //   S
  //   Z
endmodule

// Output Regs
module Output_Registery (
  input  Write,
  input  Clock,
  input  [2:0] Register,
  input  [15:0] Data,
  output [15:0] O1,
  output [15:0] O2,
  output [15:0] O3,
  output [15:0] O4,
  output [15:0] O5,
  output [15:0] O6,
  output [15:0] O7,
  output [15:0] O8
);

  wire decoder_1_out0, decoder_1_out1, decoder_1_out2, decoder_1_out3, decoder_1_out4, decoder_1_out5,
       decoder_1_out6, decoder_1_out7;

  Register #(.width(16), .trigger("falling")) u_O1 (.D(Data), .en(decoder_1_out0), .Q(O1), .clk(Clock));  // open: clr
  Register #(.width(16), .trigger("falling")) u_O2 (.D(Data), .en(decoder_1_out1), .Q(O2), .clk(Clock));  // open: clr
  Register #(.width(16), .trigger("falling")) u_O3 (.D(Data), .en(decoder_1_out2), .Q(O3), .clk(Clock));  // open: clr
  Register #(.width(16), .trigger("falling")) u_O4 (.D(Data), .en(decoder_1_out3), .Q(O4), .clk(Clock));  // open: clr
  Register #(.width(16), .trigger("falling")) u_O5 (.D(Data), .en(decoder_1_out4), .Q(O5), .clk(Clock));  // open: clr
  Register #(.width(16), .trigger("falling")) u_O6 (.D(Data), .en(decoder_1_out5), .Q(O6), .clk(Clock));  // open: clr
  Register #(.width(16), .trigger("falling")) u_O7 (.D(Data), .en(decoder_1_out6), .Q(O7), .clk(Clock));  // open: clr
  Decoder #(.select(3), .disabled(0)) decoder_1 (
    .out0(decoder_1_out0), .out1(decoder_1_out1), .out2(decoder_1_out2), .out3(decoder_1_out3),
    .out4(decoder_1_out4), .out5(decoder_1_out5), .out6(decoder_1_out6), .out7(decoder_1_out7),
    .sel(Register), .en(Write));
  Register #(.width(16), .trigger("falling")) u_O8 (.D(Data), .en(decoder_1_out7), .Q(O8), .clk(Clock));  // open: clr
endmodule

module RAM (
  input  Clock,
  input  [31:0] Input,
  input  [17:0] Address,
  input  [1:0] Mode,
  output [31:0] Output_32,
  output [15:0] Output_16,
  output [7:0] Output_8
);

  wire and_1_out, and_2_out, and_3_out, multiplexer_1_out, multiplexer_2_out, multiplexer_3_out,
       multiplexer_4_out, nor_1_out, nor_2_out, nor_3_out, nor_4_out, nor_5_out, nor_6_out, nor_7_out,
       nor_8_out, not_1_out, not_2_out, not_3_out, not_4_out, not_5_out, not_6_out, not_7_out, not_8_out,
       or_1_out, or_2_out, or_3_out, or_4_out;
  wire [7:0] multiplexer_5_out, multiplexer_6_out, multiplexer_7_out, multiplexer_8_out;

  not not_1 (not_1_out, Address[1]);
  nor nor_1 (nor_1_out, Address[0], Address[1]);
  not not_2 (not_2_out, Address[1]);
  nor nor_2 (nor_2_out, ~Address[0], Address[1]);  // NOR_Gate
  nor nor_3 (nor_3_out, Address[0], ~Address[1]);  // NOR_Gate
  and and_1 (and_1_out, Address[0], Address[1]);
  Multiplexer #(.enable("false")) multiplexer_1 (
    .in0(not_1_out), .in1(nor_1_out), .out(multiplexer_1_out), .sel(Mode[0]));
  Multiplexer #(.enable("false")) multiplexer_2 (
    .in0(not_2_out), .in1(nor_2_out), .out(multiplexer_2_out), .sel(Mode[0]));
  Multiplexer #(.enable("false")) multiplexer_3 (
    .in0(Address[1]), .in1(nor_3_out), .out(multiplexer_3_out), .sel(Mode[0]));
  Multiplexer #(.enable("false")) multiplexer_4 (
    .in0(Address[1]), .in1(and_1_out), .out(multiplexer_4_out), .sel(Mode[0]));
  and and_2 (and_2_out, Mode[1], Mode[0]);
  nor nor_4 (nor_4_out, multiplexer_1_out, and_2_out);
  or or_1 (or_1_out, nor_4_out, nor_8_out);
  nor nor_5 (nor_5_out, multiplexer_2_out, and_2_out);
  or or_2 (or_2_out, nor_5_out, nor_8_out);
  nor nor_6 (nor_6_out, multiplexer_3_out, and_2_out);
  or or_3 (or_3_out, nor_6_out, nor_8_out);
  nor nor_7 (nor_7_out, multiplexer_4_out, and_2_out);
  or or_4 (or_4_out, nor_7_out, nor_8_out);
  nor nor_8 (nor_8_out, Mode[1], Mode[0]);
  RAM_part #(.addrWidth(16)) ram_1 (
    .addr(Address[17:2]), .data(Output_32[7:0]), .clk(Clock), .ld(or_1_out));  // open: sel, clr
  not not_3 (not_3_out, or_1_out);
  RAM_part #(.addrWidth(16)) ram_2 (
    .addr(Address[17:2]), .data(Output_32[15:8]), .clk(Clock), .ld(or_2_out));  // open: sel, clr
  not not_4 (not_4_out, or_2_out);
  RAM_part #(.addrWidth(16)) ram_3 (
    .addr(Address[17:2]), .data(Output_32[23:16]), .clk(Clock), .ld(or_3_out));  // open: sel, clr
  not not_5 (not_5_out, or_3_out);
  RAM_part #(.addrWidth(16)) ram_4 (
    .addr(Address[17:2]), .data(Output_32[31:24]), .clk(Clock), .ld(or_4_out));  // open: sel, clr
  not not_6 (not_6_out, or_4_out);
  assign Output_32[7:0] = not_3_out ? Input[7:0] : 8'bz;  // Controlled_Buffer controlled_buffer_1
  assign Output_32[15:8] = not_4_out ? multiplexer_5_out : 8'bz;  // Controlled_Buffer controlled_buffer_2
  Multiplexer #(.width(8), .enable("false")) multiplexer_5 (
    .in0(Input[7:0]), .in1(Input[15:8]), .out(multiplexer_5_out), .sel(Mode[1]));
  assign Output_32[23:16] = not_5_out ? multiplexer_6_out : 8'bz;  // Controlled_Buffer controlled_buffer_3
  Multiplexer #(.width(8), .enable("false")) multiplexer_6 (
    .in0(Input[7:0]), .in1(Input[23:16]), .out(multiplexer_6_out), .sel(and_3_out));
  and and_3 (and_3_out, Mode[1], Mode[0]);
  assign Output_32[31:24] = not_6_out ? multiplexer_7_out : 8'bz;  // Controlled_Buffer controlled_buffer_4
  Multiplexer #(.width(8), .enable("false")) multiplexer_7 (
    .in0(Input[7:0]), .in1(multiplexer_8_out), .out(multiplexer_7_out), .sel(Mode[1]));
  Multiplexer #(.width(8), .enable("false")) multiplexer_8 (
    .in0(Input[15:8]), .in1(Input[31:24]), .out(multiplexer_8_out), .sel(Mode[0]));
  not not_7 (not_7_out, Address[1]);
  Multiplexer #(.width(16), .enable("false")) multiplexer_9 (
    .in0(Output_32[31:16]), .in1(Output_32[15:0]), .out(Output_16), .sel(not_7_out));
  not not_8 (not_8_out, Address[0]);
  Multiplexer #(.width(8), .enable("false")) multiplexer_10 (
    .in0(Output_16[15:8]), .in1(Output_16[7:0]), .out(Output_8), .sel(not_8_out));

  // Notes on the sheet:
  //   Modes: 0 = load, 1 = store 8b, 2 = store 16b, 3 = store 32b
endmodule

// RAM intr
module RAM_interface (
  input  [7:0] Output_8,
  input  [15:0] Output_16,
  input  [31:0] Output_32,
  input  Read_RAM,
  input  Write_RAM,
  input  [1:0] Data_Size,
  input  [31:0] Data_In,
  input  [17:0] Address,
  input  [31:0] Data_In_2,
  input  [17:0] Address_2,
  input  Write_RAM_2,
  output [1:0] Mode,
  output [17:0] Address_3,
  output [31:0] Input,
  output [31:0] Data_Out,
  output [31:0] Data_Out_2,
  output In_Use
);

  wire and_1_out, and_2_out, nor_1_out;
  wire [15:0] bit_extender_1_out, multiplexer_3_out;
  wire [31:0] bit_extender_2_out;

  Multiplexer #(.width(18), .enable("false")) multiplexer_1 (
    .in0(Address_2), .in1(Address), .out(Address_3), .sel(In_Use));
  or or_1 (Mode[1], nor_1_out, and_2_out);
  or or_2 (Mode[0], nor_1_out, and_1_out);
  and and_1 (and_1_out, Data_Size[0], Write_RAM);
  and and_2 (and_2_out, Data_Size[0], Write_RAM);
  nor nor_1 (nor_1_out, Write_RAM_2, ~In_Use);  // NOR_Gate
  Multiplexer #(.width(32), .enable("false")) multiplexer_2 (.in0(Data_In_2), .in1(Data_In), .out(Input), .sel(In_Use));
  assign bit_extender_1_out = {{8{1'b0}}, Output_8};  // Bit_Extender bit_extender_1
  Multiplexer #(.width(16), .enable("false")) multiplexer_3 (
    .in0(bit_extender_1_out), .in1(Output_16), .out(multiplexer_3_out), .sel(Data_Size[0]));
  assign bit_extender_2_out = {{16{1'b0}}, multiplexer_3_out};  // Bit_Extender bit_extender_2
  or or_3 (In_Use, Write_RAM, Read_RAM);
  Multiplexer #(.width(32), .enable("false")) multiplexer_4 (
    .in0(bit_extender_2_out), .in1(Output_32), .out(Data_Out), .sel(Data_Size[1]));

  assign Data_Out_2 = Output_32;

  // Notes on the sheet:
  //   Modes: 0 = load, 1 = store 8b, 2 = store 16b, 3 = store 32b
endmodule

module MCH (
  input  In_Use,
  input  [31:0] Data_In,
  input  [31:0] Length,
  input  [31:0] Write_To_Address,
  input  [31:0] Read_From_Address,
  input  [31:0] Data_In_2,
  input  [15:0] Storage_Devices,
  input  In_Use_2,
  input  [15:0] Command,
  input  In_Use_3,
  input  Selected,
  input  [31:0] Data_In_3,
  input  In_Use_4,
  input  Clock,
  output Write,
  output [17:0] Address,
  output [31:0] Data_Out,
  output [23:0] Address_2,
  output Write_2,
  output [31:0] Data_Out_2,
  output Write_3,
  output [31:0] Data_Out_3,
  output Done,
  output [15:0] Status,
  output [31:0] Data_Out_4,
  output [17:0] Address_3,
  output Write_4
);

  wire and_4_out, and_6_out, and_7_out, and_8_out, and_9_out, comparator_1_eq, controlled_inverter_1_out,
       controlled_inverter_3_out, d_ff_1_qn, decoder_1_out0, decoder_1_out1, decoder_1_out2, decoder_1_out3,
       decoder_2_out0, decoder_2_out1, decoder_2_out2, decoder_2_out3, nor_1_out, nor_2_out, or_1_out,
       or_2_out, or_3_out, Read_Done_q, Read_Done_qn, Write_Done_q, Write_Done_qn;
  wire [1:0] Devices_q, Devices_q_3;
  wire [15:0] multiplexer_3_out, Read_Addr_q;
  wire [15:2] Devices_q_2;
  wire [23:16] Read_Addr_q_2;
  wire [23:18] Write_Addr_q;
  wire [29:0] Length_q;
  wire [29:24] Read_Addr_q_3, Write_Addr_q_2;
  wire [31:0] controlled_buffer_1_out, register_2_q;

  and and_1 (Write_2, decoder_1_out2, controlled_inverter_1_out);
  Multiplexer #(.width(16), .enable("false")) multiplexer_1 (
    .in0(Read_Addr_q), .in1(Address_3[15:0]), .out(Address[17:2]), .sel(decoder_1_out1));
  Multiplexer #(.width(24), .enable("false")) multiplexer_2 (
    .in0({Write_Addr_q, Address_3}), .in1({Read_Addr_q_2, Read_Addr_q}), .out(Address_2), .sel(decoder_1_out2));
  assign controlled_inverter_1_out = decoder_1_out2 ? ~In_Use_2 : 1'bz;  // Controlled_Inverter controlled_inverter_1
  and and_2 (Write_3, controlled_inverter_1_out, decoder_1_out0);
  assign controlled_inverter_1_out = decoder_2_out3 ? ~In_Use_4 : 1'bz;  // Controlled_Inverter controlled_inverter_2
  assign controlled_buffer_1_out = decoder_2_out2 ? Data_In_2 : 32'bz;  // Controlled_Buffer controlled_buffer_1
  assign controlled_inverter_3_out = decoder_2_out2 ? ~In_Use_2 : 1'bz;  // Controlled_Inverter controlled_inverter_3
  assign controlled_inverter_1_out = decoder_1_out0 ? ~In_Use_3 : 1'bz;  // Controlled_Inverter controlled_inverter_4
  assign controlled_inverter_3_out = decoder_1_out3 ? ~In_Use_4 : 1'bz;  // Controlled_Inverter controlled_inverter_5
  and and_3 (Write, controlled_inverter_1_out, decoder_1_out1);
  Pull_Resistor pull_resistor_1 (.node(controlled_inverter_3_out));
  Pull_Resistor pull_resistor_2 (.node(controlled_inverter_1_out));
  assign controlled_buffer_1_out = decoder_2_out0 ? register_2_q : 32'bz;  // Controlled_Buffer controlled_buffer_2
  assign controlled_inverter_3_out = decoder_2_out0 ? 1'b1 : 1'bz;  // Controlled_Buffer controlled_buffer_3
  Register #(.width(32), .trigger("falling")) register_1 (
    .D(controlled_buffer_1_out), .en(controlled_inverter_3_out), .Q(Data_Out), .clk(Clock));  // open: clr
  assign controlled_buffer_1_out = decoder_2_out3 ? Data_In_3 : 32'bz;  // Controlled_Buffer controlled_buffer_4
  Decoder #(.select(2), .disabled(0)) decoder_1 (
    .out0(decoder_1_out0), .out1(decoder_1_out1), .out2(decoder_1_out2), .out3(decoder_1_out3),
    .sel(Devices_q_3), .en(nor_1_out));
  nor nor_1 (nor_1_out, comparator_1_eq, ~Write_Done_qn);  // NOR_Gate
  or or_1 (or_1_out, controlled_inverter_1_out, and_9_out);
  assign controlled_buffer_1_out = decoder_2_out1 ? Data_In : 32'bz;  // Controlled_Buffer controlled_buffer_5
  S_R_Flip_Flop #(.trigger("falling")) Write_Done (
    .S(or_1_out), .clk(Clock), .R(and_4_out), .Q(Write_Done_q), .Qn(Write_Done_qn));  // open: preset, reset, en
  and and_4 (and_4_out, Write_Done_q, Read_Done_q);
  and and_5 (Write_4, controlled_inverter_3_out, decoder_1_out3);
  assign controlled_inverter_3_out = decoder_2_out1 ? ~In_Use : 1'bz;  // Controlled_Inverter controlled_inverter_6
  assign controlled_inverter_1_out = decoder_1_out1 ? ~In_Use : 1'bz;  // Controlled_Inverter controlled_inverter_7
  Register #(.width(32), .trigger("falling")) register_2 (
    .D(Read_From_Address), .en(and_9_out), .Q(register_2_q), .clk(Clock));  // open: clr
  Decoder #(.select(2), .disabled(0)) decoder_2 (
    .out0(decoder_2_out0), .out1(decoder_2_out1), .out2(decoder_2_out2), .out3(decoder_2_out3),
    .sel(Devices_q), .en(nor_2_out));
  nor nor_2 (nor_2_out, comparator_1_eq, ~Read_Done_qn);  // NOR_Gate
  S_R_Flip_Flop #(.trigger("falling")) Read_Done (
    .S(controlled_inverter_3_out), .clk(Clock), .R(or_2_out), .Q(Read_Done_q), .Qn(Read_Done_qn));  // open: preset, reset, en
  or or_2 (or_2_out, and_4_out, and_9_out);
  or or_3 (or_3_out, and_4_out, and_9_out);
  and and_6 (and_6_out, and_4_out, ~and_9_out);  // AND_Gate
  and and_7 (and_7_out, and_4_out, ~and_9_out);  // AND_Gate
  and and_8 (and_8_out, and_4_out, ~and_9_out);  // AND_Gate
  Counter #(.width(30), .max('h3fffffff), .trigger("falling")) u_Length (
    .load(or_3_out), .D(Length[31:2]), .count(and_6_out), .Q(Length_q), .clk(Clock));  // open: carry, clr
  Counter #(.width(30), .max('h3fffffff), .trigger("falling")) Write_Addr (
    .load(and_9_out), .D(Write_To_Address[31:2]), .count(and_7_out),
    .Q({Write_Addr_q_2, Write_Addr_q, Address_3}), .clk(Clock));  // open: carry, clr
  Counter #(.width(30), .max('h3fffffff), .trigger("falling")) Read_Addr (
    .load(and_9_out), .D(Read_From_Address[31:2]), .count(and_8_out),
    .Q({Read_Addr_q_3, Read_Addr_q_2, Read_Addr_q}), .clk(Clock));  // open: carry, clr
  Register #(.width(16), .trigger("falling")) Devices (
    .D(Storage_Devices), .en(and_9_out), .Q({Devices_q_2[15:10], Devices_q_3, Devices_q_2[7:2], Devices_q}),
    .clk(Clock));  // open: clr
  and and_9 (and_9_out, Command[0], Selected);
  Comparator #(.width(30)) comparator_1 (.a({30{1'b0}}), .b(Length_q), .eq(comparator_1_eq));  // open: gt, lt
  D_Flip_Flop #(.trigger("falling")) d_ff_1 (
    .clk(Clock), .D(comparator_1_eq), .Qn(d_ff_1_qn));  // open: Q, preset, en, reset
  and and_10 (Done, comparator_1_eq, d_ff_1_qn);
  Multiplexer #(.width(16), .enable("false")) multiplexer_3 (
    .in0({Length_q[13:0], 2'b00}), .in1(Length_q[29:14]), .out(multiplexer_3_out), .sel(Command[1]));
  assign Status = Selected ? multiplexer_3_out : 16'bz;  // Controlled_Buffer controlled_buffer_6

  assign Address[1:0] = 2'b00;
  assign Data_Out_2 = Data_Out;
  assign Data_Out_3 = Data_Out;
  assign Data_Out_4 = Data_Out;
endmodule

module PIC (
  input  Clock,
  input  Interrupt_Request_15,
  input  Interrupt_Request_14,
  input  Interrupt_Request_13,
  input  Interrupt_Request_12,
  input  Interrupt_Request_11,
  input  Interrupt_Request_10,
  input  Interrupt_Request_9,
  input  Interrupt_Request_8,
  input  Interrupt_Request_7,
  input  Interrupt_Request_6,
  input  Interrupt_Request_5,
  input  Interrupt_Request_4,
  input  Interrupt_Request_3,
  input  Interrupt_Request_2,
  input  Interrupt_Request_1,
  input  Selected,
  input  Interrupt_Request_0,
  input  [15:0] Command_Input,
  input  [15:0] Data_Input,
  output Interrupt_Request,
  output [15:0] Output
);

  wire and_1_out, and_2_out, nand_2_out, nand_3_out, nand_4_out, nand_5_out, nand_6_out, nand_7_out,
       nand_8_out, nand_9_out, nand_10_out, nand_11_out, nand_12_out, nand_13_out, nand_14_out, nand_15_out,
       nand_16_out, nand_17_out, nor_1_out, nor_2_out, nor_3_out, nor_4_out, nor_5_out, nor_6_out, nor_7_out,
       nor_8_out, nor_9_out, nor_10_out, nor_11_out, nor_12_out, nor_13_out, nor_14_out, nor_15_out,
       nor_16_out;
  wire [15:0] bit_extender_1_out, d_ff_16_q, multiplexer_1_out, nand_18_out, s_r_ff_16_q;

  nand nand_1 (Interrupt_Request, nand_2_out, nand_3_out, nand_4_out, nand_5_out, nand_6_out, nand_7_out, nand_8_out, nand_9_out, nand_10_out, nand_11_out, nand_12_out, nand_13_out, nand_14_out, nand_15_out, nand_16_out, nand_17_out);
  assign Output = Selected ? multiplexer_1_out : 16'bz;  // Controlled_Buffer controlled_buffer_1
  Multiplexer #(.width(16), .enable("false")) multiplexer_1 (
    .in0(d_ff_16_q), .in1(s_r_ff_16_q), .out(multiplexer_1_out), .sel(Command_Input[0]));
  nand nand_2 (nand_2_out, s_r_ff_16_q[15], d_ff_16_q[15]);
  nand nand_3 (nand_3_out, s_r_ff_16_q[14], d_ff_16_q[14]);
  nand nand_4 (nand_4_out, s_r_ff_16_q[13], d_ff_16_q[13]);
  nand nand_5 (nand_5_out, s_r_ff_16_q[12], d_ff_16_q[12]);
  nand nand_6 (nand_6_out, s_r_ff_16_q[11], d_ff_16_q[11]);
  nand nand_7 (nand_7_out, s_r_ff_16_q[10], d_ff_16_q[10]);
  nand nand_8 (nand_8_out, s_r_ff_16_q[9], d_ff_16_q[9]);
  nand nand_9 (nand_9_out, s_r_ff_16_q[8], d_ff_16_q[8]);
  nand nand_10 (nand_10_out, s_r_ff_16_q[7], d_ff_16_q[7]);
  nand nand_11 (nand_11_out, s_r_ff_16_q[6], d_ff_16_q[6]);
  nand nand_12 (nand_12_out, s_r_ff_16_q[5], d_ff_16_q[5]);
  nand nand_13 (nand_13_out, s_r_ff_16_q[4], d_ff_16_q[4]);
  nand nand_14 (nand_14_out, s_r_ff_16_q[3], d_ff_16_q[3]);
  nand nand_15 (nand_15_out, s_r_ff_16_q[2], d_ff_16_q[2]);
  nand nand_16 (nand_16_out, s_r_ff_16_q[1], d_ff_16_q[1]);
  nand nand_17 (nand_17_out, s_r_ff_16_q[0], d_ff_16_q[0]);
  and and_1 (and_1_out, Selected, Command_Input[1]);
  and and_2 (and_2_out, Command_Input[2], Selected);
  D_Flip_Flop #(.trigger("falling")) d_ff_1 (
    .clk(Clock), .D(Data_Input[15]), .Q(d_ff_16_q[15]), .en(and_1_out));  // open: Qn, preset, reset
  D_Flip_Flop #(.trigger("falling")) d_ff_2 (
    .clk(Clock), .D(Data_Input[14]), .Q(d_ff_16_q[14]), .en(and_1_out));  // open: Qn, preset, reset
  D_Flip_Flop #(.trigger("falling")) d_ff_3 (
    .clk(Clock), .D(Data_Input[13]), .Q(d_ff_16_q[13]), .en(and_1_out));  // open: Qn, preset, reset
  D_Flip_Flop #(.trigger("falling")) d_ff_4 (
    .clk(Clock), .D(Data_Input[12]), .Q(d_ff_16_q[12]), .en(and_1_out));  // open: Qn, preset, reset
  D_Flip_Flop #(.trigger("falling")) d_ff_5 (
    .clk(Clock), .D(Data_Input[11]), .Q(d_ff_16_q[11]), .en(and_1_out));  // open: Qn, preset, reset
  D_Flip_Flop #(.trigger("falling")) d_ff_6 (
    .clk(Clock), .D(Data_Input[10]), .Q(d_ff_16_q[10]), .en(and_1_out));  // open: Qn, preset, reset
  D_Flip_Flop #(.trigger("falling")) d_ff_7 (
    .clk(Clock), .D(Data_Input[9]), .Q(d_ff_16_q[9]), .en(and_1_out));  // open: Qn, preset, reset
  D_Flip_Flop #(.trigger("falling")) d_ff_8 (
    .clk(Clock), .D(Data_Input[8]), .Q(d_ff_16_q[8]), .en(and_1_out));  // open: Qn, preset, reset
  D_Flip_Flop #(.trigger("falling")) d_ff_9 (
    .clk(Clock), .D(Data_Input[7]), .Q(d_ff_16_q[7]), .en(and_1_out));  // open: Qn, preset, reset
  D_Flip_Flop #(.trigger("falling")) d_ff_10 (
    .clk(Clock), .D(Data_Input[6]), .Q(d_ff_16_q[6]), .en(and_1_out));  // open: Qn, preset, reset
  D_Flip_Flop #(.trigger("falling")) d_ff_11 (
    .clk(Clock), .D(Data_Input[5]), .Q(d_ff_16_q[5]), .en(and_1_out));  // open: Qn, preset, reset
  D_Flip_Flop #(.trigger("falling")) d_ff_12 (
    .clk(Clock), .D(Data_Input[4]), .Q(d_ff_16_q[4]), .en(and_1_out));  // open: Qn, preset, reset
  D_Flip_Flop #(.trigger("falling")) d_ff_13 (
    .clk(Clock), .D(Data_Input[3]), .Q(d_ff_16_q[3]), .en(and_1_out));  // open: Qn, preset, reset
  D_Flip_Flop #(.trigger("falling")) d_ff_14 (
    .clk(Clock), .D(Data_Input[2]), .Q(d_ff_16_q[2]), .en(and_1_out));  // open: Qn, preset, reset
  D_Flip_Flop #(.trigger("falling")) d_ff_15 (
    .clk(Clock), .D(Data_Input[1]), .Q(d_ff_16_q[1]), .en(and_1_out));  // open: Qn, preset, reset
  D_Flip_Flop #(.trigger("falling")) d_ff_16 (
    .clk(Clock), .D(Data_Input[0]), .Q(d_ff_16_q[0]), .en(and_1_out));  // open: Qn, preset, reset
  assign bit_extender_1_out = {{15{and_2_out}}, and_2_out};  // Bit_Extender bit_extender_1
  assign nand_18_out = ~(bit_extender_1_out & Data_Input);  // NAND_Gate nand_18, 16 bits wide
  nor nor_1 (nor_1_out, nand_18_out[15], Interrupt_Request_15);
  nor nor_2 (nor_2_out, nand_18_out[14], Interrupt_Request_14);
  nor nor_3 (nor_3_out, nand_18_out[13], Interrupt_Request_13);
  nor nor_4 (nor_4_out, nand_18_out[12], Interrupt_Request_12);
  nor nor_5 (nor_5_out, nand_18_out[11], Interrupt_Request_11);
  nor nor_6 (nor_6_out, nand_18_out[10], Interrupt_Request_10);
  nor nor_7 (nor_7_out, nand_18_out[9], Interrupt_Request_9);
  nor nor_8 (nor_8_out, nand_18_out[8], Interrupt_Request_8);
  nor nor_9 (nor_9_out, nand_18_out[7], Interrupt_Request_7);
  nor nor_10 (nor_10_out, nand_18_out[6], Interrupt_Request_6);
  nor nor_11 (nor_11_out, nand_18_out[5], Interrupt_Request_5);
  nor nor_12 (nor_12_out, nand_18_out[4], Interrupt_Request_4);
  nor nor_13 (nor_13_out, nand_18_out[3], Interrupt_Request_3);
  nor nor_14 (nor_14_out, nand_18_out[2], Interrupt_Request_2);
  nor nor_15 (nor_15_out, nand_18_out[1], Interrupt_Request_1);
  nor nor_16 (nor_16_out, nand_18_out[0], Interrupt_Request_0);
  S_R_Flip_Flop #(.trigger("falling")) s_r_ff_1 (
    .S(Interrupt_Request_15), .clk(Clock), .R(nor_1_out), .Q(s_r_ff_16_q[15]));  // open: Qn, preset, reset, en
  S_R_Flip_Flop #(.trigger("falling")) s_r_ff_2 (
    .S(Interrupt_Request_14), .clk(Clock), .R(nor_2_out), .Q(s_r_ff_16_q[14]));  // open: Qn, preset, reset, en
  S_R_Flip_Flop #(.trigger("falling")) s_r_ff_3 (
    .S(Interrupt_Request_13), .clk(Clock), .R(nor_3_out), .Q(s_r_ff_16_q[13]));  // open: Qn, preset, reset, en
  S_R_Flip_Flop #(.trigger("falling")) s_r_ff_4 (
    .S(Interrupt_Request_12), .clk(Clock), .R(nor_4_out), .Q(s_r_ff_16_q[12]));  // open: Qn, preset, reset, en
  S_R_Flip_Flop #(.trigger("falling")) s_r_ff_5 (
    .S(Interrupt_Request_11), .clk(Clock), .R(nor_5_out), .Q(s_r_ff_16_q[11]));  // open: Qn, preset, reset, en
  S_R_Flip_Flop #(.trigger("falling")) s_r_ff_6 (
    .S(Interrupt_Request_10), .clk(Clock), .R(nor_6_out), .Q(s_r_ff_16_q[10]));  // open: Qn, preset, reset, en
  S_R_Flip_Flop #(.trigger("falling")) s_r_ff_7 (
    .S(Interrupt_Request_9), .clk(Clock), .R(nor_7_out), .Q(s_r_ff_16_q[9]));  // open: Qn, preset, reset, en
  S_R_Flip_Flop #(.trigger("falling")) s_r_ff_8 (
    .S(Interrupt_Request_8), .clk(Clock), .R(nor_8_out), .Q(s_r_ff_16_q[8]));  // open: Qn, preset, reset, en
  S_R_Flip_Flop #(.trigger("falling")) s_r_ff_9 (
    .S(Interrupt_Request_7), .clk(Clock), .R(nor_9_out), .Q(s_r_ff_16_q[7]));  // open: Qn, preset, reset, en
  S_R_Flip_Flop #(.trigger("falling")) s_r_ff_10 (
    .S(Interrupt_Request_6), .clk(Clock), .R(nor_10_out), .Q(s_r_ff_16_q[6]));  // open: Qn, preset, reset, en
  S_R_Flip_Flop #(.trigger("falling")) s_r_ff_11 (
    .S(Interrupt_Request_5), .clk(Clock), .R(nor_11_out), .Q(s_r_ff_16_q[5]));  // open: Qn, preset, reset, en
  S_R_Flip_Flop #(.trigger("falling")) s_r_ff_12 (
    .S(Interrupt_Request_4), .clk(Clock), .R(nor_12_out), .Q(s_r_ff_16_q[4]));  // open: Qn, preset, reset, en
  S_R_Flip_Flop #(.trigger("falling")) s_r_ff_13 (
    .S(Interrupt_Request_3), .clk(Clock), .R(nor_13_out), .Q(s_r_ff_16_q[3]));  // open: Qn, preset, reset, en
  S_R_Flip_Flop #(.trigger("falling")) s_r_ff_14 (
    .S(Interrupt_Request_2), .clk(Clock), .R(nor_14_out), .Q(s_r_ff_16_q[2]));  // open: Qn, preset, reset, en
  S_R_Flip_Flop #(.trigger("falling")) s_r_ff_15 (
    .S(Interrupt_Request_1), .clk(Clock), .R(nor_15_out), .Q(s_r_ff_16_q[1]));  // open: Qn, preset, reset, en
  S_R_Flip_Flop #(.trigger("falling")) s_r_ff_16 (
    .S(Interrupt_Request_0), .clk(Clock), .R(nor_16_out), .Q(s_r_ff_16_q[0]));  // open: Qn, preset, reset, en

  // Notes on the sheet:
  //   Interrupt_Request_1: pull=down
  //   Interrupt_Request_6: pull=down
  //   Interrupt_Request_10: pull=down
  //   Interrupt_Request_3: pull=down
  //   Interrupt_Request_4: pull=down
  //   Interrupt_Request_11: pull=down
  //   Interrupt_Request_2: pull=down
  //   Interrupt_Request_9: pull=down
  //   Interrupt_Request_15: pull=down
  //   Interrupt_Request_0: pull=down
  //   Interrupt_Request_5: pull=down
  //   Interrupt_Request_8: pull=down
  //   Interrupt_Request_14: pull=down
  //   Interrupt_Request_13: pull=down
  //   Interrupt_Request_12: pull=down
  //   Interrupt_Request_7: pull=down
  //   IRQ masks
  //   IRQ's
endmodule

module PIT (
  input  Selected,
  input  [15:0] Data_In,
  input  [15:0] Control,
  input  Clock,
  output Done,
  output [15:0] Data_Out
);

  wire and_2_out, and_3_out, IRQ_Once_qn, nand_1_out, or_1_out, or_2_out, Pulse_Limiter_qn, Repeat_IRQ_qn,
       subtractor_1_bout, subtractor_2_bout;
  wire [15:0] Counter_Time_q, multiplexer_1_out, multiplexer_2_out, subtractor_1_out, subtractor_2_out,
       Tick_Counter_q, Time_Counter_q;

  and and_1 (Done, nand_1_out, and_3_out);
  assign Data_Out = Selected ? subtractor_2_out : 16'bz;  // Controlled_Buffer controlled_buffer_1
  and and_2 (and_2_out, Selected, Control[0]);
  D_Flip_Flop #(.trigger("falling")) Repeat_IRQ (
    .clk(Clock), .D(Control[1]), .Qn(Repeat_IRQ_qn), .en(and_2_out));  // open: Q, preset, reset
  S_R_Flip_Flop #(.trigger("falling")) IRQ_Once (
    .S(and_2_out), .clk(Clock), .R(and_3_out), .Qn(IRQ_Once_qn));  // open: Q, preset, reset, en
  nand nand_1 (nand_1_out, IRQ_Once_qn, Repeat_IRQ_qn);
  Multiplexer #(.width(16), .enable("false")) multiplexer_1 (
    .in0(subtractor_1_out), .in1(16'h3), .out(multiplexer_1_out), .sel(subtractor_1_bout));
  Register #(.width(16), .trigger("falling")) Tick_Counter (
    .D(multiplexer_1_out), .Q(Tick_Counter_q), .clk(Clock));  // open: en, clr
  Subtractor #(.width(16)) subtractor_1 (
    .a(Tick_Counter_q), .b(16'h1), .out(subtractor_1_out), .bout(subtractor_1_bout));  // open: bin
  or or_1 (or_1_out, subtractor_2_bout, and_2_out);
  Register #(.width(16), .trigger("high")) Counter_Time (
    .D(Data_In), .en(and_2_out), .Q(Counter_Time_q), .clk(Clock));  // open: clr
  Multiplexer #(.width(16), .enable("false")) multiplexer_2 (
    .in0(subtractor_2_out), .in1(Counter_Time_q), .out(multiplexer_2_out), .sel(or_1_out));
  or or_2 (or_2_out, and_2_out, subtractor_1_bout);
  Register #(.width(16), .trigger("falling")) Time_Counter (
    .D(multiplexer_2_out), .en(or_2_out), .Q(Time_Counter_q), .clk(Clock));  // open: clr
  Subtractor #(.width(16)) subtractor_2 (
    .a(Time_Counter_q), .b(16'h1), .out(subtractor_2_out), .bout(subtractor_2_bout));  // open: bin
  and and_3 (and_3_out, subtractor_2_bout, Pulse_Limiter_qn);
  D_Flip_Flop #(.trigger("falling")) Pulse_Limiter (
    .clk(Clock), .D(subtractor_2_bout), .Qn(Pulse_Limiter_qn));  // open: Q, preset, en, reset
endmodule

// Input Gate Decd
module Input_Gate_Decoder (
  input  [15:0] Input_Gate,
  input  Request_Input,
  output Gate_15,
  output Gate_14,
  output Gate_13,
  output Gate_12,
  output Gate_11,
  output Gate_10,
  output Gate_9,
  output Gate_8,
  output Gate_7,
  output Gate_6,
  output Gate_5,
  output Gate_4,
  output Gate_3,
  output Gate_2,
  output Gate_1,
  output Gate_0
);

  wire and_1_out, nor_1_out;

  nor nor_1 (nor_1_out, Input_Gate[4], Input_Gate[5], Input_Gate[6], Input_Gate[7], Input_Gate[8], Input_Gate[9], Input_Gate[10], Input_Gate[11], Input_Gate[12], Input_Gate[13], Input_Gate[14], Input_Gate[15]);
  and and_1 (and_1_out, nor_1_out, Request_Input);
  Decoder #(.select(4), .disabled(0)) decoder_1 (
    .out0(Gate_0), .out1(Gate_1), .out2(Gate_2), .out3(Gate_3), .out4(Gate_4), .out5(Gate_5), .out6(Gate_6),
    .out7(Gate_7), .out8(Gate_8), .out9(Gate_9), .out10(Gate_10), .out11(Gate_11), .out12(Gate_12),
    .out13(Gate_13), .out14(Gate_14), .out15(Gate_15), .sel(Input_Gate[3:0]), .en(and_1_out));
endmodule
module GPU (
  input  Write,
  input  Clock,
  input  Select_2,
  input  Select_1,
  input  [15:0] Input_1,
  input  [15:0] Input_2,
  input  [15:0] Input_3,
  input  [15:0] Input_4,
  input  [15:0] Input_5,
  input  [15:0] Input_6,
  input  [15:0] Input_7,
  input  [15:0] Input_8,
  input  [17:0] Address,
  input  [31:0] Data_In,
  input  [7:0] Data_In_2,
  input  [7:0] Data_In_3,
  input  [7:0] Data_In_4,
  input  [7:0] Data_In_5,
  input  [7:0] Data_In_6,
  input  [7:0] Data_In_7,
  input  [7:0] Data_In_8,
  input  [7:0] Data_In_9,
  output In_Use,
  output Done,
  output [15:0] Output,
  output [31:0] Data_Out,
  output Load,
  output [7:0] Data_Out_2,
  output Load_2,
  output [7:0] Data_Out_3,
  output Load_3,
  output [7:0] Data_Out_4,
  output Load_4,
  output [7:0] Data_Out_5,
  output Load_5,
  output [7:0] Data_Out_6,
  output Load_6,
  output [7:0] Data_Out_7,
  output Load_7,
  output [7:0] Data_Out_8,
  output Load_8,
  output [7:0] Data_Out_9,
  output Clock_2,
  output On,
  output Clear,
  output [16:0] Address_2,
  output [19:0] Display_Address
);

  wire and_1_out, and_2_out, and_3_out, and_4_out, or_1_out, undriven, undriven_3, undriven_4, undriven_23,
       undriven_24, undriven_25, undriven_26, undriven_27;
  wire [1:0] undriven_7;
  wire [2:0] undriven_5, undriven_9, undriven_31, undriven_32;
  wire [2:2] undriven_8;
  wire [7:0] Buffer_1_q, Buffer_2_q, Cache_1_q, Cache_2_q, multiplexer_1_out, multiplexer_2_out,
       multiplexer_3_out, multiplexer_4_out, multiplexer_5_out, multiplexer_6_out, multiplexer_7_out,
       multiplexer_8_out, multiplexer_9_out, multiplexer_10_out, multiplexer_11_out, multiplexer_12_out,
       multiplexer_13_out, multiplexer_14_out, multiplexer_15_out, multiplexer_16_out, multiplexer_17_out,
       multiplexer_18_out, multiplexer_19_out, multiplexer_20_out, multiplexer_21_out, multiplexer_22_out,
       multiplexer_23_out, multiplexer_24_out, multiplexer_25_out, multiplexer_26_out, multiplexer_27_out,
       multiplexer_28_out, multiplexer_29_out, multiplexer_30_out, multiplexer_31_out, multiplexer_32_out,
       multiplexer_33_out, multiplexer_34_out, multiplexer_35_out, multiplexer_36_out, multiplexer_37_out,
       multiplexer_38_out, multiplexer_39_out, multiplexer_40_out, multiplexer_41_out, multiplexer_42_out,
       multiplexer_43_out, multiplexer_44_out, multiplexer_45_out, multiplexer_46_out, multiplexer_47_out,
       multiplexer_48_out, multiplexer_49_out, multiplexer_50_out, multiplexer_51_out, multiplexer_52_out,
       multiplexer_53_out, multiplexer_54_out, multiplexer_55_out, multiplexer_56_out, multiplexer_57_out,
       multiplexer_58_out, multiplexer_59_out, multiplexer_60_out, multiplexer_61_out, multiplexer_62_out,
       or_2_out, register_1_q, register_2_q, register_3_q, register_4_q, register_5_q, register_6_q,
       register_7_q, register_8_q, register_9_q, register_10_q, register_11_q, register_12_q, register_13_q,
       register_15_q, register_16_q, register_17_q, register_18_q, register_19_q, register_20_q,
       register_21_q, register_22_q, register_23_q, register_24_q, register_25_q, register_26_q,
       register_27_q, register_28_q, shifter_1_out, undriven_6, undriven_10, undriven_11, undriven_14,
       undriven_15, undriven_16, undriven_17, undriven_18, undriven_19, undriven_20, undriven_21,
       undriven_22, undriven_28, undriven_29, undriven_30, undriven_33;
  wire [7:3] undriven_12;
  wire [7:7] undriven_13;
  wire [16:0] Buffer_1_Addr_q;
  wire [19:0] undriven_2;

  Register #(.width(20), .trigger("falling")) Write_Addr ();  // open: D, en, Q, clk, clr
  Register #(.width(20), .trigger("falling")) Read_Addr ();  // open: D, en, Q, clk, clr
  Register #(.width(17), .trigger("falling")) Buffer_1_Addr (.Q(Buffer_1_Addr_q));  // open: D, en, clk, clr
  Register #(.width(17), .trigger("falling")) Buffer_2_Addr (.D(Buffer_1_Addr_q));  // open: en, Q, clk, clr
  Register #(.trigger("falling")) Buffer_1 (
    .D(Data_In_2), .en(undriven_3), .Q(Buffer_1_q), .clk(Clock_2));  // open: clr
  Register #(.trigger("falling")) register_1 (
    .D(Data_In_3), .en(undriven_3), .Q(register_1_q), .clk(Clock_2));  // open: clr
  Register #(.trigger("falling")) register_2 (
    .D(Data_In_4), .en(undriven_3), .Q(register_2_q), .clk(Clock_2));  // open: clr
  Register #(.trigger("falling")) register_3 (
    .D(Data_In_5), .en(undriven_3), .Q(register_3_q), .clk(Clock_2));  // open: clr
  Register #(.trigger("falling")) register_4 (
    .D(Data_In_6), .en(undriven_3), .Q(register_4_q), .clk(Clock_2));  // open: clr
  Register #(.trigger("falling")) register_5 (
    .D(Data_In_7), .en(undriven_3), .Q(register_5_q), .clk(Clock_2));  // open: clr
  Register #(.trigger("falling")) register_6 (
    .D(Data_In_8), .en(undriven_3), .Q(register_6_q), .clk(Clock_2));  // open: clr
  Register #(.trigger("falling")) register_7 (
    .D(Data_In_9), .en(undriven_3), .Q(register_7_q), .clk(Clock_2));  // open: clr
  Register #(.trigger("falling")) Buffer_2 (
    .D(Buffer_1_q), .en(undriven_3), .Q(Buffer_2_q), .clk(Clock_2));  // open: clr
  Register #(.trigger("falling")) register_8 (
    .D(register_1_q), .en(undriven_3), .Q(register_8_q), .clk(Clock_2));  // open: clr
  Register #(.trigger("falling")) register_9 (
    .D(register_2_q), .en(undriven_3), .Q(register_9_q), .clk(Clock_2));  // open: clr
  Register #(.trigger("falling")) register_10 (
    .D(register_3_q), .en(undriven_3), .Q(register_10_q), .clk(Clock_2));  // open: clr
  Register #(.trigger("falling")) register_11 (
    .D(register_4_q), .en(undriven_3), .Q(register_11_q), .clk(Clock_2));  // open: clr
  Register #(.trigger("falling")) register_12 (
    .D(register_5_q), .en(undriven_3), .Q(register_12_q), .clk(Clock_2));  // open: clr
  Register #(.trigger("falling")) register_13 (
    .D(register_6_q), .en(undriven_3), .Q(register_13_q), .clk(Clock_2));  // open: clr
  Multiplexer #(.select(3), .width(8), .enable("false")) multiplexer_1 (
    .in0(register_7_q), .in1(Buffer_2_q), .in2(register_8_q), .in3(register_9_q), .in4(register_10_q),
    .in5(register_11_q), .in6(register_12_q), .in7(register_13_q), .out(multiplexer_1_out), .sel(undriven_9));
  Multiplexer #(.select(3), .width(8), .enable("false")) multiplexer_2 (
    .in0(register_6_q), .in1(register_7_q), .in2(Buffer_2_q), .in3(register_8_q), .in4(register_9_q),
    .in5(register_10_q), .in6(register_11_q), .in7(register_12_q), .out(multiplexer_2_out), .sel(undriven_9));
  Multiplexer #(.select(3), .width(8), .enable("false")) multiplexer_3 (
    .in0(register_5_q), .in1(register_6_q), .in2(register_7_q), .in3(Buffer_2_q), .in4(register_8_q),
    .in5(register_9_q), .in6(register_10_q), .in7(register_11_q), .out(multiplexer_3_out), .sel(undriven_9));
  Multiplexer #(.select(3), .width(8), .enable("false")) multiplexer_4 (
    .in0(register_4_q), .in1(register_5_q), .in2(register_6_q), .in3(register_7_q), .in4(Buffer_2_q),
    .in5(register_8_q), .in6(register_9_q), .in7(register_10_q), .out(multiplexer_4_out), .sel(undriven_9));
  Multiplexer #(.select(3), .width(8), .enable("false")) multiplexer_5 (
    .in0(register_3_q), .in1(register_4_q), .in2(register_5_q), .in3(register_6_q), .in4(register_7_q),
    .in5(Buffer_2_q), .in6(register_8_q), .in7(register_9_q), .out(multiplexer_5_out), .sel(undriven_9));
  Multiplexer #(.select(3), .width(8), .enable("false")) multiplexer_6 (
    .in0(register_2_q), .in1(register_3_q), .in2(register_4_q), .in3(register_5_q), .in4(register_6_q),
    .in5(register_7_q), .in6(Buffer_2_q), .in7(register_8_q), .out(multiplexer_6_out), .sel(undriven_9));
  Multiplexer #(.select(3), .width(8), .enable("false")) multiplexer_7 (
    .in0(register_1_q), .in1(register_2_q), .in2(register_3_q), .in3(register_4_q), .in4(register_5_q),
    .in5(register_6_q), .in6(register_7_q), .in7(Buffer_2_q), .out(multiplexer_7_out), .sel(undriven_9));
  Multiplexer #(.select(3), .width(8), .enable("false")) multiplexer_8 (
    .in0(Buffer_1_q), .in1(register_1_q), .in2(register_2_q), .in3(register_3_q), .in4(register_4_q),
    .in5(register_5_q), .in6(register_6_q), .in7(register_7_q), .out(multiplexer_8_out), .sel(undriven_9));
  Multiplexer #(.width(8), .enable("false")) multiplexer_9 (
    .in0(multiplexer_10_out), .in1(undriven_10), .out(multiplexer_9_out), .sel(undriven_4));
  Multiplexer #(.select(3), .width(8), .enable("false")) multiplexer_10 (
    .in0(multiplexer_1_out), .in1(multiplexer_2_out), .in2(multiplexer_3_out), .in3(multiplexer_4_out),
    .in4(multiplexer_5_out), .in5(multiplexer_6_out), .in6(multiplexer_7_out), .in7(multiplexer_8_out),
    .out(multiplexer_10_out), .sel({undriven_8[2], undriven_7}));
  or or_1 (or_1_out, undriven_5[0], undriven_5[1]);
  Multiplexer #(.width(8), .enable("false")) multiplexer_11 (
    .in0(multiplexer_12_out), .in1(undriven_6), .out(multiplexer_11_out), .sel(undriven_4));
  Multiplexer #(.select(3), .width(8), .enable("false")) multiplexer_12 (
    .in0(multiplexer_2_out), .in1(multiplexer_3_out), .in2(multiplexer_4_out), .in3(multiplexer_5_out),
    .in4(multiplexer_6_out), .in5(multiplexer_7_out), .in6(multiplexer_8_out), .out(multiplexer_12_out),
    .sel({undriven_8[2], undriven_7}));  // open: in7
  or or_2 (or_2_out[0], undriven_5[0], undriven_5[1], undriven_5[2], or_2_out[7]);
  or or_3 (or_2_out[1], undriven_5[1], undriven_5[2], or_2_out[7]);
  and and_1 (and_1_out, undriven_5[0], undriven_5[1]);
  or or_4 (or_2_out[2], and_1_out, undriven_5[2], or_2_out[7]);
  or or_5 (or_2_out[3], undriven_5[2], or_2_out[7]);
  and and_2 (and_2_out, or_1_out, undriven_5[2]);
  or or_6 (or_2_out[4], and_2_out, or_2_out[7]);
  and and_3 (and_3_out, undriven_5[1], undriven_5[2]);
  or or_7 (or_2_out[5], and_3_out, or_2_out[7]);
  and and_4 (and_4_out, undriven_5[0], undriven_5[1], undriven_5[2]);
  or or_8 (or_2_out[6], and_4_out, or_2_out[7]);
  Multiplexer #(.width(8), .enable("false")) multiplexer_13 (
    .in0(multiplexer_14_out), .in1(undriven_11), .out(multiplexer_13_out), .sel(undriven_4));
  Multiplexer #(.select(3), .width(8), .enable("false")) multiplexer_14 (
    .in0(multiplexer_3_out), .in1(multiplexer_4_out), .in2(multiplexer_5_out), .in3(multiplexer_6_out),
    .in4(multiplexer_7_out), .in5(multiplexer_8_out), .out(multiplexer_14_out),
    .sel({undriven_8[2], undriven_7}));  // open: in6, in7
  not not_1 (undriven_12[7], undriven_12[3]);
  Shifter shifter_1 (.in(or_2_out), .\dist ({undriven_8[2], undriven_7}), .out(shifter_1_out));
  Multiplexer #(.width(8), .enable("false")) multiplexer_15 (
    .in0(multiplexer_16_out), .in1(undriven_14), .out(multiplexer_15_out), .sel(undriven_4));
  Multiplexer #(.select(3), .width(8), .enable("false")) multiplexer_16 (
    .in0(multiplexer_4_out), .in1(multiplexer_5_out), .in2(multiplexer_6_out), .in3(multiplexer_7_out),
    .in4(multiplexer_8_out), .out(multiplexer_16_out), .sel({undriven_8[2], undriven_7}));  // open: in5, in6, in7
  Multiplexer #(.width(8), .enable("false")) multiplexer_17 (
    .in0({{4{undriven_12[7]}}, {4{undriven_12[3]}}}), .in1(shifter_1_out), .out(multiplexer_17_out),
    .sel(undriven_4));
  Multiplexer #(.width(8), .enable("false")) multiplexer_18 (
    .in0(multiplexer_19_out), .in1(undriven_10), .out(multiplexer_18_out), .sel(undriven_4));
  Multiplexer #(.select(2), .width(8), .enable("false")) multiplexer_19 (
    .in0(multiplexer_5_out), .in1(multiplexer_6_out), .in2(multiplexer_7_out), .in3(multiplexer_8_out),
    .out(multiplexer_19_out), .sel(undriven_7));
  assign {Load, Load_2, Load_3, Load_4, Load_5, Load_6, Load_7, Load_8} = {8{undriven_13[7]}} & multiplexer_17_out;  // AND_Gate and_5, 8 bits wide
  Multiplexer #(.width(8), .enable("false")) multiplexer_20 (
    .in0(multiplexer_21_out), .in1(undriven_6), .out(multiplexer_20_out), .sel(undriven_4));
  Multiplexer #(.select(2), .width(8), .enable("false")) multiplexer_21 (
    .in0(multiplexer_6_out), .in1(multiplexer_7_out), .in2(multiplexer_8_out), .out(multiplexer_21_out),
    .sel(undriven_7));  // open: in3
  Multiplexer #(.width(8), .enable("false")) multiplexer_22 (
    .in0(multiplexer_23_out), .in1(undriven_11), .out(multiplexer_22_out), .sel(undriven_4));
  Multiplexer #(.width(8), .enable("false")) multiplexer_23 (
    .in0(multiplexer_7_out), .in1(multiplexer_8_out), .out(multiplexer_23_out), .sel(undriven_7[0]));
  Multiplexer #(.width(8), .enable("false")) multiplexer_24 (
    .in0(multiplexer_8_out), .in1(undriven_14), .out(multiplexer_24_out), .sel(undriven_4));
  Register #(.width(20), .trigger("falling")) register_14 (
    .D(undriven_2), .en(undriven), .Q(Display_Address), .clk(Clock_2));  // open: clr
  assign Data_Out_2 = Load ? multiplexer_24_out : 8'bz;  // Controlled_Buffer controlled_buffer_1
  assign Data_Out_3 = Load_2 ? multiplexer_22_out : 8'bz;  // Controlled_Buffer controlled_buffer_2
  assign Data_Out_4 = Load_3 ? multiplexer_20_out : 8'bz;  // Controlled_Buffer controlled_buffer_3
  assign Data_Out_5 = Load_4 ? multiplexer_18_out : 8'bz;  // Controlled_Buffer controlled_buffer_4
  assign Data_Out_6 = Load_5 ? multiplexer_15_out : 8'bz;  // Controlled_Buffer controlled_buffer_5
  Register #(.trigger("falling")) Cache_1 (
    .D(undriven_22), .en(undriven_24), .Q(Cache_1_q), .clk(undriven_26));  // open: clr
  Register #(.trigger("falling")) register_15 (
    .D(undriven_21), .en(undriven_24), .Q(register_15_q), .clk(undriven_26));  // open: clr
  Register #(.trigger("falling")) register_16 (
    .D(undriven_20), .en(undriven_24), .Q(register_16_q), .clk(undriven_26));  // open: clr
  Register #(.trigger("falling")) register_17 (
    .D(undriven_19), .en(undriven_24), .Q(register_17_q), .clk(undriven_26));  // open: clr
  Register #(.trigger("falling")) register_18 (
    .D(undriven_18), .en(undriven_24), .Q(register_18_q), .clk(undriven_26));  // open: clr
  Register #(.trigger("falling")) register_19 (
    .D(undriven_17), .en(undriven_24), .Q(register_19_q), .clk(undriven_26));  // open: clr
  Register #(.trigger("falling")) register_20 (
    .D(undriven_16), .en(undriven_24), .Q(register_20_q), .clk(undriven_26));  // open: clr
  Register #(.trigger("falling")) register_21 (
    .D(undriven_15), .en(undriven_24), .Q(register_21_q), .clk(undriven_26));  // open: clr
  Register #(.trigger("falling")) Cache_2 (
    .D(undriven_22), .en(undriven_23), .Q(Cache_2_q), .clk(undriven_26));  // open: clr
  Register #(.trigger("falling")) register_22 (
    .D(undriven_21), .en(undriven_23), .Q(register_22_q), .clk(undriven_26));  // open: clr
  Register #(.trigger("falling")) register_23 (
    .D(undriven_20), .en(undriven_23), .Q(register_23_q), .clk(undriven_26));  // open: clr
  Register #(.trigger("falling")) register_24 (
    .D(undriven_19), .en(undriven_23), .Q(register_24_q), .clk(undriven_26));  // open: clr
  Register #(.trigger("falling")) register_25 (
    .D(undriven_18), .en(undriven_23), .Q(register_25_q), .clk(undriven_26));  // open: clr
  Register #(.trigger("falling")) register_26 (
    .D(undriven_17), .en(undriven_23), .Q(register_26_q), .clk(undriven_26));  // open: clr
  Register #(.trigger("falling")) register_27 (
    .D(undriven_16), .en(undriven_23), .Q(register_27_q), .clk(undriven_26));  // open: clr
  Register #(.trigger("falling")) register_28 (
    .D(undriven_15), .en(undriven_23), .Q(register_28_q), .clk(undriven_26));  // open: clr
  Multiplexer #(.width(8), .enable("false")) multiplexer_25 (
    .in0(Cache_1_q), .in1(Cache_2_q), .out(multiplexer_25_out), .sel(undriven_25));
  assign Data_Out_7 = Load_6 ? multiplexer_13_out : 8'bz;  // Controlled_Buffer controlled_buffer_6
  Multiplexer #(.width(8), .enable("false")) multiplexer_26 (
    .in0(register_16_q), .in1(register_23_q), .out(multiplexer_26_out), .sel(undriven_25));
  Multiplexer #(.width(8), .enable("false")) multiplexer_27 (
    .in0(register_15_q), .in1(register_22_q), .out(multiplexer_27_out), .sel(undriven_25));
  Multiplexer #(.width(8), .enable("false")) multiplexer_28 (
    .in0(register_17_q), .in1(register_24_q), .out(multiplexer_28_out), .sel(undriven_25));
  Multiplexer #(.width(8), .enable("false")) multiplexer_29 (
    .in0(register_18_q), .in1(register_25_q), .out(multiplexer_29_out), .sel(undriven_25));
  assign Data_Out_8 = Load_7 ? multiplexer_11_out : 8'bz;  // Controlled_Buffer controlled_buffer_7
  Multiplexer #(.width(8), .enable("false")) multiplexer_30 (
    .in0(register_19_q), .in1(register_26_q), .out(multiplexer_30_out), .sel(undriven_25));
  Multiplexer #(.width(8), .enable("false")) multiplexer_31 (
    .in0(register_20_q), .in1(register_27_q), .out(multiplexer_31_out), .sel(undriven_25));
  Multiplexer #(.width(8), .enable("false")) multiplexer_32 (
    .in0(register_21_q), .in1(register_28_q), .out(multiplexer_32_out), .sel(undriven_25));
  Multiplexer #(.width(8), .enable("false")) multiplexer_33 (
    .in0(Cache_2_q), .in1(Cache_1_q), .out(multiplexer_33_out), .sel(undriven_25));
  assign Data_Out_9 = Load_8 ? multiplexer_9_out : 8'bz;  // Controlled_Buffer controlled_buffer_8
  Multiplexer #(.width(8), .enable("false")) multiplexer_34 (
    .in0(register_23_q), .in1(register_16_q), .out(multiplexer_34_out), .sel(undriven_25));
  Multiplexer #(.width(8), .enable("false")) multiplexer_35 (
    .in0(register_22_q), .in1(register_15_q), .out(multiplexer_35_out), .sel(undriven_25));
  Multiplexer #(.width(8), .enable("false")) multiplexer_36 (
    .in0(register_24_q), .in1(register_17_q), .out(multiplexer_36_out), .sel(undriven_25));
  Multiplexer #(.width(8), .enable("false")) multiplexer_37 (
    .in0(register_25_q), .in1(register_18_q), .out(multiplexer_37_out), .sel(undriven_25));
  Multiplexer #(.width(8), .enable("false")) multiplexer_38 (
    .in0(register_27_q), .in1(register_20_q), .out(multiplexer_38_out), .sel(undriven_25));
  Multiplexer #(.width(8), .enable("false")) multiplexer_39 (
    .in0(register_26_q), .in1(register_19_q), .out(multiplexer_39_out), .sel(undriven_25));
  Multiplexer #(.select(3), .width(8), .enable("false")) multiplexer_40 (
    .in0(multiplexer_32_out), .in1(multiplexer_33_out), .in2(multiplexer_35_out), .in3(multiplexer_34_out),
    .in4(multiplexer_36_out), .in5(multiplexer_37_out), .in6(multiplexer_39_out), .in7(multiplexer_38_out),
    .out(multiplexer_40_out), .sel(undriven_32));
  Multiplexer #(.select(3), .width(8), .enable("false")) multiplexer_41 (
    .in0(multiplexer_31_out), .in1(multiplexer_32_out), .in2(multiplexer_33_out), .in3(multiplexer_35_out),
    .in4(multiplexer_34_out), .in5(multiplexer_36_out), .in6(multiplexer_37_out), .in7(multiplexer_39_out),
    .out(multiplexer_41_out), .sel(undriven_32));
  Multiplexer #(.select(3), .width(8), .enable("false")) multiplexer_42 (
    .in0(multiplexer_30_out), .in1(multiplexer_31_out), .in2(multiplexer_32_out), .in3(multiplexer_33_out),
    .in4(multiplexer_35_out), .in5(multiplexer_34_out), .in6(multiplexer_36_out), .in7(multiplexer_37_out),
    .out(multiplexer_42_out), .sel(undriven_32));
  Multiplexer #(.select(3), .width(8), .enable("false")) multiplexer_43 (
    .in0(multiplexer_29_out), .in1(multiplexer_30_out), .in2(multiplexer_31_out), .in3(multiplexer_32_out),
    .in4(multiplexer_33_out), .in5(multiplexer_35_out), .in6(multiplexer_34_out), .in7(multiplexer_36_out),
    .out(multiplexer_43_out), .sel(undriven_32));
  Multiplexer #(.select(3), .width(8), .enable("false")) multiplexer_44 (
    .in0(multiplexer_28_out), .in1(multiplexer_29_out), .in2(multiplexer_30_out), .in3(multiplexer_31_out),
    .in4(multiplexer_32_out), .in5(multiplexer_33_out), .in6(multiplexer_35_out), .in7(multiplexer_34_out),
    .out(multiplexer_44_out), .sel(undriven_32));
  Multiplexer #(.select(3), .width(8), .enable("false")) multiplexer_45 (
    .in0(multiplexer_26_out), .in1(multiplexer_28_out), .in2(multiplexer_29_out), .in3(multiplexer_30_out),
    .in4(multiplexer_31_out), .in5(multiplexer_32_out), .in6(multiplexer_33_out), .in7(multiplexer_35_out),
    .out(multiplexer_45_out), .sel(undriven_32));
  Multiplexer #(.select(3), .width(8), .enable("false")) multiplexer_46 (
    .in0(multiplexer_27_out), .in1(multiplexer_26_out), .in2(multiplexer_28_out), .in3(multiplexer_29_out),
    .in4(multiplexer_30_out), .in5(multiplexer_31_out), .in6(multiplexer_32_out), .in7(multiplexer_33_out),
    .out(multiplexer_46_out), .sel(undriven_32));
  Multiplexer #(.select(3), .width(8), .enable("false")) multiplexer_47 (
    .in0(multiplexer_25_out), .in1(multiplexer_27_out), .in2(multiplexer_26_out), .in3(multiplexer_28_out),
    .in4(multiplexer_29_out), .in5(multiplexer_30_out), .in6(multiplexer_31_out), .in7(multiplexer_32_out),
    .out(multiplexer_47_out), .sel(undriven_32));
  Multiplexer #(.width(8), .enable("false")) multiplexer_48 (
    .in0(multiplexer_49_out), .in1(undriven_28), .out(multiplexer_48_out), .sel(undriven_27));
  Multiplexer #(.select(3), .width(8), .enable("false")) multiplexer_49 (
    .in0(multiplexer_40_out), .in1(multiplexer_41_out), .in2(multiplexer_42_out), .in3(multiplexer_43_out),
    .in4(multiplexer_44_out), .in5(multiplexer_45_out), .in6(multiplexer_46_out), .in7(multiplexer_47_out),
    .out(multiplexer_49_out), .sel(undriven_31));
  Multiplexer #(.select(3), .width(8), .enable("false")) multiplexer_50 (
    .in0(multiplexer_41_out), .in1(multiplexer_42_out), .in2(multiplexer_43_out), .in3(multiplexer_44_out),
    .in4(multiplexer_45_out), .in5(multiplexer_46_out), .in6(multiplexer_47_out), .out(multiplexer_50_out),
    .sel(undriven_31));  // open: in7
  Multiplexer #(.width(8), .enable("false")) multiplexer_51 (
    .in0(multiplexer_50_out), .in1(undriven_33), .out(multiplexer_51_out), .sel(undriven_27));
  Multiplexer #(.width(8), .enable("false")) multiplexer_52 (
    .in0(multiplexer_53_out), .in1(undriven_29), .out(multiplexer_52_out), .sel(undriven_27));
  Multiplexer #(.select(3), .width(8), .enable("false")) multiplexer_53 (
    .in0(multiplexer_42_out), .in1(multiplexer_43_out), .in2(multiplexer_44_out), .in3(multiplexer_45_out),
    .in4(multiplexer_46_out), .in5(multiplexer_47_out), .out(multiplexer_53_out), .sel(undriven_31));  // open: in6, in7
  Multiplexer #(.width(8), .enable("false")) multiplexer_54 (
    .in0(multiplexer_55_out), .in1(undriven_30), .out(multiplexer_54_out), .sel(undriven_27));
  Multiplexer #(.select(3), .width(8), .enable("false")) multiplexer_55 (
    .in0(multiplexer_43_out), .in1(multiplexer_44_out), .in2(multiplexer_45_out), .in3(multiplexer_46_out),
    .in4(multiplexer_47_out), .out(multiplexer_55_out), .sel(undriven_31));  // open: in5, in6, in7
  Multiplexer #(.width(8), .enable("false")) multiplexer_56 (
    .in0(multiplexer_57_out), .in1(undriven_28), .out(multiplexer_56_out), .sel(undriven_27));
  Multiplexer #(.select(2), .width(8), .enable("false")) multiplexer_57 (
    .in0(multiplexer_44_out), .in1(multiplexer_45_out), .in2(multiplexer_46_out), .in3(multiplexer_47_out),
    .out(multiplexer_57_out), .sel(undriven_31[1:0]));
  Multiplexer #(.width(8), .enable("false")) multiplexer_58 (
    .in0(multiplexer_59_out), .in1(undriven_33), .out(multiplexer_58_out), .sel(undriven_27));
  Multiplexer #(.select(2), .width(8), .enable("false")) multiplexer_59 (
    .in0(multiplexer_45_out), .in1(multiplexer_46_out), .in2(multiplexer_47_out), .out(multiplexer_59_out),
    .sel(undriven_31[1:0]));  // open: in3
  Multiplexer #(.width(8), .enable("false")) multiplexer_60 (
    .in0(multiplexer_61_out), .in1(undriven_29), .out(multiplexer_60_out), .sel(undriven_27));
  Multiplexer #(.width(8), .enable("false")) multiplexer_61 (
    .in0(multiplexer_46_out), .in1(multiplexer_47_out), .out(multiplexer_61_out), .sel(undriven_31[0]));
  Multiplexer #(.width(8), .enable("false")) multiplexer_62 (
    .in0(multiplexer_47_out), .in1(undriven_30), .out(multiplexer_62_out), .sel(undriven_27));

  assign Clear = 1'b0;
endmodule
